// Logisim project BHT.circ as structural Verilog: 3 circuits, main circuit BHT
module BHT (
  input  Branch,
  input  [31:0] EX_PC,
  input  [31:0] IF_PC,
  input  [31:0] BlockDataIn,
  input  BlkDataReady,
  input  CLK,
  output BHT_Hit,
  output [31:0] DataOut,
  output [1:0] CurrentStage
);

  wire and_1_out, and_26_out, and_27_out, and_28_out, and_29_out, and_30_out, and_31_out, and_32_out,
       and_33_out, and_38_out, and_39_out, and_40_out, and_41_out, and_42_out, and_43_out, and_44_out,
       and_45_out, clr0, clr1, clr2, clr3, clr4, clr5, clr6, clr7, comparator_1_eq, comparator_2_eq,
       comparator_3_eq, comparator_4_eq, comparator_5_eq, comparator_6_eq, comparator_7_eq, comparator_8_eq,
       comparator_9_eq, comparator_10_eq, comparator_11_eq, comparator_12_eq, comparator_13_eq,
       comparator_14_eq, comparator_15_eq, comparator_16_eq, count0, count1, count2, count3, count4, count5,
       count6, count7, EN0, EN1, EN2, EN3, EN4, EN5, EN6, EN7, L0, L1, L2, L3, L4, L5, L6, L7, Miss,
       not_1_out, not_2_out, not_3_out, not_4_out, not_5_out, not_6_out, not_7_out, not_8_out, or_10_out,
       or_11_out, or_12_out, or_13_out, or_14_out, or_15_out, or_16_out, or_17_out, or_18_out,
       priority_encoder_1_gs, register_17_q, register_18_q, register_19_q, register_20_q, register_21_q,
       register_22_q, register_23_q, register_24_q, V0, V1, V2, V3, V4, V5, V6, V7, WriteL0, WriteL1,
       WriteL2, WriteL3, WriteL4, WriteL5, WriteL6, WriteL7, \淘汰0 , \淘汰1 , \淘汰2 , \淘汰3 , \淘汰4 , \淘汰5 , \淘汰6 ,
       \淘汰7 , \行0 , \行1 , \行2 , \行3 , \行4 , \行5 , \行6 , \行7 ;
  wire [1:0] S0, S1, S2, S3, S4, S5, S6, S7, \有限状态机_1_nextstate , \有限状态机_2_nextstate , \有限状态机_3_nextstate ,
       \有限状态机_4_nextstate , \有限状态机_5_nextstate , \有限状态机_6_nextstate , \有限状态机_7_nextstate ,
       \有限状态机_8_nextstate ;
  wire [2:0] \max3_归并比较_1_max_num , \max3_归并比较_2_max_num , \max3_归并比较_3_max_num , \max3_归并比较_4_max_num ,
       \max3_归并比较_5_max_num , \max3_归并比较_6_max_num , \max3_归并比较_7_max_num , priority_encoder_1_out;
  wire [15:0] C0, C1, C2, C3, C4, C5, C6, C7, \max3_归并比较_1_max , \max3_归并比较_2_max , \max3_归并比较_3_max ,
       \max3_归并比较_4_max , \max3_归并比较_5_max , \max3_归并比较_6_max ;
  wire [31:0] register_33_q, register_34_q, register_35_q, register_36_q, register_37_q, register_38_q,
       register_39_q, register_40_q, Tag0, Tag1, Tag2, Tag3, Tag4, Tag5, Tag6, Tag7;

  \Max3_归并比较  \max3_归并比较_1  (
    .Y(C1), .X(C0), .Y_num(3'b001), .X_num(3'b000), .MAX(\max3_归并比较_1_max ), .Max_num(\max3_归并比较_1_max_num ));
  \Max3_归并比较  \max3_归并比较_2  (
    .Y(C3), .X(C2), .Y_num(3'b011), .X_num(3'b010), .MAX(\max3_归并比较_2_max ), .Max_num(\max3_归并比较_2_max_num ));
  \Max3_归并比较  \max3_归并比较_3  (
    .Y(C5), .X(C4), .Y_num(3'b101), .X_num(3'b100), .MAX(\max3_归并比较_3_max ), .Max_num(\max3_归并比较_3_max_num ));
  \Max3_归并比较  \max3_归并比较_4  (
    .Y(C7), .X(C6), .Y_num(3'b111), .X_num(3'b110), .MAX(\max3_归并比较_4_max ), .Max_num(\max3_归并比较_4_max_num ));
  Register #(.width(1), .trigger("rising"), .Select("low")) register_1 (
    .D(1'b1), .en(WriteL0), .Q(V0), .clk(CLK));  // open: clr
  Register #(.width(1), .trigger("rising"), .Select("low")) register_2 (
    .D(1'b1), .en(WriteL1), .Q(V1), .clk(CLK));  // open: clr
  Register #(.width(1), .trigger("rising"), .Select("low")) register_3 (
    .D(1'b1), .en(WriteL2), .Q(V2), .clk(CLK));  // open: clr
  Register #(.width(1), .trigger("rising"), .Select("low")) register_4 (
    .D(1'b1), .en(WriteL3), .Q(V3), .clk(CLK));  // open: clr
  Register #(.width(1), .trigger("rising"), .Select("low")) register_5 (
    .D(1'b1), .en(WriteL4), .Q(V4), .clk(CLK));  // open: clr
  Register #(.width(1), .trigger("rising"), .Select("low")) register_6 (
    .D(1'b1), .en(WriteL5), .Q(V5), .clk(CLK));  // open: clr
  Register #(.width(1), .trigger("rising"), .Select("low")) register_7 (
    .D(1'b1), .en(WriteL6), .Q(V6), .clk(CLK));  // open: clr
  Register #(.width(1), .trigger("rising"), .Select("low")) register_8 (
    .D(1'b1), .en(WriteL7), .Q(V7), .clk(CLK));  // open: clr
  \Max3_归并比较  \max3_归并比较_5  (
    .Y(\max3_归并比较_2_max ), .X(\max3_归并比较_1_max ), .Y_num(\max3_归并比较_2_max_num ),
    .X_num(\max3_归并比较_1_max_num ), .MAX(\max3_归并比较_5_max ), .Max_num(\max3_归并比较_5_max_num ));
  \Max3_归并比较  \max3_归并比较_6  (
    .Y(\max3_归并比较_4_max ), .X(\max3_归并比较_3_max ), .Y_num(\max3_归并比较_4_max_num ),
    .X_num(\max3_归并比较_3_max_num ), .MAX(\max3_归并比较_6_max ), .Max_num(\max3_归并比较_6_max_num ));
  and and_1 (and_1_out, V0, V1, V2, V3, V4, V5, V6, V7);
  Comparator #(.width(32), .mode("unsigned")) comparator_1 (.a(Tag0), .b(IF_PC), .eq(comparator_1_eq));  // open: gt, lt
  Comparator #(.width(32), .mode("unsigned")) comparator_2 (.a(Tag1), .b(IF_PC), .eq(comparator_2_eq));  // open: gt, lt
  Comparator #(.width(32), .mode("unsigned")) comparator_3 (.a(Tag2), .b(IF_PC), .eq(comparator_3_eq));  // open: gt, lt
  Comparator #(.width(32), .mode("unsigned")) comparator_4 (.a(Tag3), .b(IF_PC), .eq(comparator_4_eq));  // open: gt, lt
  Comparator #(.width(32), .mode("unsigned")) comparator_5 (.a(Tag4), .b(IF_PC), .eq(comparator_5_eq));  // open: gt, lt
  Comparator #(.width(32), .mode("unsigned")) comparator_6 (.a(Tag5), .b(IF_PC), .eq(comparator_6_eq));  // open: gt, lt
  Comparator #(.width(32), .mode("unsigned")) comparator_7 (.a(Tag6), .b(IF_PC), .eq(comparator_7_eq));  // open: gt, lt
  Comparator #(.width(32), .mode("unsigned")) comparator_8 (.a(Tag7), .b(IF_PC), .eq(comparator_8_eq));  // open: gt, lt
  Register #(.width(32), .trigger("rising"), .Select("low")) register_9 (
    .D(EX_PC), .en(WriteL0), .Q(Tag0), .clk(CLK));  // open: clr
  Register #(.width(32), .trigger("rising"), .Select("low")) register_10 (
    .D(EX_PC), .en(WriteL1), .Q(Tag1), .clk(CLK));  // open: clr
  Register #(.width(32), .trigger("rising"), .Select("low")) register_11 (
    .D(EX_PC), .en(WriteL2), .Q(Tag2), .clk(CLK));  // open: clr
  Register #(.width(32), .trigger("rising"), .Select("low")) register_12 (
    .D(EX_PC), .en(WriteL3), .Q(Tag3), .clk(CLK));  // open: clr
  Register #(.width(32), .trigger("rising"), .Select("low")) register_13 (
    .D(EX_PC), .en(WriteL4), .Q(Tag4), .clk(CLK));  // open: clr
  Register #(.width(32), .trigger("rising"), .Select("low")) register_14 (
    .D(EX_PC), .en(WriteL5), .Q(Tag5), .clk(CLK));  // open: clr
  Register #(.width(32), .trigger("rising"), .Select("low")) register_15 (
    .D(EX_PC), .en(WriteL6), .Q(Tag6), .clk(CLK));  // open: clr
  Register #(.width(32), .trigger("rising"), .Select("low")) register_16 (
    .D(EX_PC), .en(WriteL7), .Q(Tag7), .clk(CLK));  // open: clr
  \Max3_归并比较  \max3_归并比较_7  (
    .Y(\max3_归并比较_6_max ), .X(\max3_归并比较_5_max ), .Y_num(\max3_归并比较_6_max_num ),
    .X_num(\max3_归并比较_5_max_num ), .Max_num(\max3_归并比较_7_max_num ));  // open: MAX
  Decoder #(.select(3), .tristate("false"), .disabled(0), .enable("true")) decoder_1 (
    .out0(\淘汰0 ), .out1(\淘汰1 ), .out2(\淘汰2 ), .out3(\淘汰3 ), .out4(\淘汰4 ), .out5(\淘汰5 ), .out6(\淘汰6 ),
    .out7(\淘汰7 ), .sel(\max3_归并比较_7_max_num ), .en(and_1_out));
  and and_2 (L0, V0, comparator_1_eq);
  and and_3 (L1, V1, comparator_2_eq);
  and and_4 (L2, V2, comparator_3_eq);
  and and_5 (L3, V3, comparator_4_eq);
  and and_6 (L4, V4, comparator_5_eq);
  and and_7 (L5, V5, comparator_6_eq);
  and and_8 (L6, V6, comparator_7_eq);
  and and_9 (L7, V7, comparator_8_eq);
  Register #(.width(1), .trigger("rising"), .Select("low")) register_17 (
    .D(WriteL0), .Q(register_17_q), .clk(CLK));  // open: en, clr
  Register #(.width(1), .trigger("rising"), .Select("low")) register_18 (
    .D(WriteL1), .Q(register_18_q), .clk(CLK));  // open: en, clr
  Register #(.width(1), .trigger("rising"), .Select("low")) register_19 (
    .D(WriteL2), .Q(register_19_q), .clk(CLK));  // open: en, clr
  Register #(.width(1), .trigger("rising"), .Select("low")) register_20 (
    .D(WriteL3), .Q(register_20_q), .clk(CLK));  // open: en, clr
  Register #(.width(1), .trigger("rising"), .Select("low")) register_21 (
    .D(WriteL4), .Q(register_21_q), .clk(CLK));  // open: en, clr
  Register #(.width(1), .trigger("rising"), .Select("low")) register_22 (
    .D(WriteL5), .Q(register_22_q), .clk(CLK));  // open: en, clr
  Register #(.width(1), .trigger("rising"), .Select("low")) register_23 (
    .D(WriteL6), .Q(register_23_q), .clk(CLK));  // open: en, clr
  Register #(.width(1), .trigger("rising"), .Select("low")) register_24 (
    .D(WriteL7), .Q(register_24_q), .clk(CLK));  // open: en, clr
  Counter #(.width(16), .max('hffff), .ongoal("wrap"), .trigger("rising"), .behavior("old")) counter_1 (
    .count(count0), .Q(C0), .clk(CLK), .clr(clr0));  // open: load, D, carry, preset
  Counter #(.width(16), .max('hffff), .ongoal("wrap"), .trigger("rising"), .behavior("old")) counter_2 (
    .count(count1), .Q(C1), .clk(CLK), .clr(clr1));  // open: load, D, carry, preset
  Counter #(.width(16), .max('hffff), .ongoal("wrap"), .trigger("rising"), .behavior("old")) counter_3 (
    .count(count2), .Q(C2), .clk(CLK), .clr(clr2));  // open: load, D, carry, preset
  Counter #(.width(16), .max('hffff), .ongoal("wrap"), .trigger("rising"), .behavior("old")) counter_4 (
    .count(count3), .Q(C3), .clk(CLK), .clr(clr3));  // open: load, D, carry, preset
  Counter #(.width(16), .max('hffff), .ongoal("wrap"), .trigger("rising"), .behavior("old")) counter_5 (
    .count(count4), .Q(C4), .clk(CLK), .clr(clr4));  // open: load, D, carry, preset
  Counter #(.width(16), .max('hffff), .ongoal("wrap"), .trigger("rising"), .behavior("old")) counter_6 (
    .count(count5), .Q(C5), .clk(CLK), .clr(clr5));  // open: load, D, carry, preset
  Counter #(.width(16), .max('hffff), .ongoal("wrap"), .trigger("rising"), .behavior("old")) counter_7 (
    .count(count6), .Q(C6), .clk(CLK), .clr(clr6));  // open: load, D, carry, preset
  Counter #(.width(16), .max('hffff), .ongoal("wrap"), .trigger("rising"), .behavior("old")) counter_8 (
    .count(count7), .Q(C7), .clk(CLK), .clr(clr7));  // open: load, D, carry, preset
  or or_1 (BHT_Hit, L0, L1, L2, L3, L4, L5, L6, L7);
  or or_2 (clr0, L0, register_17_q);
  or or_3 (clr1, L1, register_18_q);
  or or_4 (clr2, L2, register_19_q);
  or or_5 (clr3, L3, register_20_q);
  or or_6 (clr4, L4, register_21_q);
  or or_7 (clr5, L5, register_22_q);
  or or_8 (clr6, L6, register_23_q);
  or or_9 (clr7, L7, register_24_q);
  \有限状态机  \u_有限状态机_1  (.State(S0), .Branch(Branch), .NextState(\有限状态机_1_nextstate ));
  \有限状态机  \u_有限状态机_2  (.State(S1), .Branch(Branch), .NextState(\有限状态机_2_nextstate ));
  \有限状态机  \u_有限状态机_3  (.State(S2), .Branch(Branch), .NextState(\有限状态机_3_nextstate ));
  \有限状态机  \u_有限状态机_4  (.State(S3), .Branch(Branch), .NextState(\有限状态机_4_nextstate ));
  \有限状态机  \u_有限状态机_5  (.State(S4), .Branch(Branch), .NextState(\有限状态机_5_nextstate ));
  \有限状态机  \u_有限状态机_6  (.State(S5), .Branch(Branch), .NextState(\有限状态机_6_nextstate ));
  \有限状态机  \u_有限状态机_7  (.State(S6), .Branch(Branch), .NextState(\有限状态机_7_nextstate ));
  \有限状态机  \u_有限状态机_8  (.State(S7), .Branch(Branch), .NextState(\有限状态机_8_nextstate ));
  Register #(.width(2), .trigger("rising"), .Select("low")) register_25 (
    .D(\有限状态机_1_nextstate ), .en(EN0), .Q(S0), .clk(CLK), .clr(WriteL0));
  Register #(.width(2), .trigger("rising"), .Select("low")) register_26 (
    .D(\有限状态机_2_nextstate ), .en(EN1), .Q(S1), .clk(CLK), .clr(WriteL1));
  Register #(.width(2), .trigger("rising"), .Select("low")) register_27 (
    .D(\有限状态机_3_nextstate ), .en(EN2), .Q(S2), .clk(CLK), .clr(WriteL2));
  Register #(.width(2), .trigger("rising"), .Select("low")) register_28 (
    .D(\有限状态机_4_nextstate ), .en(EN3), .Q(S3), .clk(CLK), .clr(WriteL3));
  Register #(.width(2), .trigger("rising"), .Select("low")) register_29 (
    .D(\有限状态机_5_nextstate ), .en(EN4), .Q(S4), .clk(CLK), .clr(WriteL4));
  Register #(.width(2), .trigger("rising"), .Select("low")) register_30 (
    .D(\有限状态机_6_nextstate ), .en(EN5), .Q(S5), .clk(CLK), .clr(WriteL5));
  Register #(.width(2), .trigger("rising"), .Select("low")) register_31 (
    .D(\有限状态机_7_nextstate ), .en(EN6), .Q(S6), .clk(CLK), .clr(WriteL6));
  Register #(.width(2), .trigger("rising"), .Select("low")) register_32 (
    .D(\有限状态机_8_nextstate ), .en(EN7), .Q(S7), .clk(CLK), .clr(WriteL7));
  not not_1 (not_1_out, V0);
  not not_2 (not_2_out, V1);
  not not_3 (not_3_out, V2);
  not not_4 (not_4_out, V3);
  not not_5 (not_5_out, V4);
  not not_6 (not_6_out, V5);
  not not_7 (not_7_out, V6);
  not not_8 (not_8_out, V7);
  Comparator #(.width(32), .mode("unsigned")) comparator_9 (.a(Tag0), .b(EX_PC), .eq(comparator_9_eq));  // open: gt, lt
  Comparator #(.width(32), .mode("unsigned")) comparator_10 (
    .a(Tag1), .b(EX_PC), .eq(comparator_10_eq));  // open: gt, lt
  Comparator #(.width(32), .mode("unsigned")) comparator_11 (
    .a(Tag2), .b(EX_PC), .eq(comparator_11_eq));  // open: gt, lt
  Comparator #(.width(32), .mode("unsigned")) comparator_12 (
    .a(Tag3), .b(EX_PC), .eq(comparator_12_eq));  // open: gt, lt
  Comparator #(.width(32), .mode("unsigned")) comparator_13 (
    .a(Tag4), .b(EX_PC), .eq(comparator_13_eq));  // open: gt, lt
  Comparator #(.width(32), .mode("unsigned")) comparator_14 (
    .a(Tag5), .b(EX_PC), .eq(comparator_14_eq));  // open: gt, lt
  Comparator #(.width(32), .mode("unsigned")) comparator_15 (
    .a(Tag6), .b(EX_PC), .eq(comparator_15_eq));  // open: gt, lt
  Comparator #(.width(32), .mode("unsigned")) comparator_16 (
    .a(Tag7), .b(EX_PC), .eq(comparator_16_eq));  // open: gt, lt
  Register #(.width(32), .trigger("rising"), .Select("low")) register_33 (
    .D(BlockDataIn), .en(WriteL0), .Q(register_33_q), .clk(CLK));  // open: clr
  Register #(.width(32), .trigger("rising"), .Select("low")) register_34 (
    .D(BlockDataIn), .en(WriteL1), .Q(register_34_q), .clk(CLK));  // open: clr
  Register #(.width(32), .trigger("rising"), .Select("low")) register_35 (
    .D(BlockDataIn), .en(WriteL2), .Q(register_35_q), .clk(CLK));  // open: clr
  Register #(.width(32), .trigger("rising"), .Select("low")) register_36 (
    .D(BlockDataIn), .en(WriteL3), .Q(register_36_q), .clk(CLK));  // open: clr
  Register #(.width(32), .trigger("rising"), .Select("low")) register_37 (
    .D(BlockDataIn), .en(WriteL4), .Q(register_37_q), .clk(CLK));  // open: clr
  Register #(.width(32), .trigger("rising"), .Select("low")) register_38 (
    .D(BlockDataIn), .en(WriteL5), .Q(register_38_q), .clk(CLK));  // open: clr
  Register #(.width(32), .trigger("rising"), .Select("low")) register_39 (
    .D(BlockDataIn), .en(WriteL6), .Q(register_39_q), .clk(CLK));  // open: clr
  Register #(.width(32), .trigger("rising"), .Select("low")) register_40 (
    .D(BlockDataIn), .en(WriteL7), .Q(register_40_q), .clk(CLK));  // open: clr
  Priority_Encoder #(.select(3), .disabled(0)) priority_encoder_1 (
    .in0(not_1_out), .in1(not_2_out), .in2(not_3_out), .in3(not_4_out), .in4(not_5_out), .in5(not_6_out),
    .in6(not_7_out), .in7(not_8_out), .out(priority_encoder_1_out), .gs(priority_encoder_1_gs));  // open: en_out, en_in
  and and_10 (count0, BHT_Hit, V0);
  and and_11 (count1, BHT_Hit, V1);
  and and_12 (count2, BHT_Hit, V2);
  and and_13 (count3, BHT_Hit, V3);
  and and_14 (count4, BHT_Hit, V4);
  and and_15 (count5, BHT_Hit, V5);
  and and_16 (count6, BHT_Hit, V6);
  and and_17 (count7, BHT_Hit, V7);
  assign DataOut = L0 ? register_33_q : 32'bz;  // Controlled_Buffer controlled_buffer_1
  assign DataOut = L1 ? register_34_q : 32'bz;  // Controlled_Buffer controlled_buffer_2
  assign DataOut = L2 ? register_35_q : 32'bz;  // Controlled_Buffer controlled_buffer_3
  assign DataOut = L3 ? register_36_q : 32'bz;  // Controlled_Buffer controlled_buffer_4
  assign DataOut = L4 ? register_37_q : 32'bz;  // Controlled_Buffer controlled_buffer_5
  assign DataOut = L5 ? register_38_q : 32'bz;  // Controlled_Buffer controlled_buffer_6
  assign DataOut = L6 ? register_39_q : 32'bz;  // Controlled_Buffer controlled_buffer_7
  assign DataOut = L7 ? register_40_q : 32'bz;  // Controlled_Buffer controlled_buffer_8
  Decoder #(.select(3), .tristate("false"), .disabled(0), .enable("true")) decoder_2 (
    .out0(\行0 ), .out1(\行1 ), .out2(\行2 ), .out3(\行3 ), .out4(\行4 ), .out5(\行5 ), .out6(\行6 ), .out7(\行7 ),
    .sel(priority_encoder_1_out), .en(priority_encoder_1_gs));
  and and_18 (EN0, V0, comparator_9_eq);
  and and_19 (EN1, V1, comparator_10_eq);
  and and_20 (EN2, V2, comparator_11_eq);
  and and_21 (EN3, V3, comparator_12_eq);
  and and_22 (EN4, V4, comparator_13_eq);
  and and_23 (EN5, V5, comparator_14_eq);
  and and_24 (EN6, V6, comparator_15_eq);
  and and_25 (EN7, V7, comparator_16_eq);
  not not_9 (Miss, or_10_out);
  or or_10 (or_10_out, EN0, EN1, EN2, EN3, EN4, EN5, EN6, EN7);
  and and_26 (and_26_out, \行0 , BlkDataReady);
  and and_27 (and_27_out, BlkDataReady, \淘汰0 );
  and and_28 (and_28_out, \行2 , BlkDataReady);
  and and_29 (and_29_out, BlkDataReady, \淘汰2 );
  and and_30 (and_30_out, \行4 , BlkDataReady);
  and and_31 (and_31_out, BlkDataReady, \淘汰4 );
  and and_32 (and_32_out, \行6 , BlkDataReady);
  and and_33 (and_33_out, BlkDataReady, \淘汰6 );
  or or_11 (or_11_out, and_26_out, and_27_out);
  and and_34 (WriteL0, or_11_out, Miss);
  or or_12 (or_12_out, and_28_out, and_29_out);
  and and_35 (WriteL2, or_12_out, Miss);
  or or_13 (or_13_out, and_30_out, and_31_out);
  and and_36 (WriteL4, or_13_out, Miss);
  or or_14 (or_14_out, and_32_out, and_33_out);
  and and_37 (WriteL6, or_14_out, Miss);
  assign CurrentStage = L0 ? S0 : 2'bz;  // Controlled_Buffer controlled_buffer_9
  assign CurrentStage = L1 ? S1 : 2'bz;  // Controlled_Buffer controlled_buffer_10
  assign CurrentStage = L2 ? S2 : 2'bz;  // Controlled_Buffer controlled_buffer_11
  assign CurrentStage = L3 ? S3 : 2'bz;  // Controlled_Buffer controlled_buffer_12
  assign CurrentStage = L4 ? S4 : 2'bz;  // Controlled_Buffer controlled_buffer_13
  assign CurrentStage = L5 ? S5 : 2'bz;  // Controlled_Buffer controlled_buffer_14
  assign CurrentStage = L6 ? S6 : 2'bz;  // Controlled_Buffer controlled_buffer_15
  assign CurrentStage = L7 ? S7 : 2'bz;  // Controlled_Buffer controlled_buffer_16
  and and_38 (and_38_out, \行1 , BlkDataReady);
  and and_39 (and_39_out, BlkDataReady, \淘汰1 );
  and and_40 (and_40_out, \行3 , BlkDataReady);
  and and_41 (and_41_out, BlkDataReady, \淘汰3 );
  and and_42 (and_42_out, \行5 , BlkDataReady);
  and and_43 (and_43_out, BlkDataReady, \淘汰5 );
  and and_44 (and_44_out, \行7 , BlkDataReady);
  and and_45 (and_45_out, BlkDataReady, \淘汰7 );
  or or_15 (or_15_out, and_38_out, and_39_out);
  and and_46 (WriteL1, or_15_out, Miss);
  or or_16 (or_16_out, and_40_out, and_41_out);
  and and_47 (WriteL3, or_16_out, Miss);
  or or_17 (or_17_out, and_42_out, and_43_out);
  and and_48 (WriteL5, or_17_out, Miss);
  or or_18 (or_18_out, and_44_out, and_45_out);
  and and_49 (WriteL7, or_18_out, Miss);

  // Other names for the same wires on the sheet: BlkReady = BlkDataReady; CurrentState[1:0] = CurrentStage;
  //   Hit = BHT_Hit

  // Notes on the sheet:
  //   输入引脚区
  //   Cache槽
  //   无空行时LRU算法淘汰行逻辑
  //   分支预测的并发查找逻辑
  //   Valid
  //   EX.PC
  //   LRU.Counter
  //   FSM
  //   S.Number
  //   Cache槽选择逻辑
  //   判断分支PC是否在Cache内的并发查找逻辑
  //   输出引脚区
  //   Branch.PC
  //   块载入信号产生逻辑
  //   当前状态输出
endmodule

// Max3
module \Max3_归并比较  (
  input  [15:0] Y,
  input  [15:0] X,
  input  [2:0] Y_num,
  input  [2:0] X_num,
  output [15:0] MAX,
  output [2:0] Max_num
);

  wire comparator_1_eq, comparator_1_gt, or_1_out;

  Multiplexer #(.select(1), .width(16), .disabled("Z"), .enable("false")) multiplexer_1 (
    .in0(Y), .in1(X), .out(MAX), .sel(or_1_out));
  Comparator #(.width(16), .mode("unsigned")) comparator_1 (
    .a(X), .b(Y), .gt(comparator_1_gt), .eq(comparator_1_eq));  // open: lt
  or or_1 (or_1_out, comparator_1_gt, comparator_1_eq);
  Multiplexer #(.select(1), .width(3), .disabled("Z"), .enable("false")) multiplexer_2 (
    .in0(Y_num), .in1(X_num), .out(Max_num), .sel(or_1_out));

  // Notes on the sheet:
  //   输出两个输入中的较大值，并输出较大值的3位编号
endmodule

module \有限状态机  (
  input  [1:0] State,
  input  Branch,
  output [1:0] NextState
);

  wire [1:0] multiplexer_1_out, multiplexer_2_out, multiplexer_3_out, multiplexer_4_out;

  Multiplexer #(.select(1), .width(2), .disabled("Z"), .enable("false")) multiplexer_1 (
    .in0(2'b00), .in1(2'b01), .out(multiplexer_1_out), .sel(Branch));
  Multiplexer #(.select(1), .width(2), .disabled("Z"), .enable("false")) multiplexer_2 (
    .in0(2'b00), .in1(2'b10), .out(multiplexer_2_out), .sel(Branch));
  Multiplexer #(.select(1), .width(2), .disabled("Z"), .enable("false")) multiplexer_3 (
    .in0(2'b11), .in1(2'b10), .out(multiplexer_3_out), .sel(Branch));
  Multiplexer #(.select(1), .width(2), .disabled("Z"), .enable("false")) multiplexer_4 (
    .in0(2'b00), .in1(2'b10), .out(multiplexer_4_out), .sel(Branch));
  Multiplexer #(.select(2), .width(2), .disabled("Z"), .enable("false")) multiplexer_5 (
    .in0(multiplexer_1_out), .in1(multiplexer_2_out), .in2(multiplexer_3_out), .in3(multiplexer_4_out),
    .out(NextState), .sel(State));

  // Notes on the sheet:
  //   00状态：分支成功到01，失败到00
  //   01状态：分支成功到10，失败到00
  //   10状态：分支成功到10，失败到11
  //   11状态：分支成功到10，失败到00
endmodule
