// Logisim project 练炳诚_CS1705_U201714707_井字棋.circ as structural Verilog: 8 circuits, main circuit 井字棋游戏
module \井字棋游戏  (
);

  wire _1_out, _2_out, _3_out, _4_out, _5_out, _6_out, _7_out, _8_out, _9_out, CLK, gamedriver_1_enable,
       gamedriver_1_interrept, \单周期mips_单级中断_1_eret , \单周期mips_单级中断_1_memwrite , \单周期mips_单级中断_1_syscall ,
       \复位_out ;
  wire [6:0] gamedriver_1_d1, gamedriver_1_d2, gamedriver_1_d3, gamedriver_1_d4, gamedriver_1_d5,
       gamedriver_1_x, gamedriver_1_y;
  wire [9:0] \单周期mips_单级中断_1_memaddr ;
  wire [15:0] gamedriver_1_rgb;
  wire [31:0] gamedriver_1_mdout, \单周期mips_单级中断_1_a0 , \单周期mips_单级中断_1_mdin , \单周期mips_单级中断_1_v0 ;

  Button \u_复位  (.out(\复位_out ));
  Button _1 (.out(_1_out));
  Button _4 (.out(_4_out));
  Button _7 (.out(_7_out));
  Button _2 (.out(_2_out));
  Button _3 (.out(_3_out));
  Button _6 (.out(_6_out));
  Button _5 (.out(_5_out));
  Button _8 (.out(_8_out));
  Button _9 (.out(_9_out));
  GameDriver gamedriver_1 (
    .CLK(CLK), .MDin(\单周期mips_单级中断_1_mdin ), .MemWrite(\单周期mips_单级中断_1_memwrite ), .clr(\复位_out ),
    .MemAddr(\单周期mips_单级中断_1_memaddr ), .Button1(_1_out), .Button2(_2_out), .Button3(_3_out),
    .Button4(_4_out), .Button5(_5_out), .Button6(_6_out), .Button7(_7_out), .Button8(_8_out),
    .Button9(_9_out), .MDout(gamedriver_1_mdout), .eret(\单周期mips_单级中断_1_eret ), .a0(\单周期mips_单级中断_1_a0 ),
    .v0(\单周期mips_单级中断_1_v0 ), .syscall(\单周期mips_单级中断_1_syscall ), .enable(gamedriver_1_enable),
    .X(gamedriver_1_x), .y(gamedriver_1_y), .RGB(gamedriver_1_rgb), .interrept(gamedriver_1_interrept),
    .D1(gamedriver_1_d1), .D2(gamedriver_1_d2), .D3(gamedriver_1_d3), .D4(gamedriver_1_d4),
    .D5(gamedriver_1_d5));
  \单周期MIPS_单级中断  \u_单周期mips_单级中断_1  (
    .CLK(CLK), .IR1(gamedriver_1_interrept), .MDout(gamedriver_1_mdout), .a0(\单周期mips_单级中断_1_a0 ),
    .v0(\单周期mips_单级中断_1_v0 ), .syscall(\单周期mips_单级中断_1_syscall ), .MDin(\单周期mips_单级中断_1_mdin ),
    .MemAddr(\单周期mips_单级中断_1_memaddr ), .MemWrite(\单周期mips_单级中断_1_memwrite ), .clr(\复位_out ),
    .eret(\单周期mips_单级中断_1_eret ));  // open: IR2, IR3
  // LCD_Video lcd_video_1: pin names not known; wires that end beside it: \复位_out , CLK, gamedriver_1_enable, gamedriver_1_x, gamedriver_1_y, gamedriver_1_rgb
  DotMatrix #(.inputtype("column"), .matrixcols(5), .matrixrows(7), .persist(0), .dotshape("square")) dotmatrix_1 (
    .col0(gamedriver_1_d1), .col1(gamedriver_1_d2), .col2(gamedriver_1_d3), .col3(gamedriver_1_d4),
    .col4(gamedriver_1_d5));
  Clock #(.highDuration(1), .lowDuration(1)) clock_1 (.out(CLK));

  // Notes on the sheet:
  //   为加快棋盘显示，请将时钟频率调到最大值
  //   获胜方
endmodule

// Game Driver
module GameDriver (
  input  CLK,
  input  [31:0] MDin,
  input  MemWrite,
  input  clr,
  input  eret,
  input  [31:0] a0,
  input  [31:0] v0,
  input  syscall,
  input  [9:0] MemAddr,
  input  Button1,
  input  Button2,
  input  Button3,
  input  Button4,
  input  Button5,
  input  Button6,
  input  Button7,
  input  Button8,
  input  Button9,
  output [31:0] MDout,
  output interrept,
  output [6:0] y,
  output [6:0] X,
  output [15:0] RGB,
  output enable,
  output [6:0] D1,
  output [6:0] D2,
  output [6:0] D3,
  output [6:0] D4,
  output [6:0] D5
);

  wire and_1_out, and_2_out, and_3_out, and_4_out, and_5_out, and_6_out, and_7_out, and_8_out, and_9_out,
       and_10_out, and_11_out, and_12_out, and_13_out, and_14_out, and_15_out, and_16_out, and_17_out,
       and_18_out, and_19_out, and_20_out, and_21_out, and_22_out, and_23_out, and_24_out, and_25_out,
       and_26_out, and_27_out, and_28_out, and_29_out, and_30_out, and_31_out, and_32_out, and_33_out,
       and_34_out, and_35_out, and_36_out, and_37_out, clicked1, clicked2, clicked3, clicked4, clicked5,
       clicked6, clicked7, clicked8, clicked9, comparator_1_eq, comparator_2_eq, comparator_3_eq,
       comparator_4_eq, comparator_5_eq, comparator_6_eq, comparator_7_eq, comparator_8_eq, comparator_9_eq,
       comparator_10_eq, comparator_11_eq, comparator_12_eq, comparator_13_eq, comparator_14_eq,
       comparator_15_eq, comparator_16_eq, comparator_17_eq, comparator_18_eq, comparator_19_eq,
       comparator_20_eq, demultiplexer_1_out0, demultiplexer_1_out1, demultiplexer_1_out2,
       demultiplexer_1_out3, demultiplexer_1_out4, demultiplexer_1_out5, demultiplexer_1_out6,
       demultiplexer_1_out7, demultiplexer_1_out8, en, Halt, not_1_out, not_2_out, not_3_out, not_4_out,
       or_2_out, or_3_out, or_5_out, Player1_Win, Player2_Win, State, str;
  wire [8:0] diff_q, State_q, xor_1_out;
  wire [9:0] ADDR, multiplexer_2_out;
  wire [31:0] multiplexer_1_out, U1, U2, U3, U4, U5, U6, U7, U8, U9, UN;

  not not_1 (not_1_out, interrept);
  and and_1 (and_1_out, not_1_out, Halt);
  Demultiplexer #(.select(4), .width(1), .tristate("false"), .disabled("Z"), .enable("false")) demultiplexer_1 (
    .out0(demultiplexer_1_out0), .out1(demultiplexer_1_out1), .out2(demultiplexer_1_out2),
    .out3(demultiplexer_1_out3), .out4(demultiplexer_1_out4), .out5(demultiplexer_1_out5),
    .out6(demultiplexer_1_out6), .out7(demultiplexer_1_out7), .out8(demultiplexer_1_out8), .in(1'b1),
    .sel(ADDR[3:0]));  // open: out9, out10, out11, out12, out13, out14, out15
  D_Flip_Flop #(.trigger("rising"), .Pre_Clr_Positions("LEGACY"), .NegatePresetClear("false"), .enable("true"), .NewFFLayout("false")) d_ff_1 (
    .clk(Button1), .D(1'b1), .Q(clicked1), .en(and_1_out), .reset(clr));  // open: Qn, preset
  D_Flip_Flop #(.trigger("rising"), .Pre_Clr_Positions("LEGACY"), .NegatePresetClear("false"), .enable("true"), .NewFFLayout("false")) d_ff_2 (
    .clk(Button2), .D(1'b1), .Q(clicked2), .en(and_1_out), .reset(clr));  // open: Qn, preset
  D_Flip_Flop #(.trigger("rising"), .Pre_Clr_Positions("LEGACY"), .NegatePresetClear("false"), .enable("true"), .NewFFLayout("false")) d_ff_3 (
    .clk(Button3), .D(1'b1), .Q(clicked3), .en(and_1_out), .reset(clr));  // open: Qn, preset
  D_Flip_Flop #(.trigger("rising"), .Pre_Clr_Positions("LEGACY"), .NegatePresetClear("false"), .enable("true"), .NewFFLayout("false")) d_ff_4 (
    .clk(Button4), .D(1'b1), .Q(clicked4), .en(and_1_out), .reset(clr));  // open: Qn, preset
  D_Flip_Flop #(.trigger("rising"), .Pre_Clr_Positions("LEGACY"), .NegatePresetClear("false"), .enable("true"), .NewFFLayout("false")) d_ff_5 (
    .clk(Button5), .D(1'b1), .Q(clicked5), .en(and_1_out), .reset(clr));  // open: Qn, preset
  D_Flip_Flop #(.trigger("rising"), .Pre_Clr_Positions("LEGACY"), .NegatePresetClear("false"), .enable("true"), .NewFFLayout("false")) d_ff_6 (
    .clk(Button6), .D(1'b1), .Q(clicked6), .en(and_1_out), .reset(clr));  // open: Qn, preset
  D_Flip_Flop #(.trigger("rising"), .Pre_Clr_Positions("LEGACY"), .NegatePresetClear("false"), .enable("true"), .NewFFLayout("false")) d_ff_7 (
    .clk(Button7), .D(1'b1), .Q(clicked7), .en(and_1_out), .reset(clr));  // open: Qn, preset
  D_Flip_Flop #(.trigger("rising"), .Pre_Clr_Positions("LEGACY"), .NegatePresetClear("false"), .enable("true"), .NewFFLayout("false")) d_ff_8 (
    .clk(Button8), .D(1'b1), .Q(clicked8), .en(and_1_out), .reset(clr));  // open: Qn, preset
  D_Flip_Flop #(.trigger("rising"), .Pre_Clr_Positions("LEGACY"), .NegatePresetClear("false"), .enable("true"), .NewFFLayout("false")) d_ff_9 (
    .clk(Button9), .D(1'b1), .Q(clicked9), .en(and_1_out), .reset(clr));  // open: Qn, preset
  Register #(.width(32), .trigger("rising"), .Select("low")) u_U1 (
    .D(UN), .en(demultiplexer_1_out0), .Q(U1), .clk(CLK), .clr(clr));
  Register #(.width(32), .trigger("rising"), .Select("low")) u_U2 (
    .D(UN), .en(demultiplexer_1_out1), .Q(U2), .clk(CLK), .clr(clr));
  Register #(.width(32), .trigger("rising"), .Select("low")) u_U3 (
    .D(UN), .en(demultiplexer_1_out2), .Q(U3), .clk(CLK), .clr(clr));
  Register #(.width(32), .trigger("rising"), .Select("low")) u_U4 (
    .D(UN), .en(demultiplexer_1_out3), .Q(U4), .clk(CLK), .clr(clr));
  Register #(.width(32), .trigger("rising"), .Select("low")) u_U5 (
    .D(UN), .en(demultiplexer_1_out4), .Q(U5), .clk(CLK), .clr(clr));
  Register #(.width(32), .trigger("rising"), .Select("low")) u_U6 (
    .D(UN), .en(demultiplexer_1_out5), .Q(U6), .clk(CLK), .clr(clr));
  Register #(.width(32), .trigger("rising"), .Select("low")) u_U7 (
    .D(UN), .en(demultiplexer_1_out6), .Q(U7), .clk(CLK), .clr(clr));
  Register #(.width(32), .trigger("rising"), .Select("low")) u_U8 (
    .D(UN), .en(demultiplexer_1_out7), .Q(U8), .clk(CLK), .clr(clr));
  Register #(.width(32), .trigger("rising"), .Select("low")) u_U9 (
    .D(UN), .en(demultiplexer_1_out8), .Q(U9), .clk(CLK), .clr(clr));
  Register #(.width(9), .trigger("rising"), .Select("low")) u_State (
    .D({clicked9, clicked8, clicked7, clicked6, clicked5, clicked4, clicked3, clicked2, clicked1}),
    .Q(State_q), .clk(CLK), .clr(clr));  // open: en
  assign xor_1_out = {clicked9, clicked8, clicked7, clicked6, clicked5, clicked4, clicked3, clicked2, clicked1} ^ State_q;  // XOR_Gate xor_1, 9 bits wide
  Register #(.width(9), .trigger("rising"), .Select("low")) diff (
    .D(xor_1_out), .Q(diff_q), .clk(CLK), .clr(clr));  // open: en
  Comparator #(.width(9), .mode("unsigned")) comparator_1 (
    .a(xor_1_out), .b({9{1'b0}}), .eq(comparator_1_eq));  // open: gt, lt
  or or_1 (str, diff_q[0], diff_q[1], diff_q[2], diff_q[3], diff_q[4], diff_q[5], diff_q[6], diff_q[7], diff_q[8]);
  not not_2 (not_2_out, State);
  Register #(.width(1), .trigger("rising"), .Select("low")) State_2 (
    .D(not_2_out), .Q(State), .clk(comparator_1_eq), .clr(clr));  // open: en
  Register #(.width(1), .trigger("rising"), .Select("low")) u_EN (
    .D(not_3_out), .Q(en), .clk(CLK), .clr(clr));  // open: en
  not not_3 (not_3_out, comparator_1_eq);
  Multiplexer #(.select(1), .width(32), .disabled("Z"), .enable("false")) multiplexer_1 (
    .in0(32'h2), .in1(32'h1), .out(multiplexer_1_out), .sel(State));
  Comparator #(.width(32), .mode("unsigned")) comparator_2 (.a(U1), .b(32'h1), .eq(comparator_2_eq));  // open: gt, lt
  Comparator #(.width(32), .mode("unsigned")) comparator_3 (.a(U1), .b(32'h2), .eq(comparator_3_eq));  // open: gt, lt
  Comparator #(.width(32), .mode("unsigned")) comparator_4 (.a(U2), .b(32'h1), .eq(comparator_4_eq));  // open: gt, lt
  Comparator #(.width(32), .mode("unsigned")) comparator_5 (.a(U2), .b(32'h2), .eq(comparator_5_eq));  // open: gt, lt
  Comparator #(.width(32), .mode("unsigned")) comparator_6 (.a(U3), .b(32'h1), .eq(comparator_6_eq));  // open: gt, lt
  Comparator #(.width(32), .mode("unsigned")) comparator_7 (.a(U3), .b(32'h2), .eq(comparator_7_eq));  // open: gt, lt
  Comparator #(.width(32), .mode("unsigned")) comparator_8 (.a(U4), .b(32'h1), .eq(comparator_8_eq));  // open: gt, lt
  Comparator #(.width(32), .mode("unsigned")) comparator_9 (.a(U4), .b(32'h2), .eq(comparator_9_eq));  // open: gt, lt
  Comparator #(.width(32), .mode("unsigned")) comparator_10 (.a(U5), .b(32'h1), .eq(comparator_10_eq));  // open: gt, lt
  Comparator #(.width(32), .mode("unsigned")) comparator_11 (.a(U5), .b(32'h2), .eq(comparator_11_eq));  // open: gt, lt
  Comparator #(.width(32), .mode("unsigned")) comparator_12 (.a(U6), .b(32'h1), .eq(comparator_12_eq));  // open: gt, lt
  Comparator #(.width(32), .mode("unsigned")) comparator_13 (.a(U6), .b(32'h2), .eq(comparator_13_eq));  // open: gt, lt
  Comparator #(.width(32), .mode("unsigned")) comparator_14 (.a(U7), .b(32'h1), .eq(comparator_14_eq));  // open: gt, lt
  Comparator #(.width(32), .mode("unsigned")) comparator_15 (.a(U7), .b(32'h2), .eq(comparator_15_eq));  // open: gt, lt
  Comparator #(.width(32), .mode("unsigned")) comparator_16 (.a(U8), .b(32'h1), .eq(comparator_16_eq));  // open: gt, lt
  Comparator #(.width(32), .mode("unsigned")) comparator_17 (.a(U8), .b(32'h2), .eq(comparator_17_eq));  // open: gt, lt
  Comparator #(.width(32), .mode("unsigned")) comparator_18 (.a(U9), .b(32'h1), .eq(comparator_18_eq));  // open: gt, lt
  Comparator #(.width(32), .mode("unsigned")) comparator_19 (.a(U9), .b(32'h2), .eq(comparator_19_eq));  // open: gt, lt
  assign ADDR = diff_q[0] ? {10{1'b0}} : 10'bz;  // Controlled_Buffer controlled_buffer_1
  assign ADDR = diff_q[1] ? 10'h1 : 10'bz;  // Controlled_Buffer controlled_buffer_2
  Pull_Resistor #(.pull(1)) pull_resistor_1 (.node(ADDR));
  Multiplexer #(.select(1), .width(10), .disabled("Z"), .enable("false")) multiplexer_2 (
    .in0(MemAddr), .in1(ADDR), .out(multiplexer_2_out), .sel(en));
  Multiplexer #(.select(1), .width(32), .disabled("Z"), .enable("false")) multiplexer_3 (
    .in0(MDin), .in1(multiplexer_1_out), .out(UN), .sel(en));
  D_Flip_Flop #(.trigger("rising"), .Pre_Clr_Positions("LEGACY"), .NegatePresetClear("false"), .enable("true"), .NewFFLayout("false")) d_ff_10 (
    .clk(en), .D(1'b1), .Q(interrept), .reset(or_2_out));  // open: Qn, preset, en
  or or_2 (or_2_out, eret, clr);
  assign ADDR = diff_q[2] ? 10'h2 : 10'bz;  // Controlled_Buffer controlled_buffer_3
  assign ADDR = diff_q[3] ? 10'h3 : 10'bz;  // Controlled_Buffer controlled_buffer_4
  assign ADDR = diff_q[4] ? 10'h4 : 10'bz;  // Controlled_Buffer controlled_buffer_5
  assign ADDR = diff_q[5] ? 10'h5 : 10'bz;  // Controlled_Buffer controlled_buffer_6
  or or_3 (or_3_out, MemWrite, str);
  and and_2 (and_2_out, and_4_out, and_6_out, and_8_out);
  and and_3 (and_3_out, clicked1, comparator_2_eq);
  and and_4 (and_4_out, clicked1, comparator_3_eq);
  and and_5 (and_5_out, clicked2, comparator_4_eq);
  and and_6 (and_6_out, clicked2, comparator_5_eq);
  and and_7 (and_7_out, clicked3, comparator_6_eq);
  and and_8 (and_8_out, clicked3, comparator_7_eq);
  and and_9 (and_9_out, clicked4, comparator_8_eq);
  and and_10 (and_10_out, clicked4, comparator_9_eq);
  and and_11 (and_11_out, clicked5, comparator_10_eq);
  and and_12 (and_12_out, clicked5, comparator_11_eq);
  and and_13 (and_13_out, clicked6, comparator_12_eq);
  and and_14 (and_14_out, clicked6, comparator_13_eq);
  and and_15 (and_15_out, clicked7, comparator_14_eq);
  and and_16 (and_16_out, clicked7, comparator_15_eq);
  and and_17 (and_17_out, clicked8, comparator_16_eq);
  and and_18 (and_18_out, clicked8, comparator_17_eq);
  and and_19 (and_19_out, clicked9, comparator_18_eq);
  and and_20 (and_20_out, clicked9, comparator_19_eq);
  assign ADDR = diff_q[6] ? 10'h6 : 10'bz;  // Controlled_Buffer controlled_buffer_7
  assign ADDR = diff_q[7] ? 10'h7 : 10'bz;  // Controlled_Buffer controlled_buffer_8
  assign ADDR = diff_q[8] ? 10'h8 : 10'bz;  // Controlled_Buffer controlled_buffer_9
  RAM #(.addrWidth(10), .dataWidth(32), .bus("separate"), .Select("high")) Game_Buffer (
    .addr(multiplexer_2_out), .din(UN), .data(MDout), .str(or_3_out), .clk(CLK), .clr(clr));  // open: sel, ld
  and and_21 (and_21_out, and_10_out, and_12_out, and_14_out);
  and and_22 (and_22_out, and_16_out, and_18_out, and_20_out);
  or or_4 (Player2_Win, and_2_out, and_21_out, and_22_out, and_24_out, and_23_out, and_26_out, and_25_out, and_27_out);
  and and_23 (and_23_out, and_6_out, and_12_out, and_18_out);
  and and_24 (and_24_out, and_4_out, and_10_out, and_16_out);
  and and_25 (and_25_out, and_4_out, and_12_out, and_20_out);
  and and_26 (and_26_out, and_8_out, and_14_out, and_20_out);
  and and_27 (and_27_out, and_8_out, and_12_out, and_16_out);
  not not_4 (not_4_out, interrept);
  and and_28 (and_28_out, and_3_out, and_5_out, and_7_out);
  and and_29 (and_29_out, and_3_out, and_9_out, and_15_out);
  and and_30 (and_30_out, and_5_out, and_11_out, and_17_out);
  and and_31 (and_31_out, and_3_out, and_11_out, and_19_out);
  and and_32 (and_32_out, and_7_out, and_13_out, and_19_out);
  and and_33 (and_33_out, and_7_out, and_11_out, and_15_out);
  and and_34 (and_34_out, and_9_out, and_11_out, and_13_out);
  and and_35 (and_35_out, and_15_out, and_17_out, and_19_out);
  Comparator #(.width(32), .mode("twosComplement")) comparator_20 (
    .a(v0), .b(32'h2), .eq(comparator_20_eq));  // open: gt, lt
  and and_36 (and_36_out, Player1_Win, not_4_out);
  and and_37 (and_37_out, not_4_out, Player2_Win);
  and and_38 (enable, comparator_20_eq, syscall);
  assign D3 = and_36_out ? 7'b0111110 : 7'bz;  // Controlled_Buffer controlled_buffer_10
  assign D4 = and_36_out ? 7'b0000010 : 7'bz;  // Controlled_Buffer controlled_buffer_11
  or or_5 (or_5_out, and_36_out, and_37_out);
  not not_5 (Halt, or_5_out);
  assign D2 = and_36_out ? 7'b0010010 : 7'bz;  // Controlled_Buffer controlled_buffer_12
  assign D2 = and_37_out ? 7'b0101110 : 7'bz;  // Controlled_Buffer controlled_buffer_13
  assign D3 = and_37_out ? 7'b0101010 : 7'bz;  // Controlled_Buffer controlled_buffer_14
  assign D4 = and_37_out ? 7'b0111010 : 7'bz;  // Controlled_Buffer controlled_buffer_15
  or or_6 (Player1_Win, and_28_out, and_29_out, and_30_out, and_31_out, and_32_out, and_33_out, and_34_out, and_35_out);
  Pull_Resistor #(.pull(0)) pull_resistor_2 (.node(D4));
  Pull_Resistor #(.pull(0)) pull_resistor_3 (.node(D3));
  Pull_Resistor #(.pull(0)) pull_resistor_4 (.node(D2));

  assign D1 = {7{1'b0}};
  assign D5 = {7{1'b0}};
  assign RGB = {16{1'b1}};
  assign X = a0[13:7];
  assign y = a0[6:0];

  // Notes on the sheet:
  //   D触发器存储1：按钮已被按下
  //   状态机，新旧值的异或结果中哪一位为1，表示新的按钮按下
  //   异或结果不为0，表示新的落子
  //   胜负相关判断电路，并发比较
  //   写入存储器的偏移地址，从左到右分别表示1~9号井格
  //   LED点阵驱动
endmodule

// MIPS32-CPU
module \单周期MIPS_单级中断  (
  input  CLK,
  input  IR1,
  input  [31:0] MDout,
  input  IR2,
  input  clr,
  input  IR3,
  output syscall,
  output eret,
  output MemWrite,
  output [31:0] a0,
  output [31:0] v0,
  output [31:0] MDin,
  output [9:0] MemAddr
);

  wire and_1_out, and_2_out, and_3_out, and_6_out, and_7_out, Branch, clr1, clr2, clr3, d_ff_1_q, d_ff_2_q,
       d_ff_3_q, IE_q, IR11, IR22, IR33, J_JAL, JAL, JMP, mips_alu_3_equal, not_1_out, or_1_out, or_3_out,
       or_5_out, or_7_out, or_8_out, or_9_out, or_10_out, or_11_out, or_12_out, priority_encoder_1_gs,
       RegWrite, Sequence, SignedExt, W1, W2, W3, \中断CPU , \单周期硬布线控制器_1_alu_src , \单周期硬布线控制器_1_beq ,
       \单周期硬布线控制器_1_bne , \单周期硬布线控制器_1_jr , \单周期硬布线控制器_1_memtoreg , \单周期硬布线控制器_1_regdst ;
  wire [1:0] priority_encoder_1_out, register_1_q, register_2_q;
  wire [3:0] \单周期硬布线控制器_1_alu_op ;
  wire [4:0] multiplexer_2_out, multiplexer_3_out, multiplexer_4_out, multiplexer_5_out;
  wire [31:0] bit_extender_1_out, bit_extender_2_out, IR, mips_alu_1_result, mips_alu_2_result,
       mips_alu_3_result, multiplexer_1_out, multiplexer_7_out, multiplexer_9_out, multiplexer_10_out,
       nextPC, PC, RDin, shifter_1_out, \中断入口地址 , \中断返回地址 ;

  assign nextPC = eret ? \中断返回地址  : 32'bz;  // Controlled_Buffer controlled_buffer_1
  or or_1 (or_1_out, IR11, clr);
  or or_2 (W1, or_1_out, d_ff_1_q);
  or or_3 (or_3_out, IR22, clr);
  or or_4 (W2, or_3_out, d_ff_2_q);
  or or_5 (or_5_out, IR33, clr);
  or or_6 (W3, or_5_out, d_ff_3_q);
  assign nextPC = \单周期硬布线控制器_1_jr  ? v0 : 32'bz;  // Controlled_Buffer controlled_buffer_2
  D_Flip_Flop #(.trigger("rising"), .Pre_Clr_Positions("LEGACY"), .NegatePresetClear("false"), .enable("true"), .NewFFLayout("false")) d_ff_1 (
    .clk(IR1), .D(1'b1), .Q(d_ff_1_q), .reset(or_1_out));  // open: Qn, preset, en
  D_Flip_Flop #(.trigger("rising"), .Pre_Clr_Positions("LEGACY"), .NegatePresetClear("false"), .enable("true"), .NewFFLayout("false")) d_ff_2 (
    .clk(IR2), .D(1'b1), .Q(d_ff_2_q), .reset(or_3_out));  // open: Qn, preset, en
  D_Flip_Flop #(.trigger("rising"), .Pre_Clr_Positions("LEGACY"), .NegatePresetClear("false"), .enable("true"), .NewFFLayout("false")) d_ff_3 (
    .clk(IR3), .D(1'b1), .Q(d_ff_3_q), .reset(or_5_out));  // open: Qn, preset, en
  Register #(.width(32), .trigger("rising"), .Select("low")) EPC (
    .D(nextPC), .en(\中断CPU ), .Q(\中断返回地址 ), .clk(CLK), .clr(clr));
  Multiplexer #(.select(1), .width(32), .disabled("Z"), .enable("false")) multiplexer_1 (
    .in0(nextPC), .in1(\中断入口地址 ), .out(multiplexer_1_out), .sel(\中断CPU ));
  or or_7 (or_7_out, d_ff_1_q, IR11);
  and and_1 (and_1_out, or_7_out, ~clr1);  // AND_Gate
  or or_8 (or_8_out, d_ff_2_q, IR22);
  and and_2 (and_2_out, or_8_out, ~clr2);  // AND_Gate
  or or_9 (or_9_out, d_ff_3_q, IR33);
  and and_3 (and_3_out, or_9_out, ~clr3);  // AND_Gate
  or or_10 (or_10_out, IR11, IR22, IR33);
  Register #(.width(32), .trigger("rising"), .Select("low")) u_PC (
    .D(multiplexer_1_out), .Q(PC), .clk(CLK), .clr(clr));  // open: en
  D_Flip_Flop #(.trigger("rising"), .Pre_Clr_Positions("LEGACY"), .NegatePresetClear("false"), .enable("true"), .NewFFLayout("false")) u_IR1 (
    .clk(CLK), .D(and_1_out), .Q(IR11), .reset(clr));  // open: Qn, preset, en
  D_Flip_Flop #(.trigger("rising"), .Pre_Clr_Positions("LEGACY"), .NegatePresetClear("false"), .enable("true"), .NewFFLayout("false")) u_IR2 (
    .clk(CLK), .D(and_2_out), .Q(IR22), .reset(clr));  // open: Qn, preset, en
  D_Flip_Flop #(.trigger("rising"), .Pre_Clr_Positions("LEGACY"), .NegatePresetClear("false"), .enable("true"), .NewFFLayout("false")) u_IR3 (
    .clk(CLK), .D(and_3_out), .Q(IR33), .reset(clr));  // open: Qn, preset, en
  or or_11 (or_11_out, eret, not_1_out);
  not not_1 (not_1_out, or_10_out);
  MIPS_ALU mips_alu_1 (.X(PC), .Y(32'h4), .AluOP(4'b0101), .Result(mips_alu_1_result));  // open: Equal, Result_2, shamt
  assign nextPC = Sequence ? mips_alu_1_result : 32'bz;  // Controlled_Buffer controlled_buffer_3
  nor nor_1 (Sequence, JMP, eret, Branch);
  and and_4 (J_JAL, ~\单周期硬布线控制器_1_jr , JMP);  // AND_Gate
  // Mips_Probe mips_probe_1: pin names not known; wires that end beside it: PC[11:2], IR
  ROM #(.addrWidth(10), .dataWidth(32), .Select("high")) rom_1 (.addr(PC[11:2]), .data(IR));
  Priority_Encoder #(.select(2), .disabled("Z")) priority_encoder_1 (
    .in0(1'b0), .in1(IR11), .in2(IR22), .in3(IR33), .out(priority_encoder_1_out), .gs(priority_encoder_1_gs));  // open: en_out, en_in
  D_Flip_Flop #(.trigger("rising"), .Pre_Clr_Positions("ABOVE_BELOW"), .NegatePresetClear("false"), .enable("false"), .NewFFLayout("true")) IE (
    .clk(CLK), .D(or_11_out), .Q(IE_q), .reset(clr));  // open: Qn, preset
  Pull_Resistor #(.pull(0)) pull_resistor_1 (.node(priority_encoder_1_out));
  and and_5 (\中断CPU , priority_encoder_1_gs, IE_q);
  Multiplexer #(.select(1), .width(5), .disabled("Z"), .enable("false")) multiplexer_2 (
    .in0(IR[20:16]), .in1(IR[15:11]), .out(multiplexer_2_out), .sel(\单周期硬布线控制器_1_regdst ));
  or or_12 (or_12_out, clr, eret);
  Demultiplexer #(.select(2), .width(1), .tristate("false"), .disabled("Z"), .enable("false")) demultiplexer_1 (
    .out1(clr1), .out2(clr2), .out3(clr3), .in(eret), .sel(register_2_q));  // open: out0
  Register #(.width(2), .trigger("rising"), .Select("low")) register_1 (
    .D(priority_encoder_1_out), .en(\中断CPU ), .Q(register_1_q), .clk(CLK), .clr(or_12_out));
  Multiplexer #(.select(1), .width(5), .disabled("Z"), .enable("false")) multiplexer_3 (
    .in0(IR[25:21]), .in1(5'b00010), .out(multiplexer_3_out), .sel(syscall));
  Multiplexer #(.select(1), .width(5), .disabled("Z"), .enable("false")) multiplexer_4 (
    .in0(IR[20:16]), .in1(5'b00100), .out(multiplexer_4_out), .sel(syscall));
  Multiplexer #(.select(1), .width(5), .disabled("Z"), .enable("false")) multiplexer_5 (
    .in0(multiplexer_2_out), .in1({5{1'b1}}), .out(multiplexer_5_out), .sel(JAL));
  Multiplexer #(.select(1), .width(32), .disabled("Z"), .enable("false")) multiplexer_6 (
    .in0(multiplexer_10_out), .in1(mips_alu_1_result), .out(RDin), .sel(JAL));
  assign bit_extender_1_out = {{16{IR[15]}}, IR[15:0]};  // Bit_Extender bit_extender_1
  assign bit_extender_2_out = {{16{1'b0}}, IR[15:0]};  // Bit_Extender bit_extender_2
  assign nextPC = J_JAL ? {PC[31:28], IR[25:0], 2'b00} : 32'bz;  // Controlled_Buffer controlled_buffer_4
  Register #(.width(2), .trigger("rising"), .Select("low")) register_2 (
    .D(register_1_q), .Q(register_2_q), .clk(CLK), .clr(clr));  // open: en
  \单周期硬布线控制器  \u_单周期硬布线控制器_1  (
    .Func(IR[5:0]), .OP(IR[31:26]), .ALU_OP(\单周期硬布线控制器_1_alu_op ), .MemToReg(\单周期硬布线控制器_1_memtoreg ),
    .MemWrite(MemWrite), .ALU_SRC(\单周期硬布线控制器_1_alu_src ), .RegWrite(RegWrite), .SysCALL(syscall),
    .SignedExt(SignedExt), .RegDst(\单周期硬布线控制器_1_regdst ), .JR(\单周期硬布线控制器_1_jr ), .JMP(JMP),
    .Beq(\单周期硬布线控制器_1_beq ), .JAL(JAL), .Bne(\单周期硬布线控制器_1_bne ), .ERET(eret));
  Multiplexer #(.select(1), .width(32), .disabled("Z"), .enable("false")) multiplexer_7 (
    .in0(bit_extender_2_out), .in1(bit_extender_1_out), .out(multiplexer_7_out), .sel(SignedExt));
  Multiplexer #(.select(2), .width(32), .disabled("Z"), .enable("false")) multiplexer_8 (
    .in0({32{1'b0}}), .in1(32'h3088), .in2({32{1'b0}}), .in3({32{1'b0}}), .out(\中断入口地址 ),
    .sel(priority_encoder_1_out));
  MIPS_Regifile mips_regifile_1 (
    .Din(RDin), .Clk(CLK), .R1(v0), .R2(a0), .WE(RegWrite), .W_num(multiplexer_5_out),
    .R1_num(multiplexer_3_out), .R2_num(multiplexer_4_out));
  Shifter #(.width(32), .shift("ll")) shifter_1 (.in(bit_extender_1_out), .\dist (5'b00010), .out(shifter_1_out));
  Multiplexer #(.select(1), .width(32), .disabled("Z"), .enable("false")) multiplexer_9 (
    .in0(a0), .in1(multiplexer_7_out), .out(multiplexer_9_out), .sel(\单周期硬布线控制器_1_alu_src ));
  MIPS_ALU mips_alu_2 (
    .X(shifter_1_out), .Y(mips_alu_1_result), .AluOP(4'b0101), .Result(mips_alu_2_result));  // open: Equal, Result_2, shamt
  assign nextPC = Branch ? mips_alu_2_result : 32'bz;  // Controlled_Buffer controlled_buffer_5
  MIPS_ALU mips_alu_3 (
    .X(v0), .Y(multiplexer_9_out), .AluOP(\单周期硬布线控制器_1_alu_op ), .Equal(mips_alu_3_equal),
    .Result({mips_alu_3_result[31:12], MemAddr, mips_alu_3_result[1:0]}), .shamt(IR[10:6]));  // open: Result_2
  and and_6 (and_6_out, mips_alu_3_equal, \单周期硬布线控制器_1_beq );
  and and_7 (and_7_out, \单周期硬布线控制器_1_bne , ~mips_alu_3_equal);  // AND_Gate
  or or_13 (Branch, and_6_out, and_7_out);
  Multiplexer #(.select(1), .width(32), .disabled("Z"), .enable("false")) multiplexer_10 (
    .in0({mips_alu_3_result[31:12], MemAddr, mips_alu_3_result[1:0]}), .in1(MDout), .out(multiplexer_10_out),
    .sel(\单周期硬布线控制器_1_memtoreg ));

  assign MDin = a0;

  // Notes on the sheet:
  //   CPU24+单级中断支持数据通路
  //   新增：Sequence表达式的eret约束条件
  //   PC输入源增加
  //   Reset 
  //   Reset 
  //   Reset 
  //   指令存储器
  //   contents of rom_1 (hex, n*v repeats v):
  //   201d0200 2011007f 2012002a 2013007e 20140000 20150000 292a020 1693000f 20140000 20150000 292a020
  //   16930001 8000c21 20040000 942020 15b1c0 962025 20020002 c 3084007f 22b50001 16b1fff9 8000c09
  //   20040000 942020 421c0 952025 20020002 c 30843f80 22b50001 16b1fffa 8000c05 8000c21 afb00000 afb10004
  //   afb20008 afb3000c afb40010 afa40014 afa20018 20100000 20110040 20120004 8000cae 8e130000 ae330000
  //   20110008 20120008 20010001 10330039 8000c96 8e130000 ae330000 20110032 20120008 20010001 10330032
  //   8000c96 8e130000 ae330000 2011005c 20120008 20010001 1033002b 8000c96 8e130000 ae330000 20110008
  //   20120032 20010001 10330024 8000c96 8e130000 ae330000 20110032 20120032 20010001 1033001d 8000c96
  //   8e130000 ae330000 2011005c 20120032 20010001 10330016 8000c96 8e130000 ae330000 20110008 2012005c
  //   20010001 1033000f 8000c96 8e130000 ae330000 20110032 2012005c 20010001 10330008 8000c96 8e130000
  //   ae330000 2011005c 2012005c 20010001 10330001 8000c96 2013000d 2252000d 112020 421c0 922025 20020002
  //   c 22310001 2252ffff 2273ffff 1660fff7 2013000d 112020 421c0 922025 20020002 c 22310001 22520001
  //   2273ffff 1660fff7 2013000d 112020 421c0 922025 20020002 c 2231ffff 22520001 2273ffff 1660fff7
  //   2013000d 112020 421c0 922025 20020002 c 2231ffff 2252ffff 2273ffff 1660fff7 8000cd9 2013001a 2402020
  //   11a1c0 942025 20020002 c 20040000 22310001 22520001 2273ffff 1660fff6 2231ffe6 2013001a 2402020
  //   11a1c0 942025 20020002 c 20040000 22310001 2252ffff 2273ffff 1660fff6 8000cd9 8e130000 8e340000
  //   1674ff7c 2128020 2328820 8e130000 8e340000 1674ff7e 2128020 2328820 8e130000 8e340000 1674ff80
  //   2128020 2328820 8e130000 8e340000 1674ff82 2128020 2328820 8e130000 8e340000 1674ff84 2128020
  //   2328820 8e130000 8e340000 1674ff86 2128020 2328820 8e130000 8e340000 1674ff88 2128020 2328820
  //   8e130000 8e340000 1674ff8a 2128020 2328820 8e130000 8e340000 1674ff8c 8fa20018 8fa40014 8fb40010
  //   8fb3000c 8fb20008 8fb10004 8fb00000 42000018
  //   OP
  //   Func
  //   rs
  //   指令字
  //   rt
  //   rd
  //   shamt
  //   Imm16
  //   JMP
  //   JR
  //   ERET
  //   OP
  //   Func
  //   Beq
  //   Bne
  //   MemToReg
  //   MemWrite
  //   AluOP
  //   AluSrcB
  //   RegWrite
  //   JAL
  //   RegDst
  //   Syscall
endmodule

// 单周期硬布线控制器
module \单周期硬布线控制器  (
  input  [5:0] OP,
  input  [5:0] Func,
  output [3:0] ALU_OP,
  output MemToReg,
  output MemWrite,
  output ALU_SRC,
  output RegWrite,
  output SysCALL,
  output SignedExt,
  output RegDst,
  output Beq,
  output Bne,
  output JR,
  output JMP,
  output JAL,
  output ERET
);

  \运算控制器自动生成  \u_运算控制器自动生成_1  (
    .OP0(OP[0]), .OP1(OP[1]), .OP2(OP[2]), .OP3(OP[3]), .OP4(OP[4]), .OP5(OP[5]), .F0(Func[0]), .F1(Func[1]),
    .F2(Func[2]), .F3(Func[3]), .F4(Func[4]), .F5(Func[5]), .S0(ALU_OP[0]), .S1(ALU_OP[1]), .S2(ALU_OP[2]),
    .S3(ALU_OP[3]));
  \控制信号自动生成  \u_控制信号自动生成_1  (
    .OP0(OP[0]), .OP1(OP[1]), .OP2(OP[2]), .OP3(OP[3]), .OP4(OP[4]), .OP5(OP[5]), .F0(Func[0]), .F1(Func[1]),
    .F2(Func[2]), .F3(Func[3]), .F4(Func[4]), .F5(Func[5]), .MemToReg(MemToReg), .MemWrite(MemWrite),
    .ALU_SRC(ALU_SRC), .RegWrite(RegWrite), .SysCALL(SysCALL), .SignedExt(SignedExt), .RegDst(RegDst),
    .BEQ(Beq), .BNE(Bne), .JR(JR), .JUMP(JMP), .JAL(JAL), .ERET(ERET));

  // Other names for the same wires on the sheet: OP_CODE[5:0] = OP

  // Notes on the sheet:
  //   运算器控制器，根据指令生成运算器功能选择信号
  //   控制信号生成，产生数据通路需要的其他控制信号
endmodule

// ALU
module MIPS_ALU (
  input  [4:0] shamt,
  input  [31:0] X,
  input  [31:0] Y,
  input  [3:0] AluOP,
  output Equal,
  output [31:0] Result,
  output [31:0] Result_2
);

  wire [0:0] comparator_1_lt, comparator_2_lt;
  wire [31:0] adder_1_out, AND_out, divider_1_out, divider_1_rem, multiplier_1_cout, multiplier_1_out,
       NOR_out, OR_out, shifter_1_out, shifter_2_out, shifter_3_out, subtractor_1_out, XOR_out;

  assign AND_out = X & Y;  // AND_Gate AND, 32 bits wide
  assign OR_out = X | Y;  // OR_Gate OR, 32 bits wide
  Shifter #(.width(32), .shift("ll")) shifter_1 (.in(Y), .\dist (shamt), .out(shifter_1_out));
  Shifter #(.width(32), .shift("ar")) shifter_2 (.in(Y), .\dist (shamt), .out(shifter_2_out));
  Shifter #(.width(32), .shift("lr")) shifter_3 (.in(Y), .\dist (shamt), .out(shifter_3_out));
  Multiplier #(.width(32)) multiplier_1 (.a(X), .b(Y), .out(multiplier_1_out), .cout(multiplier_1_cout));  // open: cin
  Divider #(.width(32)) divider_1 (.a(X), .b(Y), .out(divider_1_out), .rem(divider_1_rem));  // open: upper
  Adder #(.width(32)) adder_1 (.a(X), .b(Y), .out(adder_1_out));  // open: cin, cout
  Subtractor #(.width(32)) subtractor_1 (.a(X), .b(Y), .out(subtractor_1_out));  // open: bin, bout
  assign XOR_out = X ^ Y;  // XOR_Gate XOR, 32 bits wide
  assign NOR_out = ~(X | Y);  // NOR_Gate NOR, 32 bits wide
  Comparator #(.width(32), .mode("twosComplement")) comparator_1 (
    .a(X), .b(Y), .eq(Equal), .lt(comparator_1_lt[0]));  // open: gt
  Comparator #(.width(32), .mode("unsigned")) comparator_2 (.a(X), .b(Y), .lt(comparator_2_lt[0]));  // open: gt, eq
  Multiplexer #(.select(4), .width(32), .disabled("Z"), .enable("false")) multiplexer_1 (
    .in0(shifter_1_out), .in1(shifter_2_out), .in2(shifter_3_out), .in3(multiplier_1_out),
    .in4(divider_1_out), .in5(adder_1_out), .in6(subtractor_1_out), .in7(AND_out), .in8(OR_out),
    .in9(XOR_out), .in10(NOR_out), .in11({{31{1'b0}}, comparator_1_lt[0]}),
    .in12({{31{1'b0}}, comparator_2_lt[0]}), .in13({32{1'b0}}), .in14({32{1'b0}}), .in15({32{1'b0}}),
    .out(Result), .sel(AluOP));
  Multiplexer #(.select(4), .width(32), .disabled("Z"), .enable("false")) multiplexer_2 (
    .in0({32{1'b0}}), .in1({32{1'b0}}), .in2({32{1'b0}}), .in3(multiplier_1_cout), .in4(divider_1_rem),
    .in5({32{1'b0}}), .in6({32{1'b0}}), .in7({32{1'b0}}), .in8({32{1'b0}}), .in9({32{1'b0}}),
    .in10({32{1'b0}}), .in11({32{1'b0}}), .in12({32{1'b0}}), .in13({32{1'b0}}), .in14({32{1'b0}}),
    .in15({32{1'b0}}), .out(Result_2), .sel(AluOP));

  // Other names for the same wires on the sheet: Result2[31:0] = Result_2; S[3:0] = AluOP

  // Notes on the sheet:
  //   不要改变此引脚区域内容，也不要改变ALU封装形式
  //   输入引脚
  //   输出引脚
endmodule

module MIPS_Regifile (
  input  [31:0] Din,
  input  Clk,
  input  WE,
  input  [4:0] R1_num,
  input  [4:0] W_num,
  input  [4:0] R2_num,
  output [31:0] R1,
  output [31:0] R2
);

  // RegisterFile registerfile_1: pin names not known; wires that end beside it: Din, Clk, WE, W_num, R1_num, R2_num, R1, R2
endmodule

// 运算器控制器
module \运算控制器自动生成  (
  input  OP0,
  input  OP1,
  input  OP2,
  input  OP3,
  input  OP4,
  input  OP5,
  input  F0,
  input  F1,
  input  F2,
  input  F3,
  input  F4,
  input  F5,
  output S0,
  output S1,
  output S2,
  output S3
);

  wire and_1_out, and_2_out, and_3_out, and_4_out, and_5_out, and_6_out, and_7_out, and_8_out, and_9_out,
       and_10_out, and_11_out, and_12_out, and_13_out, and_14_out, and_15_out, and_16_out, and_17_out,
       and_18_out, and_19_out, and_20_out, and_21_out, and_22_out, and_23_out, and_24_out, and_25_out,
       and_26_out, and_27_out, and_28_out, and_29_out, and_30_out, and_31_out, and_32_out, and_33_out,
       and_34_out, and_35_out, and_36_out, and_37_out, and_38_out, and_39_out, not_1_out, not_2_out,
       not_3_out, not_4_out, not_5_out, not_6_out, not_7_out, not_8_out, not_9_out, not_10_out, not_11_out,
       not_12_out, not_13_out, not_14_out, not_15_out, not_16_out, not_17_out, not_18_out, not_19_out,
       not_20_out, not_21_out, not_22_out, not_23_out, not_24_out, not_25_out, not_26_out, not_27_out,
       not_28_out, not_29_out, not_30_out, not_31_out, not_32_out, not_33_out, not_34_out, not_35_out,
       not_36_out, not_37_out, not_38_out, not_39_out, not_40_out, not_41_out, not_42_out, not_43_out,
       not_44_out, not_45_out, not_46_out, not_47_out, not_48_out, not_49_out, not_50_out, not_51_out,
       not_52_out, not_53_out, not_54_out, not_55_out, not_56_out, not_57_out, not_58_out, not_59_out,
       not_60_out, not_61_out, not_62_out, not_63_out, not_64_out, not_65_out, not_66_out, not_67_out,
       not_68_out, not_69_out, not_70_out, not_71_out, not_72_out, not_73_out, not_74_out, not_75_out,
       not_76_out, not_77_out, not_78_out, not_79_out, not_80_out, not_81_out, not_82_out, not_83_out,
       not_84_out, not_85_out, not_86_out, not_87_out, not_88_out, not_89_out, not_90_out, not_91_out,
       not_92_out, not_93_out, not_94_out, not_95_out, not_96_out, not_97_out, not_98_out, not_99_out,
       not_100_out, not_101_out, not_102_out, not_103_out, not_104_out, not_105_out, not_106_out,
       not_107_out, not_108_out, not_109_out, not_110_out, not_111_out, not_112_out, not_113_out,
       not_114_out, not_115_out, not_116_out, not_117_out, not_118_out, not_119_out, not_120_out,
       not_121_out, not_122_out, not_123_out, not_124_out, not_125_out, not_126_out, not_127_out,
       not_128_out, not_129_out, not_130_out, not_131_out, not_132_out, not_133_out, not_134_out,
       not_135_out, not_136_out, not_137_out, not_138_out, not_139_out, not_140_out, not_141_out,
       not_142_out, not_143_out, not_144_out, not_145_out, not_146_out, not_147_out, not_148_out,
       not_149_out, not_150_out, not_151_out, not_152_out, not_153_out, not_154_out, not_155_out,
       not_156_out, not_157_out, not_158_out, not_159_out, not_160_out, not_161_out, not_162_out,
       not_163_out, not_164_out, not_165_out, not_166_out, not_167_out, not_168_out, not_169_out,
       not_170_out, not_171_out, not_172_out, not_173_out, not_174_out, not_175_out, not_176_out,
       not_177_out, not_178_out, not_179_out, not_180_out, not_181_out, not_182_out, not_183_out,
       not_184_out, not_185_out, not_186_out, not_187_out, not_188_out, not_189_out, not_190_out,
       not_191_out, not_192_out, not_193_out, not_194_out, not_195_out, not_196_out, not_197_out,
       not_198_out, not_199_out, not_200_out, not_201_out, not_202_out, not_203_out, not_204_out,
       not_205_out, not_206_out, not_207_out, not_208_out, not_209_out, not_210_out, not_211_out,
       not_212_out, not_213_out, not_214_out, not_215_out, not_216_out, not_217_out, not_218_out,
       not_219_out, not_220_out, not_221_out, not_222_out, not_223_out, not_224_out, not_225_out,
       not_226_out, not_227_out, not_228_out, not_229_out, not_230_out, not_231_out, not_232_out,
       not_233_out, not_234_out, not_235_out, not_236_out, not_237_out, not_238_out, not_239_out,
       not_240_out, not_241_out, not_242_out, not_243_out, not_244_out, not_245_out, not_246_out,
       not_247_out, not_248_out, not_249_out, not_250_out, not_251_out, not_252_out, not_253_out,
       not_254_out, not_255_out, not_256_out, not_257_out, not_258_out, not_259_out, not_260_out,
       not_261_out, not_262_out, not_263_out, not_264_out, not_265_out, not_266_out, not_267_out,
       not_268_out, not_269_out, not_270_out, not_271_out;

  not not_1 (not_1_out, OP5);
  not not_2 (not_2_out, OP4);
  not not_3 (not_3_out, OP3);
  not not_4 (not_4_out, OP2);
  not not_5 (not_5_out, OP1);
  not not_6 (not_6_out, OP0);
  not not_7 (not_7_out, F5);
  not not_8 (not_8_out, F4);
  not not_9 (not_9_out, F3);
  not not_10 (not_10_out, F2);
  not not_11 (not_11_out, OP5);
  not not_12 (not_12_out, OP4);
  not not_13 (not_13_out, OP3);
  not not_14 (not_14_out, OP2);
  not not_15 (not_15_out, OP1);
  not not_16 (not_16_out, OP0);
  not not_17 (not_17_out, F4);
  not not_18 (not_18_out, F3);
  not not_19 (not_19_out, F2);
  not not_20 (not_20_out, F1);
  not not_21 (not_21_out, F0);
  not not_22 (not_22_out, OP5);
  not not_23 (not_23_out, OP4);
  not not_24 (not_24_out, OP3);
  not not_25 (not_25_out, OP2);
  not not_26 (not_26_out, OP1);
  not not_27 (not_27_out, OP0);
  not not_28 (not_28_out, F4);
  not not_29 (not_29_out, F3);
  not not_30 (not_30_out, F2);
  not not_31 (not_31_out, F1);
  not not_32 (not_32_out, OP5);
  not not_33 (not_33_out, OP4);
  not not_34 (not_34_out, OP3);
  not not_35 (not_35_out, OP2);
  not not_36 (not_36_out, OP1);
  not not_37 (not_37_out, OP0);
  not not_38 (not_38_out, F4);
  not not_39 (not_39_out, F3);
  not not_40 (not_40_out, F1);
  not not_41 (not_41_out, F0);
  not not_42 (not_42_out, OP5);
  not not_43 (not_43_out, OP4);
  not not_44 (not_44_out, OP3);
  not not_45 (not_45_out, OP2);
  not not_46 (not_46_out, OP1);
  not not_47 (not_47_out, OP0);
  not not_48 (not_48_out, F4);
  not not_49 (not_49_out, F2);
  not not_50 (not_50_out, F0);
  not not_51 (not_51_out, OP5);
  not not_52 (not_52_out, OP4);
  not not_53 (not_53_out, OP2);
  not not_54 (not_54_out, OP1);
  not not_55 (not_55_out, OP0);
  not not_56 (not_56_out, OP5);
  not not_57 (not_57_out, OP4);
  not not_58 (not_58_out, OP1);
  not not_59 (not_59_out, OP0);
  not not_60 (not_60_out, OP5);
  not not_61 (not_61_out, OP4);
  not not_62 (not_62_out, OP2);
  not not_63 (not_63_out, OP1);
  not not_64 (not_64_out, OP5);
  not not_65 (not_65_out, OP4);
  not not_66 (not_66_out, OP2);
  not not_67 (not_67_out, OP0);
  not not_68 (not_68_out, OP4);
  not not_69 (not_69_out, OP3);
  not not_70 (not_70_out, OP2);
  not not_71 (not_71_out, OP4);
  not not_72 (not_72_out, OP2);
  not not_73 (not_73_out, OP5);
  not not_74 (not_74_out, OP4);
  not not_75 (not_75_out, OP3);
  not not_76 (not_76_out, OP2);
  not not_77 (not_77_out, OP1);
  not not_78 (not_78_out, OP0);
  not not_79 (not_79_out, F5);
  not not_80 (not_80_out, F4);
  not not_81 (not_81_out, F3);
  not not_82 (not_82_out, OP5);
  not not_83 (not_83_out, OP4);
  not not_84 (not_84_out, OP3);
  not not_85 (not_85_out, OP2);
  not not_86 (not_86_out, OP1);
  not not_87 (not_87_out, OP0);
  not not_88 (not_88_out, F4);
  not not_89 (not_89_out, F3);
  not not_90 (not_90_out, F0);
  not not_91 (not_91_out, OP4);
  not not_92 (not_92_out, OP3);
  not not_93 (not_93_out, OP2);
  not not_94 (not_94_out, OP1);
  not not_95 (not_95_out, OP5);
  not not_96 (not_96_out, OP4);
  not not_97 (not_97_out, OP3);
  not not_98 (not_98_out, OP2);
  not not_99 (not_99_out, OP1);
  not not_100 (not_100_out, OP0);
  not not_101 (not_101_out, F5);
  not not_102 (not_102_out, F4);
  not not_103 (not_103_out, F3);
  not not_104 (not_104_out, F2);
  not not_105 (not_105_out, F0);
  not not_106 (not_106_out, OP5);
  not not_107 (not_107_out, OP4);
  not not_108 (not_108_out, OP3);
  not not_109 (not_109_out, OP2);
  not not_110 (not_110_out, OP1);
  not not_111 (not_111_out, OP0);
  not not_112 (not_112_out, F4);
  not not_113 (not_113_out, F3);
  not not_114 (not_114_out, F2);
  not not_115 (not_115_out, F0);
  not not_116 (not_116_out, OP5);
  not not_117 (not_117_out, OP4);
  not not_118 (not_118_out, OP3);
  not not_119 (not_119_out, OP2);
  not not_120 (not_120_out, OP1);
  not not_121 (not_121_out, OP0);
  not not_122 (not_122_out, F4);
  not not_123 (not_123_out, F3);
  not not_124 (not_124_out, F1);
  not not_125 (not_125_out, F0);
  not not_126 (not_126_out, OP5);
  not not_127 (not_127_out, OP4);
  not not_128 (not_128_out, OP3);
  not not_129 (not_129_out, OP2);
  not not_130 (not_130_out, OP1);
  not not_131 (not_131_out, OP0);
  not not_132 (not_132_out, F4);
  not not_133 (not_133_out, F3);
  not not_134 (not_134_out, OP5);
  not not_135 (not_135_out, OP4);
  not not_136 (not_136_out, OP3);
  not not_137 (not_137_out, OP2);
  not not_138 (not_138_out, OP1);
  not not_139 (not_139_out, OP0);
  not not_140 (not_140_out, F4);
  not not_141 (not_141_out, F2);
  not not_142 (not_142_out, F0);
  not not_143 (not_143_out, OP5);
  not not_144 (not_144_out, OP4);
  not not_145 (not_145_out, OP1);
  not not_146 (not_146_out, OP0);
  not not_147 (not_147_out, OP5);
  not not_148 (not_148_out, OP4);
  not not_149 (not_149_out, OP2);
  not not_150 (not_150_out, OP0);
  not not_151 (not_151_out, OP5);
  not not_152 (not_152_out, OP4);
  not not_153 (not_153_out, OP3);
  not not_154 (not_154_out, OP2);
  not not_155 (not_155_out, OP1);
  not not_156 (not_156_out, OP0);
  not not_157 (not_157_out, F4);
  not not_158 (not_158_out, F3);
  not not_159 (not_159_out, F2);
  not not_160 (not_160_out, F1);
  not not_161 (not_161_out, F0);
  not not_162 (not_162_out, OP5);
  not not_163 (not_163_out, OP4);
  not not_164 (not_164_out, OP3);
  not not_165 (not_165_out, OP2);
  not not_166 (not_166_out, OP1);
  not not_167 (not_167_out, OP0);
  not not_168 (not_168_out, F4);
  not not_169 (not_169_out, F3);
  not not_170 (not_170_out, F2);
  not not_171 (not_171_out, F1);
  not not_172 (not_172_out, OP5);
  not not_173 (not_173_out, OP4);
  not not_174 (not_174_out, OP3);
  not not_175 (not_175_out, OP2);
  not not_176 (not_176_out, OP1);
  not not_177 (not_177_out, OP0);
  not not_178 (not_178_out, F4);
  not not_179 (not_179_out, F3);
  not not_180 (not_180_out, F2);
  not not_181 (not_181_out, F0);
  not not_182 (not_182_out, OP5);
  not not_183 (not_183_out, OP4);
  not not_184 (not_184_out, OP3);
  not not_185 (not_185_out, OP2);
  not not_186 (not_186_out, OP1);
  not not_187 (not_187_out, OP0);
  not not_188 (not_188_out, F4);
  not not_189 (not_189_out, F3);
  not not_190 (not_190_out, F1);
  not not_191 (not_191_out, F0);
  not not_192 (not_192_out, OP5);
  not not_193 (not_193_out, OP4);
  not not_194 (not_194_out, OP3);
  not not_195 (not_195_out, OP2);
  not not_196 (not_196_out, OP1);
  not not_197 (not_197_out, OP0);
  not not_198 (not_198_out, F4);
  not not_199 (not_199_out, F2);
  not not_200 (not_200_out, OP5);
  not not_201 (not_201_out, OP4);
  not not_202 (not_202_out, OP2);
  not not_203 (not_203_out, OP1);
  not not_204 (not_204_out, OP0);
  not not_205 (not_205_out, OP5);
  not not_206 (not_206_out, OP4);
  not not_207 (not_207_out, OP1);
  not not_208 (not_208_out, OP0);
  not not_209 (not_209_out, OP5);
  not not_210 (not_210_out, OP4);
  not not_211 (not_211_out, OP2);
  not not_212 (not_212_out, OP1);
  not not_213 (not_213_out, OP4);
  not not_214 (not_214_out, OP3);
  not not_215 (not_215_out, OP2);
  not not_216 (not_216_out, OP4);
  not not_217 (not_217_out, OP2);
  not not_218 (not_218_out, OP4);
  not not_219 (not_219_out, OP3);
  not not_220 (not_220_out, OP2);
  not not_221 (not_221_out, OP1);
  not not_222 (not_222_out, OP5);
  not not_223 (not_223_out, OP4);
  not not_224 (not_224_out, OP3);
  not not_225 (not_225_out, OP2);
  not not_226 (not_226_out, OP1);
  not not_227 (not_227_out, OP0);
  not not_228 (not_228_out, F4);
  not not_229 (not_229_out, F3);
  not not_230 (not_230_out, F1);
  not not_231 (not_231_out, OP5);
  not not_232 (not_232_out, OP4);
  not not_233 (not_233_out, OP3);
  not not_234 (not_234_out, OP2);
  not not_235 (not_235_out, OP1);
  not not_236 (not_236_out, OP0);
  not not_237 (not_237_out, F4);
  not not_238 (not_238_out, F3);
  not not_239 (not_239_out, OP5);
  not not_240 (not_240_out, OP4);
  not not_241 (not_241_out, OP3);
  not not_242 (not_242_out, OP2);
  not not_243 (not_243_out, OP1);
  not not_244 (not_244_out, OP0);
  not not_245 (not_245_out, F4);
  not not_246 (not_246_out, F2);
  not not_247 (not_247_out, F0);
  not not_248 (not_248_out, OP5);
  not not_249 (not_249_out, OP4);
  not not_250 (not_250_out, OP3);
  not not_251 (not_251_out, OP2);
  not not_252 (not_252_out, OP1);
  not not_253 (not_253_out, OP0);
  not not_254 (not_254_out, F4);
  not not_255 (not_255_out, F2);
  not not_256 (not_256_out, OP5);
  not not_257 (not_257_out, OP4);
  not not_258 (not_258_out, OP2);
  not not_259 (not_259_out, OP0);
  not not_260 (not_260_out, OP5);
  not not_261 (not_261_out, OP4);
  not not_262 (not_262_out, OP1);
  not not_263 (not_263_out, OP5);
  not not_264 (not_264_out, OP4);
  not not_265 (not_265_out, OP3);
  not not_266 (not_266_out, OP2);
  not not_267 (not_267_out, OP1);
  not not_268 (not_268_out, OP0);
  not not_269 (not_269_out, F4);
  not not_270 (not_270_out, F3);
  not not_271 (not_271_out, F0);
  and and_1 (and_1_out, not_1_out, not_2_out, not_3_out, not_4_out, not_5_out, not_6_out, not_7_out, not_8_out, not_9_out, not_10_out, F1, F0);
  and and_2 (and_2_out, not_11_out, not_12_out, not_13_out, not_14_out, not_15_out, not_16_out, F5, not_17_out, not_18_out, not_19_out, not_20_out, not_21_out);
  and and_3 (and_3_out, not_22_out, not_23_out, not_24_out, not_25_out, not_26_out, not_27_out, F5, not_28_out, not_29_out, not_30_out, not_31_out, F0);
  and and_4 (and_4_out, not_32_out, not_33_out, not_34_out, not_35_out, not_36_out, not_37_out, F5, not_38_out, not_39_out, F2, not_40_out, not_41_out);
  and and_5 (and_5_out, not_42_out, not_43_out, not_44_out, not_45_out, not_46_out, not_47_out, F5, not_48_out, F3, not_49_out, F1, not_50_out);
  and and_6 (and_6_out, not_51_out, not_52_out, OP3, not_53_out, not_54_out, not_55_out);
  and and_7 (and_7_out, not_56_out, not_57_out, OP3, OP2, not_58_out, not_59_out);
  and and_8 (and_8_out, not_60_out, not_61_out, OP3, not_62_out, not_63_out, OP0);
  and and_9 (and_9_out, not_64_out, not_65_out, OP3, not_66_out, OP1, not_67_out);
  and and_10 (and_10_out, OP5, not_68_out, not_69_out, not_70_out, OP1, OP0);
  and and_11 (and_11_out, OP5, not_71_out, OP3, not_72_out, OP1, OP0);
  and and_12 (and_12_out, not_73_out, not_74_out, not_75_out, not_76_out, not_77_out, not_78_out, not_79_out, not_80_out, not_81_out, F2, F1, F0);
  and and_13 (and_13_out, not_82_out, not_83_out, not_84_out, not_85_out, not_86_out, not_87_out, F5, not_88_out, not_89_out, F2, F1, not_90_out);
  and and_14 (and_14_out, OP5, not_91_out, not_92_out, not_93_out, not_94_out, OP0);
  and and_15 (and_15_out, not_95_out, not_96_out, not_97_out, not_98_out, not_99_out, not_100_out, not_101_out, not_102_out, not_103_out, not_104_out, F1, not_105_out);
  and and_16 (and_16_out, not_106_out, not_107_out, not_108_out, not_109_out, not_110_out, not_111_out, F5, not_112_out, not_113_out, not_114_out, F1, not_115_out);
  and and_17 (and_17_out, not_116_out, not_117_out, not_118_out, not_119_out, not_120_out, not_121_out, F5, not_122_out, not_123_out, F2, not_124_out, not_125_out);
  and and_18 (and_18_out, not_126_out, not_127_out, not_128_out, not_129_out, not_130_out, not_131_out, F5, not_132_out, not_133_out, F2, F1, F0);
  and and_19 (and_19_out, not_134_out, not_135_out, not_136_out, not_137_out, not_138_out, not_139_out, F5, not_140_out, F3, not_141_out, F1, not_142_out);
  and and_20 (and_20_out, not_143_out, not_144_out, OP3, OP2, not_145_out, not_146_out);
  and and_21 (and_21_out, not_147_out, not_148_out, OP3, not_149_out, OP1, not_150_out);
  and and_22 (and_22_out, not_151_out, not_152_out, not_153_out, not_154_out, not_155_out, not_156_out, F5, not_157_out, not_158_out, not_159_out, not_160_out, not_161_out);
  and and_23 (and_23_out, not_162_out, not_163_out, not_164_out, not_165_out, not_166_out, not_167_out, F5, not_168_out, not_169_out, not_170_out, not_171_out, F0);
  and and_24 (and_24_out, not_172_out, not_173_out, not_174_out, not_175_out, not_176_out, not_177_out, F5, not_178_out, not_179_out, not_180_out, F1, not_181_out);
  and and_25 (and_25_out, not_182_out, not_183_out, not_184_out, not_185_out, not_186_out, not_187_out, F5, not_188_out, not_189_out, F2, not_190_out, not_191_out);
  and and_26 (and_26_out, not_192_out, not_193_out, not_194_out, not_195_out, not_196_out, not_197_out, F5, not_198_out, F3, not_199_out, F1, F0);
  and and_27 (and_27_out, not_200_out, not_201_out, OP3, not_202_out, not_203_out, not_204_out);
  and and_28 (and_28_out, not_205_out, not_206_out, OP3, OP2, not_207_out, not_208_out);
  and and_29 (and_29_out, not_209_out, not_210_out, OP3, not_211_out, not_212_out, OP0);
  and and_30 (and_30_out, OP5, not_213_out, not_214_out, not_215_out, OP1, OP0);
  and and_31 (and_31_out, OP5, not_216_out, OP3, not_217_out, OP1, OP0);
  and and_32 (and_32_out, OP5, not_218_out, not_219_out, not_220_out, not_221_out, OP0);
  and and_33 (and_33_out, not_222_out, not_223_out, not_224_out, not_225_out, not_226_out, not_227_out, F5, not_228_out, not_229_out, F2, not_230_out, F0);
  and and_34 (and_34_out, not_231_out, not_232_out, not_233_out, not_234_out, not_235_out, not_236_out, F5, not_237_out, not_238_out, F2, F1, F0);
  and and_35 (and_35_out, not_239_out, not_240_out, not_241_out, not_242_out, not_243_out, not_244_out, F5, not_245_out, F3, not_246_out, F1, not_247_out);
  and and_36 (and_36_out, not_248_out, not_249_out, not_250_out, not_251_out, not_252_out, not_253_out, F5, not_254_out, F3, not_255_out, F1, F0);
  and and_37 (and_37_out, not_256_out, not_257_out, OP3, not_258_out, OP1, not_259_out);
  and and_38 (and_38_out, not_260_out, not_261_out, OP3, OP2, not_262_out, OP0);
  and and_39 (and_39_out, not_263_out, not_264_out, not_265_out, not_266_out, not_267_out, not_268_out, F5, not_269_out, not_270_out, F2, F1, not_271_out);
  or or_1 (S1, and_15_out, and_16_out, and_17_out, and_18_out, and_19_out, and_20_out, and_21_out);
  or or_2 (S2, and_22_out, and_23_out, and_24_out, and_25_out, and_26_out, and_27_out, and_28_out, and_29_out, and_30_out, and_31_out, and_32_out);
  or or_3 (S3, and_33_out, and_34_out, and_35_out, and_36_out, and_37_out, and_38_out, and_39_out);
  or or_4 (S0, and_1_out, and_2_out, and_3_out, and_4_out, and_5_out, and_6_out, and_7_out, and_8_out, and_9_out, and_10_out, and_11_out, and_12_out, and_13_out, and_14_out);
endmodule

// 控制信号生成
module \控制信号自动生成  (
  input  OP0,
  input  OP1,
  input  OP2,
  input  OP3,
  input  OP4,
  input  OP5,
  input  F0,
  input  F1,
  input  F2,
  input  F3,
  input  F4,
  input  F5,
  output MemToReg,
  output MemWrite,
  output ALU_SRC,
  output RegWrite,
  output SysCALL,
  output SignedExt,
  output RegDst,
  output BEQ,
  output BNE,
  output JR,
  output JUMP,
  output JAL,
  output ERET
);

  wire and_3_out, and_4_out, and_5_out, and_6_out, and_7_out, and_8_out, and_9_out, and_10_out, and_11_out,
       and_12_out, and_13_out, and_15_out, and_16_out, and_17_out, and_18_out, and_19_out, and_20_out,
       and_21_out, and_22_out, and_23_out, and_27_out, and_28_out, not_1_out, not_2_out, not_3_out,
       not_4_out, not_5_out, not_6_out, not_7_out, not_8_out, not_9_out, not_10_out, not_11_out, not_12_out,
       not_13_out, not_14_out, not_15_out, not_16_out, not_17_out, not_18_out, not_19_out, not_20_out,
       not_21_out, not_22_out, not_23_out, not_24_out, not_25_out, not_26_out, not_27_out, not_28_out,
       not_29_out, not_30_out, not_31_out, not_32_out, not_33_out, not_34_out, not_35_out, not_36_out,
       not_37_out, not_38_out, not_39_out, not_40_out, not_41_out, not_42_out, not_43_out, not_44_out,
       not_45_out, not_46_out, not_47_out, not_48_out, not_49_out, not_50_out, not_51_out, not_52_out,
       not_53_out, not_54_out, not_55_out, not_56_out, not_57_out, not_58_out, not_59_out, not_60_out,
       not_61_out, not_62_out, not_63_out, not_64_out, not_65_out, not_66_out, not_67_out, not_68_out,
       not_69_out, not_70_out, not_71_out, not_72_out, not_73_out, not_74_out, not_75_out, not_76_out,
       not_77_out, not_78_out, not_79_out, not_80_out, not_81_out, not_82_out, not_83_out, not_84_out,
       not_85_out, not_86_out, not_87_out, not_88_out, not_89_out, not_90_out, not_91_out, not_92_out,
       not_93_out, not_94_out, not_95_out, not_96_out, not_97_out, not_98_out, not_99_out, not_100_out,
       not_101_out, not_102_out, not_103_out, not_104_out, not_105_out, not_106_out, not_107_out,
       not_108_out, not_109_out, not_110_out, not_111_out, not_112_out, not_113_out, not_114_out,
       not_115_out, not_116_out, not_117_out, not_118_out, not_119_out, not_120_out, not_121_out,
       not_122_out, not_123_out, not_124_out, not_125_out, not_126_out, not_127_out, not_128_out,
       not_129_out, not_130_out, not_131_out, not_132_out, not_133_out, not_134_out, not_135_out,
       not_136_out, not_137_out, not_138_out, not_139_out, not_140_out, not_141_out, not_142_out,
       not_143_out, not_144_out, not_145_out, not_146_out, not_147_out, not_148_out, not_149_out,
       not_150_out, not_151_out, not_152_out, not_153_out, not_154_out, not_155_out, not_156_out,
       not_157_out, not_158_out, not_159_out, not_160_out, not_161_out, not_162_out, not_163_out,
       not_164_out, not_165_out, not_166_out, not_167_out, not_168_out, not_169_out, not_170_out,
       not_171_out, not_172_out, not_173_out, not_174_out, not_175_out, not_176_out;

  not not_1 (not_1_out, OP2);
  not not_2 (not_2_out, OP3);
  not not_3 (not_3_out, OP4);
  not not_4 (not_4_out, OP2);
  not not_5 (not_5_out, OP4);
  not not_6 (not_6_out, OP0);
  not not_7 (not_7_out, OP2);
  not not_8 (not_8_out, OP4);
  not not_9 (not_9_out, OP5);
  not not_10 (not_10_out, OP1);
  not not_11 (not_11_out, OP4);
  not not_12 (not_12_out, OP5);
  not not_13 (not_13_out, OP2);
  not not_14 (not_14_out, OP4);
  not not_15 (not_15_out, OP0);
  not not_16 (not_16_out, OP1);
  not not_17 (not_17_out, OP2);
  not not_18 (not_18_out, OP4);
  not not_19 (not_19_out, OP5);
  not not_20 (not_20_out, F0);
  not not_21 (not_21_out, F2);
  not not_22 (not_22_out, F3);
  not not_23 (not_23_out, F4);
  not not_24 (not_24_out, OP0);
  not not_25 (not_25_out, OP1);
  not not_26 (not_26_out, OP2);
  not not_27 (not_27_out, OP4);
  not not_28 (not_28_out, OP5);
  not not_29 (not_29_out, F1);
  not not_30 (not_30_out, F3);
  not not_31 (not_31_out, F4);
  not not_32 (not_32_out, OP0);
  not not_33 (not_33_out, OP1);
  not not_34 (not_34_out, OP2);
  not not_35 (not_35_out, OP4);
  not not_36 (not_36_out, OP5);
  not not_37 (not_37_out, F2);
  not not_38 (not_38_out, F3);
  not not_39 (not_39_out, F4);
  not not_40 (not_40_out, F5);
  not not_41 (not_41_out, OP0);
  not not_42 (not_42_out, OP1);
  not not_43 (not_43_out, OP2);
  not not_44 (not_44_out, OP4);
  not not_45 (not_45_out, OP5);
  not not_46 (not_46_out, F2);
  not not_47 (not_47_out, F4);
  not not_48 (not_48_out, OP0);
  not not_49 (not_49_out, OP1);
  not not_50 (not_50_out, OP2);
  not not_51 (not_51_out, OP4);
  not not_52 (not_52_out, OP5);
  not not_53 (not_53_out, F3);
  not not_54 (not_54_out, F4);
  not not_55 (not_55_out, OP0);
  not not_56 (not_56_out, OP2);
  not not_57 (not_57_out, OP4);
  not not_58 (not_58_out, OP5);
  not not_59 (not_59_out, OP1);
  not not_60 (not_60_out, OP4);
  not not_61 (not_61_out, OP5);
  not not_62 (not_62_out, OP2);
  not not_63 (not_63_out, OP3);
  not not_64 (not_64_out, OP4);
  not not_65 (not_65_out, OP0);
  not not_66 (not_66_out, OP1);
  not not_67 (not_67_out, OP2);
  not not_68 (not_68_out, OP3);
  not not_69 (not_69_out, OP4);
  not not_70 (not_70_out, OP5);
  not not_71 (not_71_out, F0);
  not not_72 (not_72_out, F1);
  not not_73 (not_73_out, F4);
  not not_74 (not_74_out, F5);
  not not_75 (not_75_out, OP0);
  not not_76 (not_76_out, OP2);
  not not_77 (not_77_out, OP4);
  not not_78 (not_78_out, OP5);
  not not_79 (not_79_out, OP1);
  not not_80 (not_80_out, OP2);
  not not_81 (not_81_out, OP4);
  not not_82 (not_82_out, OP5);
  not not_83 (not_83_out, OP1);
  not not_84 (not_84_out, OP3);
  not not_85 (not_85_out, OP4);
  not not_86 (not_86_out, OP5);
  not not_87 (not_87_out, OP2);
  not not_88 (not_88_out, OP4);
  not not_89 (not_89_out, OP0);
  not not_90 (not_90_out, OP1);
  not not_91 (not_91_out, OP2);
  not not_92 (not_92_out, OP3);
  not not_93 (not_93_out, OP4);
  not not_94 (not_94_out, OP5);
  not not_95 (not_95_out, F0);
  not not_96 (not_96_out, F2);
  not not_97 (not_97_out, F3);
  not not_98 (not_98_out, F4);
  not not_99 (not_99_out, OP0);
  not not_100 (not_100_out, OP1);
  not not_101 (not_101_out, OP2);
  not not_102 (not_102_out, OP3);
  not not_103 (not_103_out, OP4);
  not not_104 (not_104_out, OP5);
  not not_105 (not_105_out, F1);
  not not_106 (not_106_out, F3);
  not not_107 (not_107_out, F4);
  not not_108 (not_108_out, OP0);
  not not_109 (not_109_out, OP1);
  not not_110 (not_110_out, OP2);
  not not_111 (not_111_out, OP3);
  not not_112 (not_112_out, OP4);
  not not_113 (not_113_out, OP5);
  not not_114 (not_114_out, F2);
  not not_115 (not_115_out, F3);
  not not_116 (not_116_out, F4);
  not not_117 (not_117_out, F5);
  not not_118 (not_118_out, OP0);
  not not_119 (not_119_out, OP1);
  not not_120 (not_120_out, OP2);
  not not_121 (not_121_out, OP3);
  not not_122 (not_122_out, OP4);
  not not_123 (not_123_out, OP5);
  not not_124 (not_124_out, F2);
  not not_125 (not_125_out, F4);
  not not_126 (not_126_out, OP0);
  not not_127 (not_127_out, OP1);
  not not_128 (not_128_out, OP2);
  not not_129 (not_129_out, OP3);
  not not_130 (not_130_out, OP4);
  not not_131 (not_131_out, OP5);
  not not_132 (not_132_out, F3);
  not not_133 (not_133_out, F4);
  not not_134 (not_134_out, OP0);
  not not_135 (not_135_out, OP1);
  not not_136 (not_136_out, OP3);
  not not_137 (not_137_out, OP4);
  not not_138 (not_138_out, OP5);
  not not_139 (not_139_out, OP1);
  not not_140 (not_140_out, OP3);
  not not_141 (not_141_out, OP4);
  not not_142 (not_142_out, OP5);
  not not_143 (not_143_out, OP0);
  not not_144 (not_144_out, OP1);
  not not_145 (not_145_out, OP2);
  not not_146 (not_146_out, OP3);
  not not_147 (not_147_out, OP4);
  not not_148 (not_148_out, OP5);
  not not_149 (not_149_out, F0);
  not not_150 (not_150_out, F1);
  not not_151 (not_151_out, F2);
  not not_152 (not_152_out, F4);
  not not_153 (not_153_out, F5);
  not not_154 (not_154_out, OP0);
  not not_155 (not_155_out, OP2);
  not not_156 (not_156_out, OP3);
  not not_157 (not_157_out, OP4);
  not not_158 (not_158_out, OP5);
  not not_159 (not_159_out, F0);
  not not_160 (not_160_out, F1);
  not not_161 (not_161_out, F2);
  not not_162 (not_162_out, F4);
  not not_163 (not_163_out, F5);
  not not_164 (not_164_out, OP2);
  not not_165 (not_165_out, OP3);
  not not_166 (not_166_out, OP4);
  not not_167 (not_167_out, OP5);
  not not_168 (not_168_out, OP2);
  not not_169 (not_169_out, OP3);
  not not_170 (not_170_out, OP4);
  not not_171 (not_171_out, OP5);
  not not_172 (not_172_out, OP5);
  not not_173 (not_173_out, OP3);
  not not_174 (not_174_out, OP2);
  not not_175 (not_175_out, OP1);
  not not_176 (not_176_out, OP0);
  and and_1 (MemToReg, OP0, OP1, not_1_out, not_2_out, not_3_out, OP5);
  and and_2 (MemWrite, OP0, OP1, not_4_out, OP3, not_5_out, OP5);
  and and_3 (and_3_out, not_6_out, not_7_out, OP3, not_8_out, not_9_out);
  or or_1 (ALU_SRC, and_3_out, and_4_out, and_5_out);
  and and_4 (and_4_out, not_10_out, OP3, not_11_out, not_12_out);
  and and_5 (and_5_out, OP0, OP1, not_13_out, not_14_out, OP5);
  and and_6 (and_6_out, not_15_out, not_16_out, not_17_out, not_18_out, not_19_out, not_20_out, not_21_out, not_22_out, not_23_out);
  and and_7 (and_7_out, not_24_out, not_25_out, not_26_out, not_27_out, not_28_out, not_29_out, not_30_out, not_31_out, F5);
  and and_8 (and_8_out, not_32_out, not_33_out, not_34_out, not_35_out, not_36_out, F1, not_37_out, not_38_out, not_39_out, not_40_out);
  and and_9 (and_9_out, not_41_out, not_42_out, not_43_out, not_44_out, not_45_out, F1, not_46_out, F3, not_47_out, F5);
  and and_10 (and_10_out, not_48_out, not_49_out, not_50_out, not_51_out, not_52_out, F0, F2, not_53_out, not_54_out, F5);
  and and_11 (and_11_out, not_55_out, not_56_out, OP3, not_57_out, not_58_out);
  and and_12 (and_12_out, not_59_out, OP3, not_60_out, not_61_out);
  and and_13 (and_13_out, OP0, OP1, not_62_out, not_63_out, not_64_out);
  and and_14 (SysCALL, not_65_out, not_66_out, not_67_out, not_68_out, not_69_out, not_70_out, not_71_out, not_72_out, F2, F3, not_73_out, not_74_out);
  and and_15 (and_15_out, not_75_out, not_76_out, OP3, not_77_out, not_78_out);
  and and_16 (and_16_out, not_79_out, not_80_out, OP3, not_81_out, not_82_out);
  and and_17 (and_17_out, not_83_out, OP2, not_84_out, not_85_out, not_86_out);
  and and_18 (and_18_out, OP0, OP1, not_87_out, not_88_out, OP5);
  and and_19 (and_19_out, not_89_out, not_90_out, not_91_out, not_92_out, not_93_out, not_94_out, not_95_out, not_96_out, not_97_out, not_98_out);
  and and_20 (and_20_out, not_99_out, not_100_out, not_101_out, not_102_out, not_103_out, not_104_out, not_105_out, not_106_out, not_107_out, F5);
  and and_21 (and_21_out, not_108_out, not_109_out, not_110_out, not_111_out, not_112_out, not_113_out, F1, not_114_out, not_115_out, not_116_out, not_117_out);
  and and_22 (and_22_out, not_118_out, not_119_out, not_120_out, not_121_out, not_122_out, not_123_out, F1, not_124_out, F3, not_125_out, F5);
  and and_23 (and_23_out, not_126_out, not_127_out, not_128_out, not_129_out, not_130_out, not_131_out, F0, F2, not_132_out, not_133_out, F5);
  and and_24 (BEQ, not_134_out, not_135_out, OP2, not_136_out, not_137_out, not_138_out);
  and and_25 (BNE, OP0, not_139_out, OP2, not_140_out, not_141_out, not_142_out);
  and and_26 (JR, not_143_out, not_144_out, not_145_out, not_146_out, not_147_out, not_148_out, not_149_out, not_150_out, not_151_out, F3, not_152_out, not_153_out);
  and and_27 (and_27_out, not_154_out, not_155_out, not_156_out, not_157_out, not_158_out, not_159_out, not_160_out, not_161_out, F3, not_162_out, not_163_out);
  and and_28 (and_28_out, OP1, not_164_out, not_165_out, not_166_out, not_167_out);
  and and_29 (JAL, OP0, OP1, not_168_out, not_169_out, not_170_out, not_171_out);
  and and_30 (ERET, not_172_out, OP4, not_173_out, not_174_out, not_175_out, not_176_out);
  or or_2 (RegWrite, and_6_out, and_7_out, and_8_out, and_9_out, and_10_out, and_11_out, and_12_out, and_13_out);
  or or_3 (SignedExt, and_15_out, and_16_out, and_17_out, and_18_out);
  or or_4 (RegDst, and_19_out, and_20_out, and_21_out, and_22_out, and_23_out);
  or or_5 (JUMP, and_27_out, and_28_out);
endmodule
