// Logisim project 练炳诚_CS1705_U201714707_动态分支预测.circ as structural Verilog: 13 circuits, main circuit ◇动态分支预测
module \动态分支预测  (
  output RegWrite,
  output MemWrite,
  output [31:0] IF_PC,
  output [31:0] ID_PC,
  output [31:0] EX_PC,
  output [31:0] M_PC,
  output [31:0] WB_PC,
  output [31:0] RDin,
  output [31:0] MDin,
  output [31:0] LedData
);

  wire ALU_SRC, and_1_out, and_2_out, and_3_out, and_4_out, and_5_out, and_6_out, and_7_out, and_8_out,
       and_10_out, and_11_out, BEQ, BHT_Branch, BLEZ, BNE, Branch, bubble, CLK, comparator_1_eq,
       comparator_2_eq, comparator_3_gt, equal, EX_Branch, EX_Branch_J_JAL, ex_mem_1_jal_2, ex_mem_1_lh_2,
       ex_mem_1_regdst_2, ex_mem_1_syscall_2, EX_MemToReg, EX_PredictFail, EX_PredictSuccess, EX_RegWrite,
       EX_syscall, GO, Go_t, Halt, id_ex_1_lh_2, id_ex_1_memwrite_2, id_ex_1_regdst_2, ID_syscall, IR1, IR2,
       IR3, J_JAL, JAL, JMP, JR, load_use, MEM_MemToReg, MEM_RegWrite, mem_wb_1_jal_2, mem_wb_1_lh_2,
       mem_wb_1_memtoreg_2, mem_wb_1_regdst_2, multiplexer_5_out, multiplexer_6_out, multiplexer_7_out,
       multiplexer_8_out, not_1_out, not_2_out, not_3_out, or_1_out, or_2_out, or_3_out, or_4_out, or_5_out,
       PredictFail, PredictSuccess, register_1_q, register_2_q, register_3_q, RST, Sequence, SignedExt, SRAV,
       Syscall, undriven, W1, W2, W3, \单周期硬布线控制器_1_alu_src , \单周期硬布线控制器_1_beq , \单周期硬布线控制器_1_blez ,
       \单周期硬布线控制器_1_bne , \单周期硬布线控制器_1_jal , \单周期硬布线控制器_1_jmp , \单周期硬布线控制器_1_jr , \单周期硬布线控制器_1_lh ,
       \单周期硬布线控制器_1_memtoreg , \单周期硬布线控制器_1_memwrite , \单周期硬布线控制器_1_regdst , \单周期硬布线控制器_1_regwrite ,
       \单周期硬布线控制器_1_srav , \源寄存器使用情况_1_r1_used , \源寄存器使用情况_1_r2_used ;
  wire [1:0] EX_ForwardA, EX_ForwardB, ForwardA, ForwardB;
  wire [3:0] ALU_OP, \单周期硬布线控制器_1_alu_op ;
  wire [4:0] ex_mem_1_rd_num_2, ex_mem_1_rt_num_2, EX_W_num, id_ex_1_rd_num_2, id_ex_1_rt_num_2,
       id_ex_1_shamt_2, MEM_W_num, mem_wb_1_rd_num_2, mem_wb_1_rt_num_2, multiplexer_12_out,
       multiplexer_17_out, multiplexer_18_out, multiplexer_24_out, R1_num, R2_num, WB_num;
  wire [15:0] \LoadUse次数 , multiplexer_20_out, \总周期数 , \插入气泡数 , \无条件分支数 , \条件分支成功数 , \预测分支失败次数 , \预测分支成功次数 ;
  wire [27:0] if_id_1_sequence_addr_2;
  wire [31:0] A, a0, a0_prime, adder_1_out, adder_2_out, B, bit_extender_1_out, bit_extender_2_out,
       bit_extender_3_out, Branch_J_JAL_addr, Breanch_addr, EX_IR, EX_NewPC, id_ex_1_imm_2, ID_IR, IF_IR,
       JMP_addr, MEM_ALU_Result, MEM_IR, mem_wb_1_hw_2, mem_wb_1_md_2, mips_alu_2_result, mips_alu_3_result,
       multiplexer_1_out, multiplexer_3_out, multiplexer_4_out, multiplexer_11_out, multiplexer_16_out,
       multiplexer_21_out, multiplexer_22_out, PredictPC, ram_1_data, register_6_q, Sequence_addr,
       shifter_1_out, v0, v0_prime, v0_prime_prime, WB_ALU_Result, WB_IR;
  wire [31:28] if_id_1_sequence_addr_2_2;

  Button \u_总复位  (.out(RST));
  Button _1 (.out(IR1));
  Button _2 (.out(IR2));
  Button _3 (.out(IR3));
  // Probe on \总周期数 
  // Probe on \总周期数 
  Button \u_继续运行  (.out(Go_t));
  LED #(.active("true")) led_1 (.in(W1));
  LED #(.active("true")) led_2 (.in(W2));
  LED #(.active("true")) led_3 (.in(W3));
  Hex_Digit_Display hex_digit_display_1 (.value(LedData[31:28]));  // open: dp
  // Probe on IF_PC[19:0]
  // Mips_Probe mips_probe_1: pin names not known; wires that end beside it: IF_IR
  Adder #(.width(32)) adder_1 (.a(EX_PC), .b(32'h4), .out(adder_1_out));  // open: cin, cout
  Multiplexer #(.select(1), .width(32), .disabled("Z"), .enable("false")) multiplexer_1 (
    .in0(PredictPC), .in1(EX_NewPC), .out(multiplexer_1_out), .sel(bubble));
  D_Flip_Flop #(.trigger("high"), .Pre_Clr_Positions("ABOVE_BELOW"), .NegatePresetClear("false"), .enable("false"), .NewFFLayout("true")) d_ff_1 (
    .clk(Go_t), .D(1'b1), .Q(GO), .reset(register_1_q));  // open: Qn, preset
  Register #(.width(1), .trigger("rising"), .Select("low")) register_1 (
    .D(GO), .Q(register_1_q), .clk(CLK));  // open: en, clr
  Hex_Digit_Display hex_digit_display_2 (.value(LedData[23:20]));  // open: dp
  Hex_Digit_Display hex_digit_display_3 (.value(LedData[27:24]));  // open: dp
  // Probe on ID_PC[19:0]
  // Mips_Probe mips_probe_2: pin names not known; wires that end beside it: ID_IR
  // Probe on \预测分支成功次数 
  // Probe on \预测分支失败次数 
  Multiplexer #(.select(1), .width(32), .disabled("Z"), .enable("false")) multiplexer_2 (
    .in0(adder_1_out), .in1(Branch_J_JAL_addr), .out(EX_NewPC), .sel(BHT_Branch));
  Multiplexer #(.select(1), .width(32), .disabled("Z"), .enable("false")) multiplexer_3 (
    .in0(multiplexer_1_out), .in1(A), .out(multiplexer_3_out), .sel(JR));
  Hex_Digit_Display hex_digit_display_4 (.value(LedData[19:16]));  // open: dp
  Hex_Digit_Display hex_digit_display_5 (.value(LedData[15:12]));  // open: dp
  and and_1 (and_1_out, EX_PredictSuccess, EX_Branch);
  and and_2 (and_2_out, EX_Branch, EX_PredictFail);
  Register #(.width(32), .trigger("rising"), .Select("low")) PC (
    .D(multiplexer_4_out), .en(or_1_out), .Q(IF_PC), .clk(CLK));  // open: clr
  Multiplexer #(.select(1), .width(32), .disabled("Z"), .enable("false")) multiplexer_4 (
    .in0(multiplexer_3_out), .in1(adder_1_out), .out(multiplexer_4_out), .sel(GO));
  or or_1 (or_1_out, GO, and_3_out);
  and and_3 (and_3_out, not_1_out, Halt);
  not not_1 (not_1_out, load_use);
  Hex_Digit_Display hex_digit_display_6 (.value(LedData[11:8]));  // open: dp
  Hex_Digit_Display hex_digit_display_7 (.value(LedData[7:4]));  // open: dp
  Clock #(.highDuration(1), .lowDuration(1)) clock_1 (.out(CLK));
  // Probe on EX_PC[19:0]
  // Mips_Probe mips_probe_3: pin names not known; wires that end beside it: EX_IR
  Counter #(.width(16), .max('hffff), .ongoal("wrap"), .trigger("rising"), .behavior("new")) counter_1 (
    .count(Branch), .Q(\条件分支成功数 ), .clk(CLK));  // open: load, D, carry, clr, preset, down
  Counter #(.width(16), .max('hffff), .ongoal("wrap"), .trigger("rising"), .behavior("new")) counter_2 (
    .count(JMP), .Q(\无条件分支数 ), .clk(CLK));  // open: load, D, carry, clr, preset, down
  Counter #(.width(16), .max('hffff), .ongoal("wrap"), .trigger("rising"), .behavior("new")) counter_3 (
    .count(load_use), .Q(\LoadUse次数 ), .clk(CLK));  // open: load, D, carry, clr, preset, down
  Counter #(.width(16), .max('hffff), .ongoal("wrap"), .trigger("rising"), .behavior("new")) counter_4 (
    .count(and_1_out), .Q(\预测分支成功次数 ), .clk(CLK));  // open: load, D, carry, clr, preset, down
  Counter #(.width(16), .max('hffff), .ongoal("wrap"), .trigger("rising"), .behavior("new")) counter_5 (
    .count(and_2_out), .Q(\预测分支失败次数 ), .clk(CLK));  // open: load, D, carry, clr, preset, down
  Counter #(.width(16), .max('hffff), .ongoal("wrap"), .trigger("rising"), .behavior("new")) counter_6 (
    .count(bubble), .Q(\插入气泡数 ), .clk(CLK));  // open: load, D, carry, clr, preset, down
  Hex_Digit_Display hex_digit_display_8 (.value(LedData[3:0]));  // open: dp
  MIPS_ALU mips_alu_1 (.X(IF_PC), .Y(32'h4), .AluOP(4'b0101), .Result(Sequence_addr));  // open: Equal, Result_2, shamt
  not not_2 (not_2_out, load_use);
  Multiplexer #(.select(1), .width(1), .disabled("Z"), .enable("false")) multiplexer_5 (
    .in0(PredictSuccess), .in1(1'b0), .out(multiplexer_5_out), .sel(bubble));
  Multiplexer #(.select(1), .width(1), .disabled("Z"), .enable("false")) multiplexer_6 (
    .in0(PredictFail), .in1(1'b0), .out(multiplexer_6_out), .sel(bubble));
  // Probe on \总周期数 
  // Probe on M_PC[19:0]
  // Mips_Probe mips_probe_4: pin names not known; wires that end beside it: MEM_IR
  ROM #(.addrWidth(10), .dataWidth(32), .Select("high")) rom_1 (.addr(IF_PC[11:2]), .data(IF_IR));
  Register #(.width(1), .trigger("rising"), .Select("low")) register_2 (
    .D(multiplexer_5_out), .en(not_2_out), .Q(register_2_q), .clk(CLK));  // open: clr
  Register #(.width(1), .trigger("rising"), .Select("low")) register_3 (
    .D(multiplexer_6_out), .en(not_2_out), .Q(register_3_q), .clk(CLK));  // open: clr
  // Probe on \总周期数 
  // Probe on \无条件分支数 
  // Probe on \条件分支成功数 
  // Probe on \插入气泡数 
  // Probe on \LoadUse次数 
  not not_3 (not_3_out, load_use);
  or or_2 (or_2_out, GO, bubble);
  or or_3 (or_3_out, bubble, load_use);
  // Probe on IF_PC[11:0]
  // Probe on WB_PC[19:0]
  // Mips_Probe mips_probe_5: pin names not known; wires that end beside it: WB_IR
  IF_ID if_id_1 (
    .PC(IF_PC), .IR(IF_IR), .PC_2(ID_PC), .IR_2(ID_IR), .CLK(CLK), .clr(or_2_out), .EN(not_3_out),
    .Sequence_addr(Sequence_addr), .Sequence_addr_2({if_id_1_sequence_addr_2_2, if_id_1_sequence_addr_2}));
  Multiplexer #(.select(1), .width(1), .disabled("Z"), .enable("false")) multiplexer_7 (
    .in0(register_2_q), .in1(1'b0), .out(multiplexer_7_out), .sel(or_3_out));
  Multiplexer #(.select(1), .width(1), .disabled("Z"), .enable("false")) multiplexer_8 (
    .in0(register_3_q), .in1(1'b0), .out(multiplexer_8_out), .sel(or_3_out));
  // Probe on ID_PC[11:0]
  // Probe on EX_PC[11:0]
  Register #(.width(1), .trigger("rising"), .Select("low")) register_4 (
    .D(multiplexer_7_out), .Q(EX_PredictSuccess), .clk(CLK));  // open: en, clr
  Register #(.width(1), .trigger("rising"), .Select("low")) register_5 (
    .D(multiplexer_8_out), .Q(EX_PredictFail), .clk(CLK));  // open: en, clr
  // Probe on M_PC[11:0]
  Comparator #(.width(32), .mode("twosComplement")) comparator_1 (
    .a(v0_prime), .b(32'h22), .eq(comparator_1_eq));  // open: gt, lt
  Comparator #(.width(32), .mode("twosComplement")) comparator_2 (
    .a(v0_prime), .b(32'h22), .eq(comparator_2_eq));  // open: gt, lt
  \源寄存器使用情况  \u_源寄存器使用情况_1  (
    .OP0(ID_IR[26]), .OP1(ID_IR[27]), .OP2(ID_IR[28]), .OP3(ID_IR[29]), .OP4(ID_IR[30]), .OP5(ID_IR[31]),
    .F0(ID_IR[0]), .F1(ID_IR[1]), .F2(ID_IR[2]), .F3(ID_IR[3]), .F4(ID_IR[4]), .F5(ID_IR[5]),
    .R1_Used(\源寄存器使用情况_1_r1_used ), .R2_Used(\源寄存器使用情况_1_r2_used ));
  \单周期硬布线控制器  \u_单周期硬布线控制器_1  (
    .Func(ID_IR[5:0]), .OP(ID_IR[31:26]), .ALU_OP(\单周期硬布线控制器_1_alu_op ), .MemToReg(\单周期硬布线控制器_1_memtoreg ),
    .MemWrite(\单周期硬布线控制器_1_memwrite ), .ALU_SRC(\单周期硬布线控制器_1_alu_src ), .RegWrite(\单周期硬布线控制器_1_regwrite ),
    .SysCALL(ID_syscall), .SignedExt(SignedExt), .RegDst(\单周期硬布线控制器_1_regdst ), .JR(\单周期硬布线控制器_1_jr ),
    .JMP(\单周期硬布线控制器_1_jmp ), .Beq(\单周期硬布线控制器_1_beq ), .JAL(\单周期硬布线控制器_1_jal ), .Bne(\单周期硬布线控制器_1_bne ),
    .LH(\单周期硬布线控制器_1_lh ), .BLEZ(\单周期硬布线控制器_1_blez ), .SRAV(\单周期硬布线控制器_1_srav ));
  Multiplexer #(.select(1), .width(5), .disabled("Z"), .enable("false")) multiplexer_9 (
    .in0(ID_IR[25:21]), .in1(5'b00010), .out(R1_num), .sel(ID_syscall));
  Multiplexer #(.select(1), .width(5), .disabled("Z"), .enable("false")) multiplexer_10 (
    .in0(ID_IR[20:16]), .in1(5'b00100), .out(R2_num), .sel(ID_syscall));
  assign bit_extender_1_out = {{16{ID_IR[15]}}, ID_IR[15:0]};  // Bit_Extender bit_extender_1
  assign bit_extender_2_out = {{16{1'b0}}, ID_IR[15:0]};  // Bit_Extender bit_extender_2
  // Probe on WB_PC[11:0]
  Multiplexer #(.select(1), .width(32), .disabled("Z"), .enable("false")) multiplexer_11 (
    .in0(bit_extender_2_out), .in1(bit_extender_1_out), .out(multiplexer_11_out), .sel(SignedExt));
  and and_4 (and_4_out, EX_syscall, comparator_1_eq);
  Register #(.width(32), .trigger("rising"), .Select("low")) register_6 (
    .D(v0_prime), .Q(register_6_q), .clk(CLK));  // open: en, clr
  not not_4 (Halt, and_5_out);
  and and_5 (and_5_out, ~comparator_2_eq, EX_syscall);  // AND_Gate
  MIPS_Regifile mips_regifile_1 (
    .Din(RDin), .Clk(CLK), .R1(v0), .R2(a0), .WE(RegWrite), .W_num(WB_num), .R1_num(R1_num), .R2_num(R2_num));
  Shifter #(.width(32), .shift("ll")) shifter_1 (.in(bit_extender_1_out), .\dist (5'b00010), .out(shifter_1_out));
  Register #(.width(32), .trigger("rising"), .Select("low")) register_7 (
    .D(a0_prime), .en(and_4_out), .Q(LedData), .clk(CLK), .preset(undriven));  // open: clr, cs
  Register #(.width(32), .trigger("rising"), .Select("low")) register_8 (
    .D(register_6_q), .Q(v0_prime_prime), .clk(CLK));  // open: en, clr
  \重定向数据选择信号产生  \u_重定向数据选择信号产生_1  (
    .R1_num(R1_num), .R2_num(R2_num), .R1_Used(\源寄存器使用情况_1_r1_used ), .R2_Used(\源寄存器使用情况_1_r2_used ),
    .EX_W_num(EX_W_num), .EX_RegWrite(EX_RegWrite), .EX_MemToReg(EX_MemToReg), .MEM_W_num(MEM_W_num),
    .MEM_RegWrite(MEM_RegWrite), .MEM_MemToReg(MEM_MemToReg), .ForwardA(ForwardA), .ForwardB(ForwardB),
    .load_use(load_use));
  MIPS_ALU mips_alu_2 (
    .X(shifter_1_out), .Y({if_id_1_sequence_addr_2_2, if_id_1_sequence_addr_2}), .AluOP(4'b0101),
    .Result(mips_alu_2_result));  // open: Equal, Result_2, shamt
  Counter #(.width(16), .max('hffff), .ongoal("wrap"), .trigger("rising"), .behavior("new")) counter_7 (
    .count(Halt), .Q(\总周期数 ), .clk(CLK));  // open: load, D, carry, clr, preset, down
  or or_4 (or_4_out, bubble, GO, load_use);
  ID_EX id_ex_1 (
    .MemToReg(\单周期硬布线控制器_1_memtoreg ), .RegWrite(\单周期硬布线控制器_1_regwrite ), .RegDst(\单周期硬布线控制器_1_regdst ),
    .Syscall(ID_syscall), .JAL(\单周期硬布线控制器_1_jal ), .LH(\单周期硬布线控制器_1_lh ), .JR(\单周期硬布线控制器_1_jr ),
    .BEQ(\单周期硬布线控制器_1_beq ), .BNE(\单周期硬布线控制器_1_bne ), .BLEZ(\单周期硬布线控制器_1_blez ), .SRAV(\单周期硬布线控制器_1_srav ),
    .ALU_SRC(\单周期硬布线控制器_1_alu_src ), .rt_num(ID_IR[20:16]), .rd_num(ID_IR[15:11]),
    .ALU_OP(\单周期硬布线控制器_1_alu_op ), .Shamt(ID_IR[10:6]), .PC(ID_PC), .IR(ID_IR), .A(v0), .B(a0),
    .Imm(multiplexer_11_out), .JMP_addr({if_id_1_sequence_addr_2_2, ID_IR[25:0], 2'b00}), .CLK(CLK),
    .clr(or_4_out), .EN(or_5_out), .Syscall_2(EX_syscall), .MemToReg_2(EX_MemToReg),
    .RegWrite_2(EX_RegWrite), .RegDst_2(id_ex_1_regdst_2), .rt_num_2(id_ex_1_rt_num_2),
    .rd_num_2(id_ex_1_rd_num_2), .JAL_2(JAL), .JMP_Aaddr(JMP_addr), .Imm_2(id_ex_1_imm_2), .B_2(B),
    .PC_2(EX_PC), .IR_2(EX_IR), .A_2(A), .Shamt_2(id_ex_1_shamt_2), .ALU_OP_2(ALU_OP), .LH_2(id_ex_1_lh_2),
    .JR_2(JR), .BEQ_2(BEQ), .BNE_2(BNE), .BLEZ_2(BLEZ), .SRAV_2(SRAV), .ALU_SRC_2(ALU_SRC),
    .JMP(\单周期硬布线控制器_1_jmp ), .JMP_2(JMP), .MemWrite(\单周期硬布线控制器_1_memwrite ), .MemWrite_2(id_ex_1_memwrite_2),
    .Branch_addr(mips_alu_2_result), .JMP_Aaddr_2(Breanch_addr), .ForwarA(ForwardA), .ForwarA_2(EX_ForwardA),
    .ForwarB(ForwardB), .ForwarB_2(EX_ForwardB));
  and and_6 (and_6_out, equal, BEQ);
  and and_7 (and_7_out, BNE, ~equal);  // AND_Gate
  and and_8 (and_8_out, BLEZ, ~comparator_3_gt);  // AND_Gate
  Comparator #(.width(32), .mode("twosComplement")) comparator_3 (
    .a(v0_prime), .b({32{1'b0}}), .gt(comparator_3_gt));  // open: eq, lt
  nor nor_1 (Sequence, JMP, Branch);
  assign Branch_J_JAL_addr = J_JAL ? JMP_addr : 32'bz;  // Controlled_Buffer controlled_buffer_1
  assign Branch_J_JAL_addr = EX_Branch ? Breanch_addr : 32'bz;  // Controlled_Buffer controlled_buffer_2
  or or_5 (or_5_out, Halt, GO);
  or or_6 (Branch, and_6_out, and_8_out, and_7_out);
  and and_9 (J_JAL, ~JR, JMP);  // AND_Gate
  or or_7 (BHT_Branch, J_JAL, Branch);
  Multiplexer #(.select(1), .width(5), .disabled("Z"), .enable("false")) multiplexer_12 (
    .in0(id_ex_1_rt_num_2), .in1(id_ex_1_rd_num_2), .out(multiplexer_12_out), .sel(id_ex_1_regdst_2));
  Multiplexer #(.select(1), .width(5), .disabled("Z"), .enable("false")) multiplexer_13 (
    .in0(multiplexer_12_out), .in1({5{1'b1}}), .out(EX_W_num), .sel(JAL));
  \分支预测  \u_分支预测_1  (
    .IF_PC(IF_PC), .EX_PC(EX_PC), .EX_NewPC(Branch_J_JAL_addr), .Clk(CLK), .Branch(BHT_Branch),
    .EX_Branch(EX_Branch_J_JAL), .PredictSuccess(PredictSuccess), .PredictPC(PredictPC),
    .PredictFail(PredictFail));
  Multiplexer #(.select(2), .width(32), .disabled("Z"), .enable("false")) multiplexer_14 (
    .in0(A), .in1(MEM_ALU_Result), .in2(WB_ALU_Result), .in3(RDin), .out(v0_prime), .sel(EX_ForwardA));
  Multiplexer #(.select(2), .width(32), .disabled("Z"), .enable("false")) multiplexer_15 (
    .in0(B), .in1(MEM_ALU_Result), .in2(WB_ALU_Result), .in3(RDin), .out(a0_prime), .sel(EX_ForwardB));
  Multiplexer #(.select(1), .width(32), .disabled("Z"), .enable("false")) multiplexer_16 (
    .in0(a0_prime), .in1(id_ex_1_imm_2), .out(multiplexer_16_out), .sel(ALU_SRC));
  Multiplexer #(.select(1), .width(5), .disabled("Z"), .enable("false")) multiplexer_17 (
    .in0(id_ex_1_shamt_2), .in1(v0_prime[4:0]), .out(multiplexer_17_out), .sel(SRAV));
  or or_8 (EX_Branch, BEQ, BLEZ, BNE);
  MIPS_ALU mips_alu_3 (
    .X(v0_prime), .Y(multiplexer_16_out), .AluOP(ALU_OP), .Equal(equal), .Result(mips_alu_3_result),
    .shamt(multiplexer_17_out));  // open: Result_2
  or or_9 (EX_Branch_J_JAL, J_JAL, EX_Branch);
  and and_10 (and_10_out, EX_PredictSuccess, ~BHT_Branch);  // AND_Gate
  and and_11 (and_11_out, EX_PredictFail, BHT_Branch);
  or or_10 (bubble, and_10_out, and_11_out);
  EX_MEM ex_mem_1 (
    .Syscall(EX_syscall), .Syscall_2(ex_mem_1_syscall_2), .MemToReg(EX_MemToReg), .MemToReg_2(MEM_MemToReg),
    .RegWrite(EX_RegWrite), .RegWrite_2(MEM_RegWrite), .RegDst(id_ex_1_regdst_2),
    .RegDst_2(ex_mem_1_regdst_2), .rt_num(id_ex_1_rt_num_2), .rt_num_2(ex_mem_1_rt_num_2),
    .rd_num(id_ex_1_rd_num_2), .rd_num_2(ex_mem_1_rd_num_2), .MemWrite(id_ex_1_memwrite_2),
    .MemWrite_2(MemWrite), .LH(id_ex_1_lh_2), .LH_2(ex_mem_1_lh_2), .PC(EX_PC), .PC_2(M_PC), .IR(EX_IR),
    .IR_2(MEM_IR), .ALU(mips_alu_3_result), .ALU_2(MEM_ALU_Result), .B(a0_prime), .B_2(MDin), .CLK(CLK),
    .clr(GO), .JAL(JAL), .JAL_2(ex_mem_1_jal_2));  // open: EN
  Multiplexer #(.select(1), .width(5), .disabled("Z"), .enable("false")) multiplexer_18 (
    .in0(ex_mem_1_rt_num_2), .in1(ex_mem_1_rd_num_2), .out(multiplexer_18_out), .sel(ex_mem_1_regdst_2));
  Multiplexer #(.select(1), .width(5), .disabled("Z"), .enable("false")) multiplexer_19 (
    .in0(multiplexer_18_out), .in1({5{1'b1}}), .out(MEM_W_num), .sel(ex_mem_1_jal_2));
  RAM #(.addrWidth(10), .dataWidth(32), .bus("separate"), .Select("high")) ram_1 (
    .addr(MEM_ALU_Result[11:2]), .din(MDin), .data(ram_1_data), .str(MemWrite), .clk(CLK));  // open: sel, ld, clr
  Multiplexer #(.select(1), .width(16), .disabled("Z"), .enable("false")) multiplexer_20 (
    .in0(ram_1_data[15:0]), .in1(ram_1_data[31:16]), .out(multiplexer_20_out), .sel(MEM_ALU_Result[1]));
  assign bit_extender_3_out = {{16{multiplexer_20_out[15]}}, multiplexer_20_out};  // Bit_Extender bit_extender_3
  MEM_WB mem_wb_1 (
    .Syscall(ex_mem_1_syscall_2), .Syscall_2(Syscall), .MemToReg(MEM_MemToReg),
    .MemToReg_2(mem_wb_1_memtoreg_2), .RegWrite(MEM_RegWrite), .RegWrite_2(RegWrite),
    .RegDst(ex_mem_1_regdst_2), .RegDst_2(mem_wb_1_regdst_2), .rt_num(ex_mem_1_rt_num_2),
    .rt_num_2(mem_wb_1_rt_num_2), .rd_num(ex_mem_1_rd_num_2), .rd_num_2(mem_wb_1_rd_num_2),
    .JAL(ex_mem_1_jal_2), .JAL_2(mem_wb_1_jal_2), .LH(ex_mem_1_lh_2), .LH_2(mem_wb_1_lh_2), .PC(M_PC),
    .PC_2(WB_PC), .IR(MEM_IR), .IR_2(WB_IR), .ALU(MEM_ALU_Result), .ALU_2(WB_ALU_Result), .MD(ram_1_data),
    .MD_2(mem_wb_1_md_2), .CLK(CLK), .clr(GO), .HW(bit_extender_3_out), .HW_2(mem_wb_1_hw_2));  // open: EN
  Multiplexer #(.select(1), .width(32), .disabled("Z"), .enable("false")) multiplexer_21 (
    .in0(mem_wb_1_md_2), .in1(mem_wb_1_hw_2), .out(multiplexer_21_out), .sel(mem_wb_1_lh_2));
  Multiplexer #(.select(1), .width(32), .disabled("Z"), .enable("false")) multiplexer_22 (
    .in0(WB_ALU_Result), .in1(multiplexer_21_out), .out(multiplexer_22_out), .sel(mem_wb_1_memtoreg_2));
  Adder #(.width(32)) adder_2 (.a(WB_PC), .b(32'h4), .out(adder_2_out));  // open: cin, cout
  Multiplexer #(.select(1), .width(32), .disabled("Z"), .enable("false")) multiplexer_23 (
    .in0(multiplexer_22_out), .in1(adder_2_out), .out(RDin), .sel(mem_wb_1_jal_2));
  Multiplexer #(.select(1), .width(5), .disabled("Z"), .enable("false")) multiplexer_24 (
    .in0(mem_wb_1_rt_num_2), .in1(mem_wb_1_rd_num_2), .out(multiplexer_24_out), .sel(mem_wb_1_regdst_2));
  Multiplexer #(.select(1), .width(5), .disabled("Z"), .enable("false")) multiplexer_25 (
    .in0(multiplexer_24_out), .in1({5{1'b1}}), .out(WB_num), .sel(mem_wb_1_jal_2));

  // Other names for the same wires on the sheet: rd_num[4:0] = ID_IR[15:11]; rt_num[4:0] = ID_IR[20:16];
  //   MEM_PC[31:0] = M_PC; WB_WBData[31:0] = RDin

  // Notes on the sheet:
  //   中断源
  //   时空图监测，可删除
  //   中断等待指示
  //   数码管输出
  //   指令存储器
  //   指令字
  //   contents of rom_1 (hex, n*v repeats v):
  //   20110001 8000c05 20110001 20120002 20130003 8000c09 20110001 20120002 20130003 8000c0d 20110001
  //   20120002 20130003 8000c11 20110001 20120002 20130003 c000cf9 20100001 20110001 118fc0 112020
  //   20020022 c 118882 12200001 8000c15 112020 20020022 c 20110001 118880 112020 20020022 c 12200001
  //   8000c1f 20110001 118fc0 112020 20020022 c 1188c3 112020 20020022 c 118903 112020 20020022 c 118903
  //   112020 20020022 c 118903 112020 20020022 c 118903 112020 20020022 c 118903 112020 20020022 c 118903
  //   112020 20020022 c 118903 112020 20020022 c 20100001 109fc0 139fc3 8021 2012000c 24160003 26100001
  //   3210000f 20080008 20090001 139900 2709825 132020 20020022 c 1094022 1500fff9 22100001 2018000f
  //   2188024 108700 20080008 20090001 139902 2709825 132021 20020022 c 1094022 1500fff9 108702 2c9b022
  //   12c00001 8000c50 4020 1084027 84400 3508ffff 82021 20020022 c 2010ffff 20110000 ae300000 22100001
  //   22310004 ae300000 22100001 22310004 ae300000 22100001 22310004 ae300000 22100001 22310004 ae300000
  //   22100001 22310004 ae300000 22100001 22310004 ae300000 22100001 22310004 ae300000 22100001 22310004
  //   ae300000 22100001 22310004 ae300000 22100001 22310004 ae300000 22100001 22310004 ae300000 22100001
  //   22310004 ae300000 22100001 22310004 ae300000 22100001 22310004 ae300000 22100001 22310004 ae300000
  //   22100001 22310004 22100001 8020 2011003c 8e130000 8e340000 274402a 11000002 ae330000 ae140000
  //   2231fffc 1611fff8 102020 20020022 c 22100004 2011003c 1611fff2 20020032 c 20080001 20090003 20110876
  //   118d00 112020 20020022 c 200b0008 1118807 1318807 112020 20020022 c 216bffff 1560fff9 2002000a c
  //   2008ffff 20117777 112020 20020022 c 200b0010 2288826 112020 20020022 c 216bffff 1560fffa 2002000a c
  //   20090000 200b0010 34118483 20120404 118c00 129400 36318281 22520404 ad310000 2328820 21290004
  //   216bffff 1560fffb 200b0020 20090000 85310000 112020 20020022 c 21290002 216bffff 1560fff9 2002000a c
  //   2011fff1 112020 20020022 c 22310001 1a20fffb 2002000a c 2002000a c 20100000 22100001 102020 20020022
  //   c 22100002 102020 20020022 c 22100003 102020 20020022 c 22100004 102020 20020022 c 22100005 102020
  //   20020022 c 22100006 102020 20020022 c 22100007 102020 20020022 c 22100008 102020 20020022 20020022 c
  //   3e00008
  //   Imm16
  //   OP
  //   Func
  //   rs
  //   rt
  //   rd
  //   shamt
  //   流水调试日志用
  //   LED显示及停机逻辑
  //   PC总线输入使能信号产生逻辑
  //   为方便自动评测，需要输出流水线各段保存的PC值，注意是PC不是PC+4，另外ID段寄存器写入信息，Mem段内存写入信息也要输出
endmodule

module \分支预测  (
  input  Clk,
  input  [31:0] IF_PC,
  input  [31:0] EX_PC,
  input  [31:0] EX_NewPC,
  input  Branch,
  input  EX_Branch,
  output PredictSuccess,
  output [31:0] PredictPC,
  output PredictFail
);

  wire BHT_Hit;
  wire [0:0] CurrentStage;
  wire [31:0] adder_1_out, BHT_NextPC, multiplexer_1_out;

  not not_1 (PredictFail, PredictSuccess);
  Pull_Resistor #(.pull(0)) pull_resistor_1 (.node({PredictSuccess, CurrentStage[0]}));
  BHT bht_1 (
    .EX_PC(EX_PC), .BlkDataReady(EX_Branch), .CLK(Clk), .BHT_Hit(BHT_Hit), .DataOut(BHT_NextPC),
    .Branch(Branch), .IF_PC(IF_PC), .BlockDataIn(EX_NewPC), .CurrentStage({PredictSuccess, CurrentStage[0]}));
  Adder #(.width(32)) adder_1 (.a(IF_PC), .b(32'h4), .out(adder_1_out));  // open: cin, cout
  Multiplexer #(.select(2), .width(32), .disabled("Z"), .enable("false")) multiplexer_1 (
    .in0(adder_1_out), .in1(adder_1_out), .in2(BHT_NextPC), .in3(BHT_NextPC), .out(multiplexer_1_out),
    .sel({PredictSuccess, CurrentStage[0]}));
  Multiplexer #(.select(1), .width(32), .disabled("Z"), .enable("false")) multiplexer_2 (
    .in0(adder_1_out), .in1(multiplexer_1_out), .out(PredictPC), .sel(BHT_Hit));

  // Other names for the same wires on the sheet: CurrentStage[1] = PredictSuccess; Predict_PC[31:0] = PredictPC
endmodule

module \源寄存器使用情况  (
  input  OP0,
  input  OP1,
  input  OP2,
  input  OP3,
  input  OP4,
  input  OP5,
  input  F0,
  input  F1,
  input  F2,
  input  F3,
  input  F4,
  input  F5,
  output R1_Used,
  output R2_Used
);

  wire and_1_out, and_2_out, and_3_out, and_4_out, and_5_out, and_6_out, and_7_out, and_8_out, and_9_out,
       and_10_out, and_11_out, and_12_out, and_13_out, and_14_out, and_15_out, and_16_out, and_17_out,
       and_18_out, and_19_out, and_20_out, and_21_out, and_22_out, and_23_out, and_24_out, and_25_out,
       and_26_out, and_27_out, and_28_out, and_29_out, and_30_out, and_31_out, and_32_out, and_33_out,
       and_34_out, and_35_out, and_36_out, and_37_out, and_38_out, and_39_out, and_40_out, not_1_out,
       not_2_out, not_3_out, not_4_out, not_5_out, not_6_out, not_7_out, not_8_out, not_9_out, not_10_out,
       not_11_out, not_12_out, not_13_out, not_14_out, not_15_out, not_16_out, not_17_out, not_18_out,
       not_19_out, not_20_out, not_21_out, not_22_out, not_23_out, not_24_out, not_25_out, not_26_out,
       not_27_out, not_28_out, not_29_out, not_30_out, not_31_out, not_32_out, not_33_out, not_34_out,
       not_35_out, not_36_out, not_37_out, not_38_out, not_39_out, not_40_out, not_41_out, not_42_out,
       not_43_out, not_44_out, not_45_out, not_46_out, not_47_out, not_48_out, not_49_out, not_50_out,
       not_51_out, not_52_out, not_53_out, not_54_out, not_55_out, not_56_out, not_57_out, not_58_out,
       not_59_out, not_60_out, not_61_out, not_62_out, not_63_out, not_64_out, not_65_out, not_66_out,
       not_67_out, not_68_out, not_69_out, not_70_out, not_71_out, not_72_out, not_73_out, not_74_out,
       not_75_out, not_76_out, not_77_out, not_78_out, not_79_out, not_80_out, not_81_out, not_82_out,
       not_83_out, not_84_out, not_85_out, not_86_out, not_87_out, not_88_out, not_89_out, not_90_out,
       not_91_out, not_92_out, not_93_out, not_94_out, not_95_out, not_96_out, not_97_out, not_98_out,
       not_99_out, not_100_out, not_101_out, not_102_out, not_103_out, not_104_out, not_105_out, not_106_out,
       not_107_out, not_108_out, not_109_out, not_110_out, not_111_out, not_112_out, not_113_out,
       not_114_out, not_115_out, not_116_out, not_117_out, not_118_out, not_119_out, not_120_out,
       not_121_out, not_122_out, not_123_out, not_124_out, not_125_out, not_126_out, not_127_out,
       not_128_out, not_129_out, not_130_out, not_131_out, not_132_out, not_133_out, not_134_out,
       not_135_out, not_136_out, not_137_out, not_138_out, not_139_out, not_140_out, not_141_out,
       not_142_out, not_143_out, not_144_out, not_145_out, not_146_out, not_147_out, not_148_out,
       not_149_out, not_150_out, not_151_out, not_152_out, not_153_out, not_154_out, not_155_out,
       not_156_out, not_157_out, not_158_out, not_159_out, not_160_out, not_161_out, not_162_out,
       not_163_out, not_164_out, not_165_out, not_166_out, not_167_out, not_168_out, not_169_out,
       not_170_out, not_171_out, not_172_out, not_173_out, not_174_out, not_175_out, not_176_out,
       not_177_out, not_178_out, not_179_out, not_180_out, not_181_out, not_182_out, not_183_out,
       not_184_out, not_185_out, not_186_out, not_187_out, not_188_out, not_189_out, not_190_out,
       not_191_out, not_192_out, not_193_out, not_194_out, not_195_out, not_196_out, not_197_out,
       not_198_out, not_199_out, not_200_out, not_201_out, not_202_out, not_203_out, not_204_out,
       not_205_out, not_206_out, not_207_out, not_208_out, not_209_out, not_210_out, not_211_out,
       not_212_out, not_213_out, not_214_out, not_215_out, not_216_out, not_217_out, not_218_out,
       not_219_out, not_220_out, not_221_out, not_222_out, not_223_out, not_224_out, not_225_out,
       not_226_out, not_227_out, not_228_out, not_229_out, not_230_out, not_231_out, not_232_out,
       not_233_out, not_234_out, not_235_out, not_236_out, not_237_out, not_238_out, not_239_out,
       not_240_out, not_241_out, not_242_out, not_243_out, not_244_out, not_245_out, not_246_out,
       not_247_out, not_248_out, not_249_out, not_250_out, not_251_out, not_252_out, not_253_out,
       not_254_out, not_255_out, not_256_out, not_257_out, not_258_out, not_259_out, not_260_out,
       not_261_out, not_262_out, not_263_out, not_264_out, not_265_out, not_266_out, not_267_out,
       not_268_out, not_269_out, not_270_out, not_271_out, not_272_out, not_273_out, not_274_out,
       not_275_out, not_276_out, not_277_out, not_278_out, not_279_out, not_280_out, not_281_out,
       not_282_out, not_283_out, not_284_out, not_285_out, not_286_out, not_287_out, not_288_out,
       not_289_out, not_290_out, not_291_out, not_292_out, not_293_out, not_294_out, not_295_out,
       not_296_out, not_297_out, not_298_out, not_299_out, not_300_out, not_301_out, not_302_out, not_303_out;

  not not_1 (not_1_out, OP5);
  not not_2 (not_2_out, OP4);
  not not_3 (not_3_out, OP3);
  not not_4 (not_4_out, OP2);
  not not_5 (not_5_out, OP1);
  not not_6 (not_6_out, OP0);
  not not_7 (not_7_out, F4);
  not not_8 (not_8_out, F3);
  not not_9 (not_9_out, F2);
  not not_10 (not_10_out, F1);
  not not_11 (not_11_out, F0);
  not not_12 (not_12_out, OP5);
  not not_13 (not_13_out, OP4);
  not not_14 (not_14_out, OP3);
  not not_15 (not_15_out, OP2);
  not not_16 (not_16_out, OP1);
  not not_17 (not_17_out, OP0);
  not not_18 (not_18_out, F4);
  not not_19 (not_19_out, F3);
  not not_20 (not_20_out, F2);
  not not_21 (not_21_out, F1);
  not not_22 (not_22_out, OP5);
  not not_23 (not_23_out, OP4);
  not not_24 (not_24_out, OP3);
  not not_25 (not_25_out, OP2);
  not not_26 (not_26_out, OP1);
  not not_27 (not_27_out, OP0);
  not not_28 (not_28_out, F4);
  not not_29 (not_29_out, F3);
  not not_30 (not_30_out, F2);
  not not_31 (not_31_out, F0);
  not not_32 (not_32_out, OP5);
  not not_33 (not_33_out, OP4);
  not not_34 (not_34_out, OP3);
  not not_35 (not_35_out, OP2);
  not not_36 (not_36_out, OP1);
  not not_37 (not_37_out, OP0);
  not not_38 (not_38_out, F4);
  not not_39 (not_39_out, F3);
  not not_40 (not_40_out, F1);
  not not_41 (not_41_out, F0);
  not not_42 (not_42_out, OP5);
  not not_43 (not_43_out, OP4);
  not not_44 (not_44_out, OP3);
  not not_45 (not_45_out, OP2);
  not not_46 (not_46_out, OP1);
  not not_47 (not_47_out, OP0);
  not not_48 (not_48_out, F4);
  not not_49 (not_49_out, F3);
  not not_50 (not_50_out, F1);
  not not_51 (not_51_out, OP5);
  not not_52 (not_52_out, OP4);
  not not_53 (not_53_out, OP3);
  not not_54 (not_54_out, OP2);
  not not_55 (not_55_out, OP1);
  not not_56 (not_56_out, OP0);
  not not_57 (not_57_out, F4);
  not not_58 (not_58_out, F3);
  not not_59 (not_59_out, OP5);
  not not_60 (not_60_out, OP4);
  not not_61 (not_61_out, OP3);
  not not_62 (not_62_out, OP2);
  not not_63 (not_63_out, OP1);
  not not_64 (not_64_out, OP0);
  not not_65 (not_65_out, F4);
  not not_66 (not_66_out, F2);
  not not_67 (not_67_out, F0);
  not not_68 (not_68_out, OP5);
  not not_69 (not_69_out, OP4);
  not not_70 (not_70_out, OP3);
  not not_71 (not_71_out, OP2);
  not not_72 (not_72_out, OP1);
  not not_73 (not_73_out, OP0);
  not not_74 (not_74_out, F4);
  not not_75 (not_75_out, F2);
  not not_76 (not_76_out, OP5);
  not not_77 (not_77_out, OP4);
  not not_78 (not_78_out, OP3);
  not not_79 (not_79_out, OP2);
  not not_80 (not_80_out, OP1);
  not not_81 (not_81_out, OP0);
  not not_82 (not_82_out, F5);
  not not_83 (not_83_out, F4);
  not not_84 (not_84_out, F2);
  not not_85 (not_85_out, F1);
  not not_86 (not_86_out, F0);
  not not_87 (not_87_out, OP5);
  not not_88 (not_88_out, OP4);
  not not_89 (not_89_out, OP3);
  not not_90 (not_90_out, OP2);
  not not_91 (not_91_out, OP1);
  not not_92 (not_92_out, OP0);
  not not_93 (not_93_out, F5);
  not not_94 (not_94_out, F4);
  not not_95 (not_95_out, F1);
  not not_96 (not_96_out, F0);
  not not_97 (not_97_out, OP5);
  not not_98 (not_98_out, OP4);
  not not_99 (not_99_out, OP3);
  not not_100 (not_100_out, OP1);
  not not_101 (not_101_out, OP0);
  not not_102 (not_102_out, OP5);
  not not_103 (not_103_out, OP4);
  not not_104 (not_104_out, OP3);
  not not_105 (not_105_out, OP1);
  not not_106 (not_106_out, OP5);
  not not_107 (not_107_out, OP4);
  not not_108 (not_108_out, OP2);
  not not_109 (not_109_out, OP1);
  not not_110 (not_110_out, OP0);
  not not_111 (not_111_out, OP5);
  not not_112 (not_112_out, OP4);
  not not_113 (not_113_out, OP1);
  not not_114 (not_114_out, OP0);
  not not_115 (not_115_out, OP5);
  not not_116 (not_116_out, OP4);
  not not_117 (not_117_out, OP2);
  not not_118 (not_118_out, OP1);
  not not_119 (not_119_out, OP5);
  not not_120 (not_120_out, OP4);
  not not_121 (not_121_out, OP2);
  not not_122 (not_122_out, OP0);
  not not_123 (not_123_out, OP5);
  not not_124 (not_124_out, OP4);
  not not_125 (not_125_out, OP1);
  not not_126 (not_126_out, OP4);
  not not_127 (not_127_out, OP3);
  not not_128 (not_128_out, OP2);
  not not_129 (not_129_out, OP4);
  not not_130 (not_130_out, OP2);
  not not_131 (not_131_out, OP5);
  not not_132 (not_132_out, OP4);
  not not_133 (not_133_out, OP3);
  not not_134 (not_134_out, OP2);
  not not_135 (not_135_out, OP1);
  not not_136 (not_136_out, OP0);
  not not_137 (not_137_out, F5);
  not not_138 (not_138_out, F4);
  not not_139 (not_139_out, F3);
  not not_140 (not_140_out, OP5);
  not not_141 (not_141_out, OP4);
  not not_142 (not_142_out, OP3);
  not not_143 (not_143_out, OP2);
  not not_144 (not_144_out, OP1);
  not not_145 (not_145_out, OP0);
  not not_146 (not_146_out, F4);
  not not_147 (not_147_out, F3);
  not not_148 (not_148_out, F0);
  not not_149 (not_149_out, OP4);
  not not_150 (not_150_out, OP3);
  not not_151 (not_151_out, OP2);
  not not_152 (not_152_out, OP1);
  not not_153 (not_153_out, OP5);
  not not_154 (not_154_out, OP4);
  not not_155 (not_155_out, OP3);
  not not_156 (not_156_out, OP0);
  not not_157 (not_157_out, OP5);
  not not_158 (not_158_out, OP4);
  not not_159 (not_159_out, OP3);
  not not_160 (not_160_out, OP2);
  not not_161 (not_161_out, OP1);
  not not_162 (not_162_out, OP0);
  not not_163 (not_163_out, F5);
  not not_164 (not_164_out, F4);
  not not_165 (not_165_out, F3);
  not not_166 (not_166_out, F2);
  not not_167 (not_167_out, F1);
  not not_168 (not_168_out, F0);
  not not_169 (not_169_out, OP5);
  not not_170 (not_170_out, OP4);
  not not_171 (not_171_out, OP3);
  not not_172 (not_172_out, OP2);
  not not_173 (not_173_out, OP1);
  not not_174 (not_174_out, OP0);
  not not_175 (not_175_out, F5);
  not not_176 (not_176_out, F4);
  not not_177 (not_177_out, F3);
  not not_178 (not_178_out, F2);
  not not_179 (not_179_out, OP5);
  not not_180 (not_180_out, OP4);
  not not_181 (not_181_out, OP3);
  not not_182 (not_182_out, OP2);
  not not_183 (not_183_out, OP1);
  not not_184 (not_184_out, OP0);
  not not_185 (not_185_out, F5);
  not not_186 (not_186_out, F4);
  not not_187 (not_187_out, F3);
  not not_188 (not_188_out, F2);
  not not_189 (not_189_out, F0);
  not not_190 (not_190_out, OP5);
  not not_191 (not_191_out, OP4);
  not not_192 (not_192_out, OP3);
  not not_193 (not_193_out, OP2);
  not not_194 (not_194_out, OP1);
  not not_195 (not_195_out, OP0);
  not not_196 (not_196_out, F4);
  not not_197 (not_197_out, F3);
  not not_198 (not_198_out, F2);
  not not_199 (not_199_out, F1);
  not not_200 (not_200_out, F0);
  not not_201 (not_201_out, OP5);
  not not_202 (not_202_out, OP4);
  not not_203 (not_203_out, OP3);
  not not_204 (not_204_out, OP2);
  not not_205 (not_205_out, OP1);
  not not_206 (not_206_out, OP0);
  not not_207 (not_207_out, F4);
  not not_208 (not_208_out, F3);
  not not_209 (not_209_out, F2);
  not not_210 (not_210_out, F1);
  not not_211 (not_211_out, OP5);
  not not_212 (not_212_out, OP4);
  not not_213 (not_213_out, OP3);
  not not_214 (not_214_out, OP2);
  not not_215 (not_215_out, OP1);
  not not_216 (not_216_out, OP0);
  not not_217 (not_217_out, F4);
  not not_218 (not_218_out, F3);
  not not_219 (not_219_out, F2);
  not not_220 (not_220_out, F0);
  not not_221 (not_221_out, OP5);
  not not_222 (not_222_out, OP4);
  not not_223 (not_223_out, OP3);
  not not_224 (not_224_out, OP2);
  not not_225 (not_225_out, OP1);
  not not_226 (not_226_out, OP0);
  not not_227 (not_227_out, F4);
  not not_228 (not_228_out, F3);
  not not_229 (not_229_out, F1);
  not not_230 (not_230_out, F0);
  not not_231 (not_231_out, OP5);
  not not_232 (not_232_out, OP4);
  not not_233 (not_233_out, OP3);
  not not_234 (not_234_out, OP2);
  not not_235 (not_235_out, OP1);
  not not_236 (not_236_out, OP0);
  not not_237 (not_237_out, F4);
  not not_238 (not_238_out, F3);
  not not_239 (not_239_out, F1);
  not not_240 (not_240_out, OP5);
  not not_241 (not_241_out, OP4);
  not not_242 (not_242_out, OP3);
  not not_243 (not_243_out, OP2);
  not not_244 (not_244_out, OP1);
  not not_245 (not_245_out, OP0);
  not not_246 (not_246_out, F4);
  not not_247 (not_247_out, F3);
  not not_248 (not_248_out, OP5);
  not not_249 (not_249_out, OP4);
  not not_250 (not_250_out, OP3);
  not not_251 (not_251_out, OP2);
  not not_252 (not_252_out, OP1);
  not not_253 (not_253_out, OP0);
  not not_254 (not_254_out, F4);
  not not_255 (not_255_out, F2);
  not not_256 (not_256_out, F0);
  not not_257 (not_257_out, OP5);
  not not_258 (not_258_out, OP4);
  not not_259 (not_259_out, OP3);
  not not_260 (not_260_out, OP2);
  not not_261 (not_261_out, OP1);
  not not_262 (not_262_out, OP0);
  not not_263 (not_263_out, F4);
  not not_264 (not_264_out, F2);
  not not_265 (not_265_out, OP5);
  not not_266 (not_266_out, OP4);
  not not_267 (not_267_out, OP3);
  not not_268 (not_268_out, OP2);
  not not_269 (not_269_out, OP1);
  not not_270 (not_270_out, OP0);
  not not_271 (not_271_out, F5);
  not not_272 (not_272_out, F4);
  not not_273 (not_273_out, F1);
  not not_274 (not_274_out, F0);
  not not_275 (not_275_out, OP5);
  not not_276 (not_276_out, OP4);
  not not_277 (not_277_out, OP3);
  not not_278 (not_278_out, OP1);
  not not_279 (not_279_out, OP0);
  not not_280 (not_280_out, OP5);
  not not_281 (not_281_out, OP4);
  not not_282 (not_282_out, OP3);
  not not_283 (not_283_out, OP1);
  not not_284 (not_284_out, OP4);
  not not_285 (not_285_out, OP2);
  not not_286 (not_286_out, OP5);
  not not_287 (not_287_out, OP4);
  not not_288 (not_288_out, OP3);
  not not_289 (not_289_out, OP2);
  not not_290 (not_290_out, OP1);
  not not_291 (not_291_out, OP0);
  not not_292 (not_292_out, F5);
  not not_293 (not_293_out, F4);
  not not_294 (not_294_out, F3);
  not not_295 (not_295_out, OP5);
  not not_296 (not_296_out, OP4);
  not not_297 (not_297_out, OP3);
  not not_298 (not_298_out, OP2);
  not not_299 (not_299_out, OP1);
  not not_300 (not_300_out, OP0);
  not not_301 (not_301_out, F4);
  not not_302 (not_302_out, F3);
  not not_303 (not_303_out, F0);
  and and_1 (and_1_out, not_1_out, not_2_out, not_3_out, not_4_out, not_5_out, not_6_out, F5, not_7_out, not_8_out, not_9_out, not_10_out, not_11_out);
  and and_2 (and_2_out, not_12_out, not_13_out, not_14_out, not_15_out, not_16_out, not_17_out, F5, not_18_out, not_19_out, not_20_out, not_21_out, F0);
  and and_3 (and_3_out, not_22_out, not_23_out, not_24_out, not_25_out, not_26_out, not_27_out, F5, not_28_out, not_29_out, not_30_out, F1, not_31_out);
  and and_4 (and_4_out, not_32_out, not_33_out, not_34_out, not_35_out, not_36_out, not_37_out, F5, not_38_out, not_39_out, F2, not_40_out, not_41_out);
  and and_5 (and_5_out, not_42_out, not_43_out, not_44_out, not_45_out, not_46_out, not_47_out, F5, not_48_out, not_49_out, F2, not_50_out, F0);
  and and_6 (and_6_out, not_51_out, not_52_out, not_53_out, not_54_out, not_55_out, not_56_out, F5, not_57_out, not_58_out, F2, F1, F0);
  and and_7 (and_7_out, not_59_out, not_60_out, not_61_out, not_62_out, not_63_out, not_64_out, F5, not_65_out, F3, not_66_out, F1, not_67_out);
  and and_8 (and_8_out, not_68_out, not_69_out, not_70_out, not_71_out, not_72_out, not_73_out, F5, not_74_out, F3, not_75_out, F1, F0);
  and and_9 (and_9_out, not_76_out, not_77_out, not_78_out, not_79_out, not_80_out, not_81_out, not_82_out, not_83_out, F3, not_84_out, not_85_out, not_86_out);
  and and_10 (and_10_out, not_87_out, not_88_out, not_89_out, not_90_out, not_91_out, not_92_out, not_93_out, not_94_out, F3, F2, not_95_out, not_96_out);
  and and_11 (and_11_out, not_97_out, not_98_out, not_99_out, OP2, not_100_out, not_101_out);
  and and_12 (and_12_out, not_102_out, not_103_out, not_104_out, OP2, not_105_out, OP0);
  and and_13 (and_13_out, not_106_out, not_107_out, OP3, not_108_out, not_109_out, not_110_out);
  and and_14 (and_14_out, not_111_out, not_112_out, OP3, OP2, not_113_out, not_114_out);
  and and_15 (and_15_out, not_115_out, not_116_out, OP3, not_117_out, not_118_out, OP0);
  and and_16 (and_16_out, not_119_out, not_120_out, OP3, not_121_out, OP1, not_122_out);
  and and_17 (and_17_out, not_123_out, not_124_out, OP3, OP2, not_125_out, OP0);
  and and_18 (and_18_out, OP5, not_126_out, not_127_out, not_128_out, OP1, OP0);
  and and_19 (and_19_out, OP5, not_129_out, OP3, not_130_out, OP1, OP0);
  and and_20 (and_20_out, not_131_out, not_132_out, not_133_out, not_134_out, not_135_out, not_136_out, not_137_out, not_138_out, not_139_out, F2, F1, F0);
  and and_21 (and_21_out, not_140_out, not_141_out, not_142_out, not_143_out, not_144_out, not_145_out, F5, not_146_out, not_147_out, F2, F1, not_148_out);
  and and_22 (and_22_out, OP5, not_149_out, not_150_out, not_151_out, not_152_out, OP0);
  and and_23 (and_23_out, not_153_out, not_154_out, not_155_out, OP2, OP1, not_156_out);
  and and_24 (and_24_out, not_157_out, not_158_out, not_159_out, not_160_out, not_161_out, not_162_out, not_163_out, not_164_out, not_165_out, not_166_out, not_167_out, not_168_out);
  and and_25 (and_25_out, not_169_out, not_170_out, not_171_out, not_172_out, not_173_out, not_174_out, not_175_out, not_176_out, not_177_out, not_178_out, F1, F0);
  and and_26 (and_26_out, not_179_out, not_180_out, not_181_out, not_182_out, not_183_out, not_184_out, not_185_out, not_186_out, not_187_out, not_188_out, F1, not_189_out);
  and and_27 (and_27_out, not_190_out, not_191_out, not_192_out, not_193_out, not_194_out, not_195_out, F5, not_196_out, not_197_out, not_198_out, not_199_out, not_200_out);
  and and_28 (and_28_out, not_201_out, not_202_out, not_203_out, not_204_out, not_205_out, not_206_out, F5, not_207_out, not_208_out, not_209_out, not_210_out, F0);
  and and_29 (and_29_out, not_211_out, not_212_out, not_213_out, not_214_out, not_215_out, not_216_out, F5, not_217_out, not_218_out, not_219_out, F1, not_220_out);
  and and_30 (and_30_out, not_221_out, not_222_out, not_223_out, not_224_out, not_225_out, not_226_out, F5, not_227_out, not_228_out, F2, not_229_out, not_230_out);
  and and_31 (and_31_out, not_231_out, not_232_out, not_233_out, not_234_out, not_235_out, not_236_out, F5, not_237_out, not_238_out, F2, not_239_out, F0);
  and and_32 (and_32_out, not_240_out, not_241_out, not_242_out, not_243_out, not_244_out, not_245_out, F5, not_246_out, not_247_out, F2, F1, F0);
  and and_33 (and_33_out, not_248_out, not_249_out, not_250_out, not_251_out, not_252_out, not_253_out, F5, not_254_out, F3, not_255_out, F1, not_256_out);
  and and_34 (and_34_out, not_257_out, not_258_out, not_259_out, not_260_out, not_261_out, not_262_out, F5, not_263_out, F3, not_264_out, F1, F0);
  and and_35 (and_35_out, not_265_out, not_266_out, not_267_out, not_268_out, not_269_out, not_270_out, not_271_out, not_272_out, F3, F2, not_273_out, not_274_out);
  and and_36 (and_36_out, not_275_out, not_276_out, not_277_out, OP2, not_278_out, not_279_out);
  and and_37 (and_37_out, not_280_out, not_281_out, not_282_out, OP2, not_283_out, OP0);
  and and_38 (and_38_out, OP5, not_284_out, OP3, not_285_out, OP1, OP0);
  and and_39 (and_39_out, not_286_out, not_287_out, not_288_out, not_289_out, not_290_out, not_291_out, not_292_out, not_293_out, not_294_out, F2, F1, F0);
  and and_40 (and_40_out, not_295_out, not_296_out, not_297_out, not_298_out, not_299_out, not_300_out, F5, not_301_out, not_302_out, F2, F1, not_303_out);
  or or_1 (R1_Used, and_1_out, and_2_out, and_3_out, and_4_out, and_5_out, and_6_out, and_7_out, and_8_out, and_9_out, and_10_out, and_11_out, and_12_out, and_13_out, and_14_out, and_15_out, and_16_out, and_17_out, and_18_out, and_19_out, and_20_out, and_21_out, and_22_out, and_23_out);
  or or_2 (R2_Used, and_24_out, and_25_out, and_26_out, and_27_out, and_28_out, and_29_out, and_30_out, and_31_out, and_32_out, and_33_out, and_34_out, and_35_out, and_36_out, and_37_out, and_38_out, and_39_out, and_40_out);
endmodule

module \重定向数据选择信号产生  (
  input  R1_Used,
  input  [4:0] R1_num,
  input  EX_RegWrite,
  input  [4:0] EX_W_num,
  input  MEM_RegWrite,
  input  [4:0] MEM_W_num,
  input  EX_MemToReg,
  input  MEM_MemToReg,
  input  R2_Used,
  input  [4:0] R2_num,
  output load_use,
  output [1:0] ForwardA,
  output [1:0] ForwardB
);

  wire comparator_1_eq, comparator_2_eq, comparator_3_eq, comparator_4_eq, comparator_5_eq, comparator_6_eq,
       EX_R1_Used, EX_R2_Used, MEM_R1_Used, MEM_R2_Used, not_1_out, not_2_out, R1_loaduse, R2_loaduse,
       WB_R1_lUsed, WB_R2_lUsed;
  wire [1:0] multiplexer_1_out, multiplexer_2_out, multiplexer_3_out, multiplexer_4_out;

  Comparator #(.width(5), .mode("twosComplement")) comparator_1 (
    .a(R1_num), .b({5{1'b0}}), .eq(comparator_1_eq));  // open: gt, lt
  not not_1 (not_1_out, comparator_1_eq);
  Comparator #(.width(5), .mode("twosComplement")) comparator_2 (
    .a(R1_num), .b(EX_W_num), .eq(comparator_2_eq));  // open: gt, lt
  Comparator #(.width(5), .mode("twosComplement")) comparator_3 (
    .a(R1_num), .b(MEM_W_num), .eq(comparator_3_eq));  // open: gt, lt
  Comparator #(.width(5), .mode("twosComplement")) comparator_4 (
    .a(R2_num), .b({5{1'b0}}), .eq(comparator_4_eq));  // open: gt, lt
  not not_2 (not_2_out, comparator_4_eq);
  Comparator #(.width(5), .mode("twosComplement")) comparator_5 (
    .a(R2_num), .b(EX_W_num), .eq(comparator_5_eq));  // open: gt, lt
  Comparator #(.width(5), .mode("twosComplement")) comparator_6 (
    .a(R2_num), .b(MEM_W_num), .eq(comparator_6_eq));  // open: gt, lt
  and and_1 (EX_R1_Used, R1_Used, not_1_out, EX_RegWrite, comparator_2_eq);
  and and_2 (MEM_R1_Used, R1_Used, not_1_out, MEM_RegWrite, comparator_3_eq);
  and and_3 (EX_R2_Used, R2_Used, not_2_out, comparator_5_eq, EX_RegWrite);
  and and_4 (MEM_R2_Used, R2_Used, not_2_out, MEM_RegWrite, comparator_6_eq);
  and and_5 (R1_loaduse, EX_R1_Used, EX_MemToReg);
  and and_6 (WB_R1_lUsed, MEM_R1_Used, MEM_MemToReg);
  and and_7 (R2_loaduse, EX_R2_Used, EX_MemToReg);
  and and_8 (WB_R2_lUsed, MEM_R2_Used, MEM_MemToReg);
  Multiplexer #(.select(1), .width(2), .disabled("Z"), .enable("false")) multiplexer_1 (
    .in0(2'b00), .in1(2'b10), .out(multiplexer_1_out), .sel(WB_R1_lUsed));
  Multiplexer #(.select(1), .width(2), .disabled("Z"), .enable("false")) multiplexer_2 (
    .in0(2'b00), .in1(2'b10), .out(multiplexer_2_out), .sel(WB_R2_lUsed));
  Multiplexer #(.select(1), .width(2), .disabled("Z"), .enable("false")) multiplexer_3 (
    .in0(multiplexer_1_out), .in1(2'b11), .out(multiplexer_3_out), .sel(MEM_R1_Used));
  Multiplexer #(.select(1), .width(2), .disabled("Z"), .enable("false")) multiplexer_4 (
    .in0(multiplexer_2_out), .in1(2'b11), .out(multiplexer_4_out), .sel(MEM_R2_Used));
  or or_1 (load_use, R1_loaduse, R2_loaduse);
  Multiplexer #(.select(1), .width(2), .disabled("Z"), .enable("false")) multiplexer_5 (
    .in0(multiplexer_3_out), .in1(2'b01), .out(ForwardA), .sel(EX_R1_Used));
  Multiplexer #(.select(1), .width(2), .disabled("Z"), .enable("false")) multiplexer_6 (
    .in0(multiplexer_4_out), .in1(2'b01), .out(ForwardB), .sel(EX_R2_Used));
endmodule

// 单周期硬布线控制器
module \单周期硬布线控制器  (
  input  [5:0] OP,
  input  [5:0] Func,
  output [3:0] ALU_OP,
  output MemToReg,
  output MemWrite,
  output ALU_SRC,
  output RegWrite,
  output SysCALL,
  output SignedExt,
  output RegDst,
  output Beq,
  output Bne,
  output JR,
  output JMP,
  output JAL,
  output LH,
  output BLEZ,
  output SRAV
);

  \运算控制器自动生成  \u_运算控制器自动生成_1  (
    .OP0(OP[0]), .OP1(OP[1]), .OP2(OP[2]), .OP3(OP[3]), .OP4(OP[4]), .OP5(OP[5]), .F0(Func[0]), .F1(Func[1]),
    .F2(Func[2]), .F3(Func[3]), .F4(Func[4]), .F5(Func[5]), .S0(ALU_OP[0]), .S1(ALU_OP[1]), .S2(ALU_OP[2]),
    .S3(ALU_OP[3]));
  \控制信号自动生成  \u_控制信号自动生成_1  (
    .OP0(OP[0]), .OP1(OP[1]), .OP2(OP[2]), .OP3(OP[3]), .OP4(OP[4]), .OP5(OP[5]), .F0(Func[0]), .F1(Func[1]),
    .F2(Func[2]), .F3(Func[3]), .F4(Func[4]), .F5(Func[5]), .MemToReg(MemToReg), .MemWrite(MemWrite),
    .ALU_SRC(ALU_SRC), .RegWrite(RegWrite), .SysCALL(SysCALL), .SignedExt(SignedExt), .RegDst(RegDst),
    .BEQ(Beq), .BNE(Bne), .JR(JR), .JUMP(JMP), .JAL(JAL), .LH(LH), .BLEZ(BLEZ), .SRAV(SRAV));

  // Other names for the same wires on the sheet: OP_CODE[5:0] = OP

  // Notes on the sheet:
  //   控制信号生成，产生数据通路需要的其他控制信号
  //   运算器控制器，根据指令生成运算器功能选择信号
endmodule

// 运算器控制器
module \运算控制器自动生成  (
  input  OP0,
  input  OP1,
  input  OP2,
  input  OP3,
  input  OP4,
  input  OP5,
  input  F0,
  input  F1,
  input  F2,
  input  F3,
  input  F4,
  input  F5,
  output S0,
  output S1,
  output S2,
  output S3
);

  wire and_1_out, and_2_out, and_3_out, and_4_out, and_5_out, and_6_out, and_7_out, and_8_out, and_9_out,
       and_10_out, and_11_out, and_12_out, and_13_out, and_14_out, and_15_out, and_16_out, and_17_out,
       and_18_out, and_19_out, and_20_out, and_21_out, and_22_out, and_23_out, and_24_out, and_25_out,
       and_26_out, and_27_out, and_28_out, and_29_out, and_30_out, and_31_out, and_32_out, and_33_out,
       and_34_out, and_35_out, and_36_out, and_37_out, and_38_out, and_39_out, not_1_out, not_2_out,
       not_3_out, not_4_out, not_5_out, not_6_out, not_7_out, not_8_out, not_9_out, not_10_out, not_11_out,
       not_12_out, not_13_out, not_14_out, not_15_out, not_16_out, not_17_out, not_18_out, not_19_out,
       not_20_out, not_21_out, not_22_out, not_23_out, not_24_out, not_25_out, not_26_out, not_27_out,
       not_28_out, not_29_out, not_30_out, not_31_out, not_32_out, not_33_out, not_34_out, not_35_out,
       not_36_out, not_37_out, not_38_out, not_39_out, not_40_out, not_41_out, not_42_out, not_43_out,
       not_44_out, not_45_out, not_46_out, not_47_out, not_48_out, not_49_out, not_50_out, not_51_out,
       not_52_out, not_53_out, not_54_out, not_55_out, not_56_out, not_57_out, not_58_out, not_59_out,
       not_60_out, not_61_out, not_62_out, not_63_out, not_64_out, not_65_out, not_66_out, not_67_out,
       not_68_out, not_69_out, not_70_out, not_71_out, not_72_out, not_73_out, not_74_out, not_75_out,
       not_76_out, not_77_out, not_78_out, not_79_out, not_80_out, not_81_out, not_82_out, not_83_out,
       not_84_out, not_85_out, not_86_out, not_87_out, not_88_out, not_89_out, not_90_out, not_91_out,
       not_92_out, not_93_out, not_94_out, not_95_out, not_96_out, not_97_out, not_98_out, not_99_out,
       not_100_out, not_101_out, not_102_out, not_103_out, not_104_out, not_105_out, not_106_out,
       not_107_out, not_108_out, not_109_out, not_110_out, not_111_out, not_112_out, not_113_out,
       not_114_out, not_115_out, not_116_out, not_117_out, not_118_out, not_119_out, not_120_out,
       not_121_out, not_122_out, not_123_out, not_124_out, not_125_out, not_126_out, not_127_out,
       not_128_out, not_129_out, not_130_out, not_131_out, not_132_out, not_133_out, not_134_out,
       not_135_out, not_136_out, not_137_out, not_138_out, not_139_out, not_140_out, not_141_out,
       not_142_out, not_143_out, not_144_out, not_145_out, not_146_out, not_147_out, not_148_out,
       not_149_out, not_150_out, not_151_out, not_152_out, not_153_out, not_154_out, not_155_out,
       not_156_out, not_157_out, not_158_out, not_159_out, not_160_out, not_161_out, not_162_out,
       not_163_out, not_164_out, not_165_out, not_166_out, not_167_out, not_168_out, not_169_out,
       not_170_out, not_171_out, not_172_out, not_173_out, not_174_out, not_175_out, not_176_out,
       not_177_out, not_178_out, not_179_out, not_180_out, not_181_out, not_182_out, not_183_out,
       not_184_out, not_185_out, not_186_out, not_187_out, not_188_out, not_189_out, not_190_out,
       not_191_out, not_192_out, not_193_out, not_194_out, not_195_out, not_196_out, not_197_out,
       not_198_out, not_199_out, not_200_out, not_201_out, not_202_out, not_203_out, not_204_out,
       not_205_out, not_206_out, not_207_out, not_208_out, not_209_out, not_210_out, not_211_out,
       not_212_out, not_213_out, not_214_out, not_215_out, not_216_out, not_217_out, not_218_out,
       not_219_out, not_220_out, not_221_out, not_222_out, not_223_out, not_224_out, not_225_out,
       not_226_out, not_227_out, not_228_out, not_229_out, not_230_out, not_231_out, not_232_out,
       not_233_out, not_234_out, not_235_out, not_236_out, not_237_out, not_238_out, not_239_out,
       not_240_out, not_241_out, not_242_out, not_243_out, not_244_out, not_245_out, not_246_out,
       not_247_out, not_248_out, not_249_out, not_250_out, not_251_out, not_252_out, not_253_out,
       not_254_out, not_255_out, not_256_out, not_257_out, not_258_out, not_259_out, not_260_out,
       not_261_out, not_262_out, not_263_out, not_264_out, not_265_out, not_266_out, not_267_out,
       not_268_out, not_269_out, not_270_out, not_271_out;

  not not_1 (not_1_out, OP5);
  not not_2 (not_2_out, OP4);
  not not_3 (not_3_out, OP3);
  not not_4 (not_4_out, OP2);
  not not_5 (not_5_out, OP1);
  not not_6 (not_6_out, OP0);
  not not_7 (not_7_out, F5);
  not not_8 (not_8_out, F4);
  not not_9 (not_9_out, F3);
  not not_10 (not_10_out, F2);
  not not_11 (not_11_out, OP5);
  not not_12 (not_12_out, OP4);
  not not_13 (not_13_out, OP3);
  not not_14 (not_14_out, OP2);
  not not_15 (not_15_out, OP1);
  not not_16 (not_16_out, OP0);
  not not_17 (not_17_out, F4);
  not not_18 (not_18_out, F3);
  not not_19 (not_19_out, F2);
  not not_20 (not_20_out, F1);
  not not_21 (not_21_out, F0);
  not not_22 (not_22_out, OP5);
  not not_23 (not_23_out, OP4);
  not not_24 (not_24_out, OP3);
  not not_25 (not_25_out, OP2);
  not not_26 (not_26_out, OP1);
  not not_27 (not_27_out, OP0);
  not not_28 (not_28_out, F4);
  not not_29 (not_29_out, F3);
  not not_30 (not_30_out, F2);
  not not_31 (not_31_out, F1);
  not not_32 (not_32_out, OP5);
  not not_33 (not_33_out, OP4);
  not not_34 (not_34_out, OP3);
  not not_35 (not_35_out, OP2);
  not not_36 (not_36_out, OP1);
  not not_37 (not_37_out, OP0);
  not not_38 (not_38_out, F4);
  not not_39 (not_39_out, F3);
  not not_40 (not_40_out, F1);
  not not_41 (not_41_out, F0);
  not not_42 (not_42_out, OP5);
  not not_43 (not_43_out, OP4);
  not not_44 (not_44_out, OP3);
  not not_45 (not_45_out, OP2);
  not not_46 (not_46_out, OP1);
  not not_47 (not_47_out, OP0);
  not not_48 (not_48_out, F4);
  not not_49 (not_49_out, F2);
  not not_50 (not_50_out, F0);
  not not_51 (not_51_out, OP5);
  not not_52 (not_52_out, OP4);
  not not_53 (not_53_out, OP2);
  not not_54 (not_54_out, OP1);
  not not_55 (not_55_out, OP0);
  not not_56 (not_56_out, OP5);
  not not_57 (not_57_out, OP4);
  not not_58 (not_58_out, OP1);
  not not_59 (not_59_out, OP0);
  not not_60 (not_60_out, OP5);
  not not_61 (not_61_out, OP4);
  not not_62 (not_62_out, OP2);
  not not_63 (not_63_out, OP1);
  not not_64 (not_64_out, OP5);
  not not_65 (not_65_out, OP4);
  not not_66 (not_66_out, OP2);
  not not_67 (not_67_out, OP0);
  not not_68 (not_68_out, OP4);
  not not_69 (not_69_out, OP3);
  not not_70 (not_70_out, OP2);
  not not_71 (not_71_out, OP4);
  not not_72 (not_72_out, OP2);
  not not_73 (not_73_out, OP5);
  not not_74 (not_74_out, OP4);
  not not_75 (not_75_out, OP3);
  not not_76 (not_76_out, OP2);
  not not_77 (not_77_out, OP1);
  not not_78 (not_78_out, OP0);
  not not_79 (not_79_out, F5);
  not not_80 (not_80_out, F4);
  not not_81 (not_81_out, F3);
  not not_82 (not_82_out, OP5);
  not not_83 (not_83_out, OP4);
  not not_84 (not_84_out, OP3);
  not not_85 (not_85_out, OP2);
  not not_86 (not_86_out, OP1);
  not not_87 (not_87_out, OP0);
  not not_88 (not_88_out, F4);
  not not_89 (not_89_out, F3);
  not not_90 (not_90_out, F0);
  not not_91 (not_91_out, OP4);
  not not_92 (not_92_out, OP3);
  not not_93 (not_93_out, OP2);
  not not_94 (not_94_out, OP1);
  not not_95 (not_95_out, OP5);
  not not_96 (not_96_out, OP4);
  not not_97 (not_97_out, OP3);
  not not_98 (not_98_out, OP2);
  not not_99 (not_99_out, OP1);
  not not_100 (not_100_out, OP0);
  not not_101 (not_101_out, F5);
  not not_102 (not_102_out, F4);
  not not_103 (not_103_out, F3);
  not not_104 (not_104_out, F2);
  not not_105 (not_105_out, F0);
  not not_106 (not_106_out, OP5);
  not not_107 (not_107_out, OP4);
  not not_108 (not_108_out, OP3);
  not not_109 (not_109_out, OP2);
  not not_110 (not_110_out, OP1);
  not not_111 (not_111_out, OP0);
  not not_112 (not_112_out, F4);
  not not_113 (not_113_out, F3);
  not not_114 (not_114_out, F2);
  not not_115 (not_115_out, F0);
  not not_116 (not_116_out, OP5);
  not not_117 (not_117_out, OP4);
  not not_118 (not_118_out, OP3);
  not not_119 (not_119_out, OP2);
  not not_120 (not_120_out, OP1);
  not not_121 (not_121_out, OP0);
  not not_122 (not_122_out, F4);
  not not_123 (not_123_out, F3);
  not not_124 (not_124_out, F1);
  not not_125 (not_125_out, F0);
  not not_126 (not_126_out, OP5);
  not not_127 (not_127_out, OP4);
  not not_128 (not_128_out, OP3);
  not not_129 (not_129_out, OP2);
  not not_130 (not_130_out, OP1);
  not not_131 (not_131_out, OP0);
  not not_132 (not_132_out, F4);
  not not_133 (not_133_out, F3);
  not not_134 (not_134_out, OP5);
  not not_135 (not_135_out, OP4);
  not not_136 (not_136_out, OP3);
  not not_137 (not_137_out, OP2);
  not not_138 (not_138_out, OP1);
  not not_139 (not_139_out, OP0);
  not not_140 (not_140_out, F4);
  not not_141 (not_141_out, F2);
  not not_142 (not_142_out, F0);
  not not_143 (not_143_out, OP5);
  not not_144 (not_144_out, OP4);
  not not_145 (not_145_out, OP1);
  not not_146 (not_146_out, OP0);
  not not_147 (not_147_out, OP5);
  not not_148 (not_148_out, OP4);
  not not_149 (not_149_out, OP2);
  not not_150 (not_150_out, OP0);
  not not_151 (not_151_out, OP5);
  not not_152 (not_152_out, OP4);
  not not_153 (not_153_out, OP3);
  not not_154 (not_154_out, OP2);
  not not_155 (not_155_out, OP1);
  not not_156 (not_156_out, OP0);
  not not_157 (not_157_out, F4);
  not not_158 (not_158_out, F3);
  not not_159 (not_159_out, F2);
  not not_160 (not_160_out, F1);
  not not_161 (not_161_out, F0);
  not not_162 (not_162_out, OP5);
  not not_163 (not_163_out, OP4);
  not not_164 (not_164_out, OP3);
  not not_165 (not_165_out, OP2);
  not not_166 (not_166_out, OP1);
  not not_167 (not_167_out, OP0);
  not not_168 (not_168_out, F4);
  not not_169 (not_169_out, F3);
  not not_170 (not_170_out, F2);
  not not_171 (not_171_out, F1);
  not not_172 (not_172_out, OP5);
  not not_173 (not_173_out, OP4);
  not not_174 (not_174_out, OP3);
  not not_175 (not_175_out, OP2);
  not not_176 (not_176_out, OP1);
  not not_177 (not_177_out, OP0);
  not not_178 (not_178_out, F4);
  not not_179 (not_179_out, F3);
  not not_180 (not_180_out, F2);
  not not_181 (not_181_out, F0);
  not not_182 (not_182_out, OP5);
  not not_183 (not_183_out, OP4);
  not not_184 (not_184_out, OP3);
  not not_185 (not_185_out, OP2);
  not not_186 (not_186_out, OP1);
  not not_187 (not_187_out, OP0);
  not not_188 (not_188_out, F4);
  not not_189 (not_189_out, F3);
  not not_190 (not_190_out, F1);
  not not_191 (not_191_out, F0);
  not not_192 (not_192_out, OP5);
  not not_193 (not_193_out, OP4);
  not not_194 (not_194_out, OP3);
  not not_195 (not_195_out, OP2);
  not not_196 (not_196_out, OP1);
  not not_197 (not_197_out, OP0);
  not not_198 (not_198_out, F4);
  not not_199 (not_199_out, F2);
  not not_200 (not_200_out, OP5);
  not not_201 (not_201_out, OP4);
  not not_202 (not_202_out, OP2);
  not not_203 (not_203_out, OP1);
  not not_204 (not_204_out, OP0);
  not not_205 (not_205_out, OP5);
  not not_206 (not_206_out, OP4);
  not not_207 (not_207_out, OP1);
  not not_208 (not_208_out, OP0);
  not not_209 (not_209_out, OP5);
  not not_210 (not_210_out, OP4);
  not not_211 (not_211_out, OP2);
  not not_212 (not_212_out, OP1);
  not not_213 (not_213_out, OP4);
  not not_214 (not_214_out, OP3);
  not not_215 (not_215_out, OP2);
  not not_216 (not_216_out, OP4);
  not not_217 (not_217_out, OP2);
  not not_218 (not_218_out, OP4);
  not not_219 (not_219_out, OP3);
  not not_220 (not_220_out, OP2);
  not not_221 (not_221_out, OP1);
  not not_222 (not_222_out, OP5);
  not not_223 (not_223_out, OP4);
  not not_224 (not_224_out, OP3);
  not not_225 (not_225_out, OP2);
  not not_226 (not_226_out, OP1);
  not not_227 (not_227_out, OP0);
  not not_228 (not_228_out, F4);
  not not_229 (not_229_out, F3);
  not not_230 (not_230_out, F1);
  not not_231 (not_231_out, OP5);
  not not_232 (not_232_out, OP4);
  not not_233 (not_233_out, OP3);
  not not_234 (not_234_out, OP2);
  not not_235 (not_235_out, OP1);
  not not_236 (not_236_out, OP0);
  not not_237 (not_237_out, F4);
  not not_238 (not_238_out, F3);
  not not_239 (not_239_out, OP5);
  not not_240 (not_240_out, OP4);
  not not_241 (not_241_out, OP3);
  not not_242 (not_242_out, OP2);
  not not_243 (not_243_out, OP1);
  not not_244 (not_244_out, OP0);
  not not_245 (not_245_out, F4);
  not not_246 (not_246_out, F2);
  not not_247 (not_247_out, F0);
  not not_248 (not_248_out, OP5);
  not not_249 (not_249_out, OP4);
  not not_250 (not_250_out, OP3);
  not not_251 (not_251_out, OP2);
  not not_252 (not_252_out, OP1);
  not not_253 (not_253_out, OP0);
  not not_254 (not_254_out, F4);
  not not_255 (not_255_out, F2);
  not not_256 (not_256_out, OP5);
  not not_257 (not_257_out, OP4);
  not not_258 (not_258_out, OP2);
  not not_259 (not_259_out, OP0);
  not not_260 (not_260_out, OP5);
  not not_261 (not_261_out, OP4);
  not not_262 (not_262_out, OP1);
  not not_263 (not_263_out, OP5);
  not not_264 (not_264_out, OP4);
  not not_265 (not_265_out, OP3);
  not not_266 (not_266_out, OP2);
  not not_267 (not_267_out, OP1);
  not not_268 (not_268_out, OP0);
  not not_269 (not_269_out, F4);
  not not_270 (not_270_out, F3);
  not not_271 (not_271_out, F0);
  and and_1 (and_1_out, not_1_out, not_2_out, not_3_out, not_4_out, not_5_out, not_6_out, not_7_out, not_8_out, not_9_out, not_10_out, F1, F0);
  and and_2 (and_2_out, not_11_out, not_12_out, not_13_out, not_14_out, not_15_out, not_16_out, F5, not_17_out, not_18_out, not_19_out, not_20_out, not_21_out);
  and and_3 (and_3_out, not_22_out, not_23_out, not_24_out, not_25_out, not_26_out, not_27_out, F5, not_28_out, not_29_out, not_30_out, not_31_out, F0);
  and and_4 (and_4_out, not_32_out, not_33_out, not_34_out, not_35_out, not_36_out, not_37_out, F5, not_38_out, not_39_out, F2, not_40_out, not_41_out);
  and and_5 (and_5_out, not_42_out, not_43_out, not_44_out, not_45_out, not_46_out, not_47_out, F5, not_48_out, F3, not_49_out, F1, not_50_out);
  and and_6 (and_6_out, not_51_out, not_52_out, OP3, not_53_out, not_54_out, not_55_out);
  and and_7 (and_7_out, not_56_out, not_57_out, OP3, OP2, not_58_out, not_59_out);
  and and_8 (and_8_out, not_60_out, not_61_out, OP3, not_62_out, not_63_out, OP0);
  and and_9 (and_9_out, not_64_out, not_65_out, OP3, not_66_out, OP1, not_67_out);
  and and_10 (and_10_out, OP5, not_68_out, not_69_out, not_70_out, OP1, OP0);
  and and_11 (and_11_out, OP5, not_71_out, OP3, not_72_out, OP1, OP0);
  and and_12 (and_12_out, not_73_out, not_74_out, not_75_out, not_76_out, not_77_out, not_78_out, not_79_out, not_80_out, not_81_out, F2, F1, F0);
  and and_13 (and_13_out, not_82_out, not_83_out, not_84_out, not_85_out, not_86_out, not_87_out, F5, not_88_out, not_89_out, F2, F1, not_90_out);
  and and_14 (and_14_out, OP5, not_91_out, not_92_out, not_93_out, not_94_out, OP0);
  and and_15 (and_15_out, not_95_out, not_96_out, not_97_out, not_98_out, not_99_out, not_100_out, not_101_out, not_102_out, not_103_out, not_104_out, F1, not_105_out);
  and and_16 (and_16_out, not_106_out, not_107_out, not_108_out, not_109_out, not_110_out, not_111_out, F5, not_112_out, not_113_out, not_114_out, F1, not_115_out);
  and and_17 (and_17_out, not_116_out, not_117_out, not_118_out, not_119_out, not_120_out, not_121_out, F5, not_122_out, not_123_out, F2, not_124_out, not_125_out);
  and and_18 (and_18_out, not_126_out, not_127_out, not_128_out, not_129_out, not_130_out, not_131_out, F5, not_132_out, not_133_out, F2, F1, F0);
  and and_19 (and_19_out, not_134_out, not_135_out, not_136_out, not_137_out, not_138_out, not_139_out, F5, not_140_out, F3, not_141_out, F1, not_142_out);
  and and_20 (and_20_out, not_143_out, not_144_out, OP3, OP2, not_145_out, not_146_out);
  and and_21 (and_21_out, not_147_out, not_148_out, OP3, not_149_out, OP1, not_150_out);
  and and_22 (and_22_out, not_151_out, not_152_out, not_153_out, not_154_out, not_155_out, not_156_out, F5, not_157_out, not_158_out, not_159_out, not_160_out, not_161_out);
  and and_23 (and_23_out, not_162_out, not_163_out, not_164_out, not_165_out, not_166_out, not_167_out, F5, not_168_out, not_169_out, not_170_out, not_171_out, F0);
  and and_24 (and_24_out, not_172_out, not_173_out, not_174_out, not_175_out, not_176_out, not_177_out, F5, not_178_out, not_179_out, not_180_out, F1, not_181_out);
  and and_25 (and_25_out, not_182_out, not_183_out, not_184_out, not_185_out, not_186_out, not_187_out, F5, not_188_out, not_189_out, F2, not_190_out, not_191_out);
  and and_26 (and_26_out, not_192_out, not_193_out, not_194_out, not_195_out, not_196_out, not_197_out, F5, not_198_out, F3, not_199_out, F1, F0);
  and and_27 (and_27_out, not_200_out, not_201_out, OP3, not_202_out, not_203_out, not_204_out);
  and and_28 (and_28_out, not_205_out, not_206_out, OP3, OP2, not_207_out, not_208_out);
  and and_29 (and_29_out, not_209_out, not_210_out, OP3, not_211_out, not_212_out, OP0);
  and and_30 (and_30_out, OP5, not_213_out, not_214_out, not_215_out, OP1, OP0);
  and and_31 (and_31_out, OP5, not_216_out, OP3, not_217_out, OP1, OP0);
  and and_32 (and_32_out, OP5, not_218_out, not_219_out, not_220_out, not_221_out, OP0);
  and and_33 (and_33_out, not_222_out, not_223_out, not_224_out, not_225_out, not_226_out, not_227_out, F5, not_228_out, not_229_out, F2, not_230_out, F0);
  and and_34 (and_34_out, not_231_out, not_232_out, not_233_out, not_234_out, not_235_out, not_236_out, F5, not_237_out, not_238_out, F2, F1, F0);
  and and_35 (and_35_out, not_239_out, not_240_out, not_241_out, not_242_out, not_243_out, not_244_out, F5, not_245_out, F3, not_246_out, F1, not_247_out);
  and and_36 (and_36_out, not_248_out, not_249_out, not_250_out, not_251_out, not_252_out, not_253_out, F5, not_254_out, F3, not_255_out, F1, F0);
  and and_37 (and_37_out, not_256_out, not_257_out, OP3, not_258_out, OP1, not_259_out);
  and and_38 (and_38_out, not_260_out, not_261_out, OP3, OP2, not_262_out, OP0);
  and and_39 (and_39_out, not_263_out, not_264_out, not_265_out, not_266_out, not_267_out, not_268_out, F5, not_269_out, not_270_out, F2, F1, not_271_out);
  or or_1 (S1, and_15_out, and_16_out, and_17_out, and_18_out, and_19_out, and_20_out, and_21_out);
  or or_2 (S2, and_22_out, and_23_out, and_24_out, and_25_out, and_26_out, and_27_out, and_28_out, and_29_out, and_30_out, and_31_out, and_32_out);
  or or_3 (S3, and_33_out, and_34_out, and_35_out, and_36_out, and_37_out, and_38_out, and_39_out);
  or or_4 (S0, and_1_out, and_2_out, and_3_out, and_4_out, and_5_out, and_6_out, and_7_out, and_8_out, and_9_out, and_10_out, and_11_out, and_12_out, and_13_out, and_14_out);
endmodule

// 控制信号生成
module \控制信号自动生成  (
  input  OP0,
  input  OP1,
  input  OP2,
  input  OP3,
  input  OP4,
  input  OP5,
  input  F0,
  input  F1,
  input  F2,
  input  F3,
  input  F4,
  input  F5,
  output MemToReg,
  output MemWrite,
  output ALU_SRC,
  output RegWrite,
  output SysCALL,
  output SignedExt,
  output RegDst,
  output BEQ,
  output BNE,
  output JR,
  output JUMP,
  output JAL,
  output LH,
  output BLEZ,
  output SRAV
);

  wire and_3_out, and_4_out, and_5_out, and_6_out, and_7_out, and_8_out, and_9_out, and_10_out, and_11_out,
       and_12_out, and_13_out, and_14_out, and_15_out, and_17_out, and_18_out, and_19_out, and_20_out,
       and_21_out, and_22_out, and_23_out, and_24_out, and_25_out, and_26_out, and_27_out, and_31_out,
       and_32_out, not_1_out, not_2_out, not_3_out, not_4_out, not_5_out, not_6_out, not_7_out, not_8_out,
       not_9_out, not_10_out, not_11_out, not_12_out, not_13_out, not_14_out, not_15_out, not_16_out,
       not_17_out, not_18_out, not_19_out, not_20_out, not_21_out, not_22_out, not_23_out, not_24_out,
       not_25_out, not_26_out, not_27_out, not_28_out, not_29_out, not_30_out, not_31_out, not_32_out,
       not_33_out, not_34_out, not_35_out, not_36_out, not_37_out, not_38_out, not_39_out, not_40_out,
       not_41_out, not_42_out, not_43_out, not_44_out, not_45_out, not_46_out, not_47_out, not_48_out,
       not_49_out, not_50_out, not_51_out, not_52_out, not_53_out, not_54_out, not_55_out, not_56_out,
       not_57_out, not_58_out, not_59_out, not_60_out, not_61_out, not_62_out, not_63_out, not_64_out,
       not_65_out, not_66_out, not_67_out, not_68_out, not_69_out, not_70_out, not_71_out, not_72_out,
       not_73_out, not_74_out, not_75_out, not_76_out, not_77_out, not_78_out, not_79_out, not_80_out,
       not_81_out, not_82_out, not_83_out, not_84_out, not_85_out, not_86_out, not_87_out, not_88_out,
       not_89_out, not_90_out, not_91_out, not_92_out, not_93_out, not_94_out, not_95_out, not_96_out,
       not_97_out, not_98_out, not_99_out, not_100_out, not_101_out, not_102_out, not_103_out, not_104_out,
       not_105_out, not_106_out, not_107_out, not_108_out, not_109_out, not_110_out, not_111_out,
       not_112_out, not_113_out, not_114_out, not_115_out, not_116_out, not_117_out, not_118_out,
       not_119_out, not_120_out, not_121_out, not_122_out, not_123_out, not_124_out, not_125_out,
       not_126_out, not_127_out, not_128_out, not_129_out, not_130_out, not_131_out, not_132_out,
       not_133_out, not_134_out, not_135_out, not_136_out, not_137_out, not_138_out, not_139_out,
       not_140_out, not_141_out, not_142_out, not_143_out, not_144_out, not_145_out, not_146_out,
       not_147_out, not_148_out, not_149_out, not_150_out, not_151_out, not_152_out, not_153_out,
       not_154_out, not_155_out, not_156_out, not_157_out, not_158_out, not_159_out, not_160_out,
       not_161_out, not_162_out, not_163_out, not_164_out, not_165_out, not_166_out, not_167_out,
       not_168_out, not_169_out, not_170_out, not_171_out, not_172_out, not_173_out, not_174_out,
       not_175_out, not_176_out, not_177_out, not_178_out, not_179_out, not_180_out, not_181_out,
       not_182_out, not_183_out, not_184_out, not_185_out, not_186_out, not_187_out, not_188_out,
       not_189_out, not_190_out, not_191_out, not_192_out, not_193_out, not_194_out, not_195_out,
       not_196_out, not_197_out, not_198_out, not_199_out;

  not not_1 (not_1_out, OP2);
  not not_2 (not_2_out, OP3);
  not not_3 (not_3_out, OP4);
  not not_4 (not_4_out, OP2);
  not not_5 (not_5_out, OP4);
  not not_6 (not_6_out, OP0);
  not not_7 (not_7_out, OP2);
  not not_8 (not_8_out, OP4);
  not not_9 (not_9_out, OP5);
  not not_10 (not_10_out, OP1);
  not not_11 (not_11_out, OP4);
  not not_12 (not_12_out, OP5);
  not not_13 (not_13_out, OP2);
  not not_14 (not_14_out, OP3);
  not not_15 (not_15_out, OP4);
  not not_16 (not_16_out, OP2);
  not not_17 (not_17_out, OP4);
  not not_18 (not_18_out, OP0);
  not not_19 (not_19_out, OP1);
  not not_20 (not_20_out, OP2);
  not not_21 (not_21_out, OP4);
  not not_22 (not_22_out, OP5);
  not not_23 (not_23_out, F0);
  not not_24 (not_24_out, F2);
  not not_25 (not_25_out, F3);
  not not_26 (not_26_out, F4);
  not not_27 (not_27_out, OP0);
  not not_28 (not_28_out, OP1);
  not not_29 (not_29_out, OP2);
  not not_30 (not_30_out, OP4);
  not not_31 (not_31_out, OP5);
  not not_32 (not_32_out, F1);
  not not_33 (not_33_out, F3);
  not not_34 (not_34_out, F4);
  not not_35 (not_35_out, OP0);
  not not_36 (not_36_out, OP1);
  not not_37 (not_37_out, OP2);
  not not_38 (not_38_out, OP4);
  not not_39 (not_39_out, OP5);
  not not_40 (not_40_out, F3);
  not not_41 (not_41_out, F4);
  not not_42 (not_42_out, OP0);
  not not_43 (not_43_out, OP1);
  not not_44 (not_44_out, OP2);
  not not_45 (not_45_out, OP4);
  not not_46 (not_46_out, OP5);
  not not_47 (not_47_out, F2);
  not not_48 (not_48_out, F4);
  not not_49 (not_49_out, OP0);
  not not_50 (not_50_out, OP1);
  not not_51 (not_51_out, OP2);
  not not_52 (not_52_out, OP4);
  not not_53 (not_53_out, OP5);
  not not_54 (not_54_out, F3);
  not not_55 (not_55_out, F4);
  not not_56 (not_56_out, F5);
  not not_57 (not_57_out, OP0);
  not not_58 (not_58_out, OP2);
  not not_59 (not_59_out, OP4);
  not not_60 (not_60_out, OP5);
  not not_61 (not_61_out, OP1);
  not not_62 (not_62_out, OP4);
  not not_63 (not_63_out, OP5);
  not not_64 (not_64_out, OP2);
  not not_65 (not_65_out, OP3);
  not not_66 (not_66_out, OP4);
  not not_67 (not_67_out, OP2);
  not not_68 (not_68_out, OP3);
  not not_69 (not_69_out, OP4);
  not not_70 (not_70_out, OP0);
  not not_71 (not_71_out, OP1);
  not not_72 (not_72_out, OP2);
  not not_73 (not_73_out, OP3);
  not not_74 (not_74_out, OP4);
  not not_75 (not_75_out, OP5);
  not not_76 (not_76_out, F0);
  not not_77 (not_77_out, F1);
  not not_78 (not_78_out, F4);
  not not_79 (not_79_out, F5);
  not not_80 (not_80_out, OP0);
  not not_81 (not_81_out, OP2);
  not not_82 (not_82_out, OP4);
  not not_83 (not_83_out, OP5);
  not not_84 (not_84_out, OP1);
  not not_85 (not_85_out, OP2);
  not not_86 (not_86_out, OP4);
  not not_87 (not_87_out, OP5);
  not not_88 (not_88_out, OP0);
  not not_89 (not_89_out, OP3);
  not not_90 (not_90_out, OP4);
  not not_91 (not_91_out, OP5);
  not not_92 (not_92_out, OP1);
  not not_93 (not_93_out, OP3);
  not not_94 (not_94_out, OP4);
  not not_95 (not_95_out, OP5);
  not not_96 (not_96_out, OP2);
  not not_97 (not_97_out, OP3);
  not not_98 (not_98_out, OP4);
  not not_99 (not_99_out, OP2);
  not not_100 (not_100_out, OP4);
  not not_101 (not_101_out, OP0);
  not not_102 (not_102_out, OP1);
  not not_103 (not_103_out, OP2);
  not not_104 (not_104_out, OP3);
  not not_105 (not_105_out, OP4);
  not not_106 (not_106_out, OP5);
  not not_107 (not_107_out, F0);
  not not_108 (not_108_out, F2);
  not not_109 (not_109_out, F3);
  not not_110 (not_110_out, F4);
  not not_111 (not_111_out, OP0);
  not not_112 (not_112_out, OP1);
  not not_113 (not_113_out, OP2);
  not not_114 (not_114_out, OP3);
  not not_115 (not_115_out, OP4);
  not not_116 (not_116_out, OP5);
  not not_117 (not_117_out, F1);
  not not_118 (not_118_out, F3);
  not not_119 (not_119_out, F4);
  not not_120 (not_120_out, OP0);
  not not_121 (not_121_out, OP1);
  not not_122 (not_122_out, OP2);
  not not_123 (not_123_out, OP3);
  not not_124 (not_124_out, OP4);
  not not_125 (not_125_out, OP5);
  not not_126 (not_126_out, F3);
  not not_127 (not_127_out, F4);
  not not_128 (not_128_out, OP0);
  not not_129 (not_129_out, OP1);
  not not_130 (not_130_out, OP2);
  not not_131 (not_131_out, OP3);
  not not_132 (not_132_out, OP4);
  not not_133 (not_133_out, OP5);
  not not_134 (not_134_out, F2);
  not not_135 (not_135_out, F4);
  not not_136 (not_136_out, OP0);
  not not_137 (not_137_out, OP1);
  not not_138 (not_138_out, OP2);
  not not_139 (not_139_out, OP3);
  not not_140 (not_140_out, OP4);
  not not_141 (not_141_out, OP5);
  not not_142 (not_142_out, F3);
  not not_143 (not_143_out, F4);
  not not_144 (not_144_out, F5);
  not not_145 (not_145_out, OP0);
  not not_146 (not_146_out, OP1);
  not not_147 (not_147_out, OP3);
  not not_148 (not_148_out, OP4);
  not not_149 (not_149_out, OP5);
  not not_150 (not_150_out, OP1);
  not not_151 (not_151_out, OP3);
  not not_152 (not_152_out, OP4);
  not not_153 (not_153_out, OP5);
  not not_154 (not_154_out, OP0);
  not not_155 (not_155_out, OP1);
  not not_156 (not_156_out, OP2);
  not not_157 (not_157_out, OP3);
  not not_158 (not_158_out, OP4);
  not not_159 (not_159_out, OP5);
  not not_160 (not_160_out, F0);
  not not_161 (not_161_out, F1);
  not not_162 (not_162_out, F2);
  not not_163 (not_163_out, F4);
  not not_164 (not_164_out, F5);
  not not_165 (not_165_out, OP0);
  not not_166 (not_166_out, OP2);
  not not_167 (not_167_out, OP3);
  not not_168 (not_168_out, OP4);
  not not_169 (not_169_out, OP5);
  not not_170 (not_170_out, F0);
  not not_171 (not_171_out, F1);
  not not_172 (not_172_out, F2);
  not not_173 (not_173_out, F4);
  not not_174 (not_174_out, F5);
  not not_175 (not_175_out, OP2);
  not not_176 (not_176_out, OP3);
  not not_177 (not_177_out, OP4);
  not not_178 (not_178_out, OP5);
  not not_179 (not_179_out, OP2);
  not not_180 (not_180_out, OP3);
  not not_181 (not_181_out, OP4);
  not not_182 (not_182_out, OP5);
  not not_183 (not_183_out, OP1);
  not not_184 (not_184_out, OP2);
  not not_185 (not_185_out, OP3);
  not not_186 (not_186_out, OP4);
  not not_187 (not_187_out, OP0);
  not not_188 (not_188_out, OP3);
  not not_189 (not_189_out, OP4);
  not not_190 (not_190_out, OP5);
  not not_191 (not_191_out, OP5);
  not not_192 (not_192_out, OP4);
  not not_193 (not_193_out, OP3);
  not not_194 (not_194_out, OP2);
  not not_195 (not_195_out, OP1);
  not not_196 (not_196_out, OP0);
  not not_197 (not_197_out, F5);
  not not_198 (not_198_out, F4);
  not not_199 (not_199_out, F3);
  and and_1 (MemToReg, OP0, not_1_out, not_2_out, not_3_out, OP5);
  and and_2 (MemWrite, OP0, OP1, not_4_out, OP3, not_5_out, OP5);
  and and_3 (and_3_out, not_6_out, not_7_out, OP3, not_8_out, not_9_out);
  and and_4 (and_4_out, not_10_out, OP3, not_11_out, not_12_out);
  and and_5 (and_5_out, OP0, not_13_out, not_14_out, not_15_out, OP5);
  and and_6 (and_6_out, OP0, OP1, not_16_out, not_17_out, OP5);
  and and_7 (and_7_out, not_18_out, not_19_out, not_20_out, not_21_out, not_22_out, not_23_out, not_24_out, not_25_out, not_26_out);
  and and_8 (and_8_out, not_27_out, not_28_out, not_29_out, not_30_out, not_31_out, not_32_out, not_33_out, not_34_out, F5);
  and and_9 (and_9_out, not_35_out, not_36_out, not_37_out, not_38_out, not_39_out, F2, not_40_out, not_41_out, F5);
  and and_10 (and_10_out, not_42_out, not_43_out, not_44_out, not_45_out, not_46_out, F1, not_47_out, F3, not_48_out, F5);
  and and_11 (and_11_out, not_49_out, not_50_out, not_51_out, not_52_out, not_53_out, F0, F1, not_54_out, not_55_out, not_56_out);
  and and_12 (and_12_out, not_57_out, not_58_out, OP3, not_59_out, not_60_out);
  and and_13 (and_13_out, not_61_out, OP3, not_62_out, not_63_out);
  and and_14 (and_14_out, OP0, not_64_out, not_65_out, not_66_out, OP5);
  and and_15 (and_15_out, OP0, OP1, not_67_out, not_68_out, not_69_out);
  and and_16 (SysCALL, not_70_out, not_71_out, not_72_out, not_73_out, not_74_out, not_75_out, not_76_out, not_77_out, F2, F3, not_78_out, not_79_out);
  and and_17 (and_17_out, not_80_out, not_81_out, OP3, not_82_out, not_83_out);
  and and_18 (and_18_out, not_84_out, not_85_out, OP3, not_86_out, not_87_out);
  and and_19 (and_19_out, not_88_out, OP2, not_89_out, not_90_out, not_91_out);
  and and_20 (and_20_out, not_92_out, OP2, not_93_out, not_94_out, not_95_out);
  and and_21 (and_21_out, OP0, not_96_out, not_97_out, not_98_out, OP5);
  and and_22 (and_22_out, OP0, OP1, not_99_out, not_100_out, OP5);
  and and_23 (and_23_out, not_101_out, not_102_out, not_103_out, not_104_out, not_105_out, not_106_out, not_107_out, not_108_out, not_109_out, not_110_out);
  and and_24 (and_24_out, not_111_out, not_112_out, not_113_out, not_114_out, not_115_out, not_116_out, not_117_out, not_118_out, not_119_out, F5);
  and and_25 (and_25_out, not_120_out, not_121_out, not_122_out, not_123_out, not_124_out, not_125_out, F2, not_126_out, not_127_out, F5);
  and and_26 (and_26_out, not_128_out, not_129_out, not_130_out, not_131_out, not_132_out, not_133_out, F1, not_134_out, F3, not_135_out, F5);
  and and_27 (and_27_out, not_136_out, not_137_out, not_138_out, not_139_out, not_140_out, not_141_out, F0, F1, not_142_out, not_143_out, not_144_out);
  and and_28 (BEQ, not_145_out, not_146_out, OP2, not_147_out, not_148_out, not_149_out);
  and and_29 (BNE, OP0, not_150_out, OP2, not_151_out, not_152_out, not_153_out);
  and and_30 (JR, not_154_out, not_155_out, not_156_out, not_157_out, not_158_out, not_159_out, not_160_out, not_161_out, not_162_out, F3, not_163_out, not_164_out);
  and and_31 (and_31_out, not_165_out, not_166_out, not_167_out, not_168_out, not_169_out, not_170_out, not_171_out, not_172_out, F3, not_173_out, not_174_out);
  and and_32 (and_32_out, OP1, not_175_out, not_176_out, not_177_out, not_178_out);
  and and_33 (JAL, OP0, OP1, not_179_out, not_180_out, not_181_out, not_182_out);
  and and_34 (LH, OP0, not_183_out, not_184_out, not_185_out, not_186_out, OP5);
  and and_35 (BLEZ, not_187_out, OP1, OP2, not_188_out, not_189_out, not_190_out);
  and and_36 (SRAV, not_191_out, not_192_out, not_193_out, not_194_out, not_195_out, not_196_out, not_197_out, not_198_out, not_199_out, F2, F1, F0);
  or or_1 (ALU_SRC, and_3_out, and_4_out, and_5_out, and_6_out);
  or or_2 (RegWrite, and_7_out, and_8_out, and_9_out, and_10_out, and_11_out, and_12_out, and_13_out, and_14_out, and_15_out);
  or or_3 (SignedExt, and_17_out, and_18_out, and_19_out, and_20_out, and_21_out, and_22_out);
  or or_4 (RegDst, and_23_out, and_24_out, and_25_out, and_26_out, and_27_out);
  or or_5 (JUMP, and_31_out, and_32_out);
endmodule

// ALU
module MIPS_ALU (
  input  [4:0] shamt,
  input  [31:0] X,
  input  [31:0] Y,
  input  [3:0] AluOP,
  output Equal,
  output [31:0] Result,
  output [31:0] Result_2
);

  wire [0:0] comparator_1_lt, comparator_2_lt;
  wire [31:0] adder_1_out, AND_out, divider_1_out, divider_1_rem, multiplier_1_cout, multiplier_1_out,
       NOR_out, OR_out, shifter_1_out, shifter_2_out, shifter_3_out, subtractor_1_out, XOR_out;

  assign AND_out = X & Y;  // AND_Gate AND, 32 bits wide
  assign OR_out = X | Y;  // OR_Gate OR, 32 bits wide
  Shifter #(.width(32), .shift("ll")) shifter_1 (.in(Y), .\dist (shamt), .out(shifter_1_out));
  Shifter #(.width(32), .shift("ar")) shifter_2 (.in(Y), .\dist (shamt), .out(shifter_2_out));
  Shifter #(.width(32), .shift("lr")) shifter_3 (.in(Y), .\dist (shamt), .out(shifter_3_out));
  Multiplier #(.width(32)) multiplier_1 (.a(X), .b(Y), .out(multiplier_1_out), .cout(multiplier_1_cout));  // open: cin
  Divider #(.width(32)) divider_1 (.a(X), .b(Y), .out(divider_1_out), .rem(divider_1_rem));  // open: upper
  Adder #(.width(32)) adder_1 (.a(X), .b(Y), .out(adder_1_out));  // open: cin, cout
  Subtractor #(.width(32)) subtractor_1 (.a(X), .b(Y), .out(subtractor_1_out));  // open: bin, bout
  assign XOR_out = X ^ Y;  // XOR_Gate XOR, 32 bits wide
  assign NOR_out = ~(X | Y);  // NOR_Gate NOR, 32 bits wide
  Comparator #(.width(32), .mode("twosComplement")) comparator_1 (
    .a(X), .b(Y), .eq(Equal), .lt(comparator_1_lt[0]));  // open: gt
  Comparator #(.width(32), .mode("unsigned")) comparator_2 (.a(X), .b(Y), .lt(comparator_2_lt[0]));  // open: gt, eq
  Multiplexer #(.select(4), .width(32), .disabled("Z"), .enable("false")) multiplexer_1 (
    .in0(shifter_1_out), .in1(shifter_2_out), .in2(shifter_3_out), .in3(multiplier_1_out),
    .in4(divider_1_out), .in5(adder_1_out), .in6(subtractor_1_out), .in7(AND_out), .in8(OR_out),
    .in9(XOR_out), .in10(NOR_out), .in11({{31{1'b0}}, comparator_1_lt[0]}),
    .in12({{31{1'b0}}, comparator_2_lt[0]}), .in13({32{1'b0}}), .in14({32{1'b0}}), .in15({32{1'b0}}),
    .out(Result), .sel(AluOP));
  Multiplexer #(.select(4), .width(32), .disabled("Z"), .enable("false")) multiplexer_2 (
    .in0({32{1'b0}}), .in1({32{1'b0}}), .in2({32{1'b0}}), .in3(multiplier_1_cout), .in4(divider_1_rem),
    .in5({32{1'b0}}), .in6({32{1'b0}}), .in7({32{1'b0}}), .in8({32{1'b0}}), .in9({32{1'b0}}),
    .in10({32{1'b0}}), .in11({32{1'b0}}), .in12({32{1'b0}}), .in13({32{1'b0}}), .in14({32{1'b0}}),
    .in15({32{1'b0}}), .out(Result_2), .sel(AluOP));

  // Other names for the same wires on the sheet: Result2[31:0] = Result_2; S[3:0] = AluOP

  // Notes on the sheet:
  //   不要改变此引脚区域内容，也不要改变ALU封装形式
  //   输入引脚
  //   输出引脚
endmodule

module MIPS_Regifile (
  input  [31:0] Din,
  input  Clk,
  input  WE,
  input  [4:0] R1_num,
  input  [4:0] W_num,
  input  [4:0] R2_num,
  output [31:0] R1,
  output [31:0] R2
);

  // RegisterFile registerfile_1: pin names not known; wires that end beside it: Din, Clk, WE, W_num, R1_num, R2_num, R1, R2
endmodule

module IF_ID (
  input  [31:0] PC,
  input  [31:0] IR,
  input  [31:0] Sequence_addr,
  input  CLK,
  input  clr,
  input  EN,
  output [31:0] PC_2,
  output [31:0] IR_2,
  output [31:0] Sequence_addr_2
);

  wire [31:0] multiplexer_1_out, multiplexer_2_out, multiplexer_3_out;

  Pull_Resistor #(.pull(0)) pull_resistor_1 (.node(clr));
  Multiplexer #(.select(1), .width(32), .disabled("Z"), .enable("false")) multiplexer_1 (
    .in0(PC), .in1({32{1'b0}}), .out(multiplexer_1_out), .sel(clr));
  Multiplexer #(.select(1), .width(32), .disabled("Z"), .enable("false")) multiplexer_2 (
    .in0(IR), .in1({32{1'b0}}), .out(multiplexer_2_out), .sel(clr));
  Multiplexer #(.select(1), .width(32), .disabled("Z"), .enable("false")) multiplexer_3 (
    .in0(Sequence_addr), .in1({32{1'b0}}), .out(multiplexer_3_out), .sel(clr));
  Register #(.width(32), .trigger("rising"), .Select("low")) register_1 (
    .D(multiplexer_1_out), .en(EN), .Q(PC_2), .clk(CLK));  // open: clr
  Register #(.width(32), .trigger("rising"), .Select("low")) register_2 (
    .D(multiplexer_2_out), .en(EN), .Q(IR_2), .clk(CLK));  // open: clr
  Register #(.width(32), .trigger("rising"), .Select("low")) register_3 (
    .D(multiplexer_3_out), .en(EN), .Q(Sequence_addr_2), .clk(CLK));  // open: clr
endmodule

module ID_EX (
  input  Syscall,
  input  MemToReg,
  input  RegWrite,
  input  RegDst,
  input  [4:0] rt_num,
  input  [4:0] rd_num,
  input  MemWrite,
  input  JMP,
  input  JAL,
  input  LH,
  input  JR,
  input  BEQ,
  input  BNE,
  input  BLEZ,
  input  SRAV,
  input  ALU_SRC,
  input  [3:0] ALU_OP,
  input  [4:0] Shamt,
  input  [31:0] PC,
  input  [31:0] IR,
  input  [31:0] A,
  input  [31:0] B,
  input  [31:0] Imm,
  input  [31:0] JMP_addr,
  input  [31:0] Branch_addr,
  input  [1:0] ForwarA,
  input  [1:0] ForwarB,
  input  CLK,
  input  clr,
  input  EN,
  output Syscall_2,
  output MemToReg_2,
  output RegWrite_2,
  output RegDst_2,
  output [4:0] rt_num_2,
  output [4:0] rd_num_2,
  output MemWrite_2,
  output JMP_2,
  output JAL_2,
  output LH_2,
  output JR_2,
  output BEQ_2,
  output BNE_2,
  output BLEZ_2,
  output SRAV_2,
  output ALU_SRC_2,
  output [3:0] ALU_OP_2,
  output [4:0] Shamt_2,
  output [31:0] PC_2,
  output [31:0] IR_2,
  output [31:0] A_2,
  output [31:0] B_2,
  output [31:0] Imm_2,
  output [31:0] JMP_Aaddr,
  output [31:0] JMP_Aaddr_2,
  output [1:0] ForwarA_2,
  output [1:0] ForwarB_2
);

  wire multiplexer_1_out, multiplexer_2_out, multiplexer_3_out, multiplexer_4_out, multiplexer_7_out,
       multiplexer_8_out, multiplexer_9_out, multiplexer_10_out, multiplexer_11_out, multiplexer_12_out,
       multiplexer_13_out, multiplexer_14_out, multiplexer_15_out, multiplexer_16_out;
  wire [1:0] multiplexer_26_out, multiplexer_27_out;
  wire [3:0] multiplexer_17_out;
  wire [4:0] multiplexer_5_out, multiplexer_6_out, multiplexer_18_out;
  wire [31:0] multiplexer_19_out, multiplexer_20_out, multiplexer_21_out, multiplexer_22_out,
       multiplexer_23_out, multiplexer_24_out, multiplexer_25_out;

  Pull_Resistor #(.pull(0)) pull_resistor_1 (.node(clr));
  Multiplexer #(.select(1), .width(1), .disabled("Z"), .enable("false")) multiplexer_1 (
    .in0(Syscall), .in1(1'b0), .out(multiplexer_1_out), .sel(clr));
  Multiplexer #(.select(1), .width(1), .disabled("Z"), .enable("false")) multiplexer_2 (
    .in0(MemToReg), .in1(1'b0), .out(multiplexer_2_out), .sel(clr));
  Multiplexer #(.select(1), .width(1), .disabled("Z"), .enable("false")) multiplexer_3 (
    .in0(RegWrite), .in1(1'b0), .out(multiplexer_3_out), .sel(clr));
  Multiplexer #(.select(1), .width(1), .disabled("Z"), .enable("false")) multiplexer_4 (
    .in0(RegDst), .in1(1'b0), .out(multiplexer_4_out), .sel(clr));
  Multiplexer #(.select(1), .width(5), .disabled("Z"), .enable("false")) multiplexer_5 (
    .in0(rt_num), .in1({5{1'b0}}), .out(multiplexer_5_out), .sel(clr));
  Multiplexer #(.select(1), .width(5), .disabled("Z"), .enable("false")) multiplexer_6 (
    .in0(rd_num), .in1({5{1'b0}}), .out(multiplexer_6_out), .sel(clr));
  Multiplexer #(.select(1), .width(1), .disabled("Z"), .enable("false")) multiplexer_7 (
    .in0(MemWrite), .in1(1'b0), .out(multiplexer_7_out), .sel(clr));
  Multiplexer #(.select(1), .width(1), .disabled("Z"), .enable("false")) multiplexer_8 (
    .in0(JMP), .in1(1'b0), .out(multiplexer_8_out), .sel(clr));
  Multiplexer #(.select(1), .width(1), .disabled("Z"), .enable("false")) multiplexer_9 (
    .in0(JAL), .in1(1'b0), .out(multiplexer_9_out), .sel(clr));
  Multiplexer #(.select(1), .width(1), .disabled("Z"), .enable("false")) multiplexer_10 (
    .in0(LH), .in1(1'b0), .out(multiplexer_10_out), .sel(clr));
  Multiplexer #(.select(1), .width(1), .disabled("Z"), .enable("false")) multiplexer_11 (
    .in0(JR), .in1(1'b0), .out(multiplexer_11_out), .sel(clr));
  Multiplexer #(.select(1), .width(1), .disabled("Z"), .enable("false")) multiplexer_12 (
    .in0(BEQ), .in1(1'b0), .out(multiplexer_12_out), .sel(clr));
  Multiplexer #(.select(1), .width(1), .disabled("Z"), .enable("false")) multiplexer_13 (
    .in0(BNE), .in1(1'b0), .out(multiplexer_13_out), .sel(clr));
  Multiplexer #(.select(1), .width(1), .disabled("Z"), .enable("false")) multiplexer_14 (
    .in0(BLEZ), .in1(1'b0), .out(multiplexer_14_out), .sel(clr));
  Multiplexer #(.select(1), .width(1), .disabled("Z"), .enable("false")) multiplexer_15 (
    .in0(SRAV), .in1(1'b0), .out(multiplexer_15_out), .sel(clr));
  Multiplexer #(.select(1), .width(1), .disabled("Z"), .enable("false")) multiplexer_16 (
    .in0(ALU_SRC), .in1(1'b0), .out(multiplexer_16_out), .sel(clr));
  Multiplexer #(.select(1), .width(4), .disabled("Z"), .enable("false")) multiplexer_17 (
    .in0(ALU_OP), .in1(4'b0000), .out(multiplexer_17_out), .sel(clr));
  Multiplexer #(.select(1), .width(5), .disabled("Z"), .enable("false")) multiplexer_18 (
    .in0(Shamt), .in1({5{1'b0}}), .out(multiplexer_18_out), .sel(clr));
  Multiplexer #(.select(1), .width(32), .disabled("Z"), .enable("false")) multiplexer_19 (
    .in0(PC), .in1({32{1'b0}}), .out(multiplexer_19_out), .sel(clr));
  Multiplexer #(.select(1), .width(32), .disabled("Z"), .enable("false")) multiplexer_20 (
    .in0(IR), .in1({32{1'b0}}), .out(multiplexer_20_out), .sel(clr));
  Multiplexer #(.select(1), .width(32), .disabled("Z"), .enable("false")) multiplexer_21 (
    .in0(A), .in1({32{1'b0}}), .out(multiplexer_21_out), .sel(clr));
  Multiplexer #(.select(1), .width(32), .disabled("Z"), .enable("false")) multiplexer_22 (
    .in0(B), .in1({32{1'b0}}), .out(multiplexer_22_out), .sel(clr));
  Multiplexer #(.select(1), .width(32), .disabled("Z"), .enable("false")) multiplexer_23 (
    .in0(Imm), .in1({32{1'b0}}), .out(multiplexer_23_out), .sel(clr));
  Multiplexer #(.select(1), .width(32), .disabled("Z"), .enable("false")) multiplexer_24 (
    .in0(JMP_addr), .in1({32{1'b0}}), .out(multiplexer_24_out), .sel(clr));
  Multiplexer #(.select(1), .width(32), .disabled("Z"), .enable("false")) multiplexer_25 (
    .in0(Branch_addr), .in1({32{1'b0}}), .out(multiplexer_25_out), .sel(clr));
  Multiplexer #(.select(1), .width(2), .disabled("Z"), .enable("false")) multiplexer_26 (
    .in0(ForwarA), .in1(2'b00), .out(multiplexer_26_out), .sel(clr));
  Multiplexer #(.select(1), .width(2), .disabled("Z"), .enable("false")) multiplexer_27 (
    .in0(ForwarB), .in1(2'b00), .out(multiplexer_27_out), .sel(clr));
  Register #(.width(1), .trigger("rising"), .Select("low")) register_1 (
    .D(multiplexer_1_out), .en(EN), .Q(Syscall_2), .clk(CLK));  // open: clr
  Register #(.width(1), .trigger("rising"), .Select("low")) register_2 (
    .D(multiplexer_2_out), .en(EN), .Q(MemToReg_2), .clk(CLK));  // open: clr
  Register #(.width(1), .trigger("rising"), .Select("low")) register_3 (
    .D(multiplexer_3_out), .en(EN), .Q(RegWrite_2), .clk(CLK));  // open: clr
  Register #(.width(1), .trigger("rising"), .Select("low")) register_4 (
    .D(multiplexer_4_out), .en(EN), .Q(RegDst_2), .clk(CLK));  // open: clr
  Register #(.width(5), .trigger("rising"), .Select("low")) register_5 (
    .D(multiplexer_5_out), .en(EN), .Q(rt_num_2), .clk(CLK));  // open: clr
  Register #(.width(5), .trigger("rising"), .Select("low")) register_6 (
    .D(multiplexer_6_out), .en(EN), .Q(rd_num_2), .clk(CLK));  // open: clr
  Register #(.width(1), .trigger("rising"), .Select("low")) register_7 (
    .D(multiplexer_7_out), .en(EN), .Q(MemWrite_2), .clk(CLK));  // open: clr
  Register #(.width(1), .trigger("rising"), .Select("low")) register_8 (
    .D(multiplexer_8_out), .en(EN), .Q(JMP_2), .clk(CLK));  // open: clr
  Register #(.width(1), .trigger("rising"), .Select("low")) register_9 (
    .D(multiplexer_9_out), .en(EN), .Q(JAL_2), .clk(CLK));  // open: clr
  Register #(.width(1), .trigger("rising"), .Select("low")) register_10 (
    .D(multiplexer_10_out), .en(EN), .Q(LH_2), .clk(CLK));  // open: clr
  Register #(.width(1), .trigger("rising"), .Select("low")) register_11 (
    .D(multiplexer_11_out), .en(EN), .Q(JR_2), .clk(CLK));  // open: clr
  Register #(.width(1), .trigger("rising"), .Select("low")) register_12 (
    .D(multiplexer_12_out), .en(EN), .Q(BEQ_2), .clk(CLK));  // open: clr
  Register #(.width(1), .trigger("rising"), .Select("low")) register_13 (
    .D(multiplexer_13_out), .en(EN), .Q(BNE_2), .clk(CLK));  // open: clr
  Register #(.width(1), .trigger("rising"), .Select("low")) register_14 (
    .D(multiplexer_14_out), .en(EN), .Q(BLEZ_2), .clk(CLK));  // open: clr
  Register #(.width(1), .trigger("rising"), .Select("low")) register_15 (
    .D(multiplexer_15_out), .en(EN), .Q(SRAV_2), .clk(CLK));  // open: clr
  Register #(.width(1), .trigger("rising"), .Select("low")) register_16 (
    .D(multiplexer_16_out), .en(EN), .Q(ALU_SRC_2), .clk(CLK));  // open: clr
  Register #(.width(4), .trigger("rising"), .Select("low")) register_17 (
    .D(multiplexer_17_out), .en(EN), .Q(ALU_OP_2), .clk(CLK));  // open: clr
  Register #(.width(5), .trigger("rising"), .Select("low")) register_18 (
    .D(multiplexer_18_out), .en(EN), .Q(Shamt_2), .clk(CLK));  // open: clr
  Register #(.width(32), .trigger("rising"), .Select("low")) register_19 (
    .D(multiplexer_19_out), .en(EN), .Q(PC_2), .clk(CLK));  // open: clr
  Register #(.width(32), .trigger("rising"), .Select("low")) register_20 (
    .D(multiplexer_20_out), .en(EN), .Q(IR_2), .clk(CLK));  // open: clr
  Register #(.width(32), .trigger("rising"), .Select("low")) register_21 (
    .D(multiplexer_21_out), .en(EN), .Q(A_2), .clk(CLK));  // open: clr
  Register #(.width(32), .trigger("rising"), .Select("low")) register_22 (
    .D(multiplexer_22_out), .en(EN), .Q(B_2), .clk(CLK));  // open: clr
  Register #(.width(32), .trigger("rising"), .Select("low")) register_23 (
    .D(multiplexer_23_out), .en(EN), .Q(Imm_2), .clk(CLK));  // open: clr
  Register #(.width(32), .trigger("rising"), .Select("low")) register_24 (
    .D(multiplexer_24_out), .en(EN), .Q(JMP_Aaddr), .clk(CLK));  // open: clr
  Register #(.width(32), .trigger("rising"), .Select("low")) register_25 (
    .D(multiplexer_25_out), .en(EN), .Q(JMP_Aaddr_2), .clk(CLK));  // open: clr
  Register #(.width(2), .trigger("rising"), .Select("low")) register_26 (
    .D(multiplexer_26_out), .en(EN), .Q(ForwarA_2), .clk(CLK));  // open: clr
  Register #(.width(2), .trigger("rising"), .Select("low")) register_27 (
    .D(multiplexer_27_out), .en(EN), .Q(ForwarB_2), .clk(CLK));  // open: clr
endmodule
module EX_MEM (
  input  Syscall,
  input  MemToReg,
  input  RegWrite,
  input  RegDst,
  input  [4:0] rt_num,
  input  [4:0] rd_num,
  input  MemWrite,
  input  JAL,
  input  LH,
  input  [31:0] PC,
  input  [31:0] IR,
  input  [31:0] ALU,
  input  [31:0] B,
  input  CLK,
  input  clr,
  input  EN,
  output Syscall_2,
  output MemToReg_2,
  output RegWrite_2,
  output RegDst_2,
  output [4:0] rt_num_2,
  output [4:0] rd_num_2,
  output MemWrite_2,
  output JAL_2,
  output LH_2,
  output [31:0] PC_2,
  output [31:0] IR_2,
  output [31:0] ALU_2,
  output [31:0] B_2
);

  wire multiplexer_1_out, multiplexer_2_out, multiplexer_3_out, multiplexer_4_out, multiplexer_7_out,
       multiplexer_8_out, multiplexer_9_out;
  wire [4:0] multiplexer_5_out, multiplexer_6_out;
  wire [31:0] multiplexer_10_out, multiplexer_11_out, multiplexer_12_out, multiplexer_13_out;

  Pull_Resistor #(.pull(0)) pull_resistor_1 (.node(clr));
  Multiplexer #(.select(1), .width(1), .disabled("Z"), .enable("false")) multiplexer_1 (
    .in0(Syscall), .in1(1'b0), .out(multiplexer_1_out), .sel(clr));
  Multiplexer #(.select(1), .width(1), .disabled("Z"), .enable("false")) multiplexer_2 (
    .in0(MemToReg), .in1(1'b0), .out(multiplexer_2_out), .sel(clr));
  Multiplexer #(.select(1), .width(1), .disabled("Z"), .enable("false")) multiplexer_3 (
    .in0(RegWrite), .in1(1'b0), .out(multiplexer_3_out), .sel(clr));
  Multiplexer #(.select(1), .width(1), .disabled("Z"), .enable("false")) multiplexer_4 (
    .in0(RegDst), .in1(1'b0), .out(multiplexer_4_out), .sel(clr));
  Multiplexer #(.select(1), .width(5), .disabled("Z"), .enable("false")) multiplexer_5 (
    .in0(rt_num), .in1({5{1'b0}}), .out(multiplexer_5_out), .sel(clr));
  Multiplexer #(.select(1), .width(5), .disabled("Z"), .enable("false")) multiplexer_6 (
    .in0(rd_num), .in1({5{1'b0}}), .out(multiplexer_6_out), .sel(clr));
  Multiplexer #(.select(1), .width(1), .disabled("Z"), .enable("false")) multiplexer_7 (
    .in0(MemWrite), .in1(1'b0), .out(multiplexer_7_out), .sel(clr));
  Multiplexer #(.select(1), .width(1), .disabled("Z"), .enable("false")) multiplexer_8 (
    .in0(JAL), .in1(1'b0), .out(multiplexer_8_out), .sel(clr));
  Multiplexer #(.select(1), .width(1), .disabled("Z"), .enable("false")) multiplexer_9 (
    .in0(LH), .in1(1'b0), .out(multiplexer_9_out), .sel(clr));
  Multiplexer #(.select(1), .width(32), .disabled("Z"), .enable("false")) multiplexer_10 (
    .in0(PC), .in1({32{1'b0}}), .out(multiplexer_10_out), .sel(clr));
  Multiplexer #(.select(1), .width(32), .disabled("Z"), .enable("false")) multiplexer_11 (
    .in0(IR), .in1({32{1'b0}}), .out(multiplexer_11_out), .sel(clr));
  Multiplexer #(.select(1), .width(32), .disabled("Z"), .enable("false")) multiplexer_12 (
    .in0(ALU), .in1({32{1'b0}}), .out(multiplexer_12_out), .sel(clr));
  Multiplexer #(.select(1), .width(32), .disabled("Z"), .enable("false")) multiplexer_13 (
    .in0(B), .in1({32{1'b0}}), .out(multiplexer_13_out), .sel(clr));
  Register #(.width(1), .trigger("rising"), .Select("low")) register_1 (
    .D(multiplexer_1_out), .en(EN), .Q(Syscall_2), .clk(CLK));  // open: clr
  Register #(.width(1), .trigger("rising"), .Select("low")) register_2 (
    .D(multiplexer_2_out), .en(EN), .Q(MemToReg_2), .clk(CLK));  // open: clr
  Register #(.width(1), .trigger("rising"), .Select("low")) register_3 (
    .D(multiplexer_3_out), .en(EN), .Q(RegWrite_2), .clk(CLK));  // open: clr
  Register #(.width(1), .trigger("rising"), .Select("low")) register_4 (
    .D(multiplexer_4_out), .en(EN), .Q(RegDst_2), .clk(CLK));  // open: clr
  Register #(.width(5), .trigger("rising"), .Select("low")) register_5 (
    .D(multiplexer_5_out), .en(EN), .Q(rt_num_2), .clk(CLK));  // open: clr
  Register #(.width(5), .trigger("rising"), .Select("low")) register_6 (
    .D(multiplexer_6_out), .en(EN), .Q(rd_num_2), .clk(CLK));  // open: clr
  Register #(.width(1), .trigger("rising"), .Select("low")) register_7 (
    .D(multiplexer_7_out), .en(EN), .Q(MemWrite_2), .clk(CLK));  // open: clr
  Register #(.width(1), .trigger("rising"), .Select("low")) register_8 (
    .D(multiplexer_8_out), .en(EN), .Q(JAL_2), .clk(CLK));  // open: clr
  Register #(.width(1), .trigger("rising"), .Select("low")) register_9 (
    .D(multiplexer_9_out), .en(EN), .Q(LH_2), .clk(CLK));  // open: clr
  Register #(.width(32), .trigger("rising"), .Select("low")) register_10 (
    .D(multiplexer_10_out), .en(EN), .Q(PC_2), .clk(CLK));  // open: clr
  Register #(.width(32), .trigger("rising"), .Select("low")) register_11 (
    .D(multiplexer_11_out), .en(EN), .Q(IR_2), .clk(CLK));  // open: clr
  Register #(.width(32), .trigger("rising"), .Select("low")) register_12 (
    .D(multiplexer_12_out), .en(EN), .Q(ALU_2), .clk(CLK));  // open: clr
  Register #(.width(32), .trigger("rising"), .Select("low")) register_13 (
    .D(multiplexer_13_out), .en(EN), .Q(B_2), .clk(CLK));  // open: clr
endmodule

module MEM_WB (
  input  Syscall,
  input  MemToReg,
  input  RegWrite,
  input  RegDst,
  input  [4:0] rt_num,
  input  [4:0] rd_num,
  input  JAL,
  input  LH,
  input  [31:0] PC,
  input  [31:0] IR,
  input  [31:0] ALU,
  input  [31:0] MD,
  input  [31:0] HW,
  input  CLK,
  input  clr,
  input  EN,
  output Syscall_2,
  output MemToReg_2,
  output RegWrite_2,
  output RegDst_2,
  output [4:0] rt_num_2,
  output [4:0] rd_num_2,
  output JAL_2,
  output LH_2,
  output [31:0] PC_2,
  output [31:0] IR_2,
  output [31:0] ALU_2,
  output [31:0] MD_2,
  output [31:0] HW_2
);

  wire multiplexer_1_out, multiplexer_2_out, multiplexer_3_out, multiplexer_4_out, multiplexer_7_out,
       multiplexer_8_out;
  wire [4:0] multiplexer_5_out, multiplexer_6_out;
  wire [31:0] multiplexer_9_out, multiplexer_10_out, multiplexer_11_out, multiplexer_12_out,
       multiplexer_13_out;

  Pull_Resistor #(.pull(0)) pull_resistor_1 (.node(clr));
  Multiplexer #(.select(1), .width(1), .disabled("Z"), .enable("false")) multiplexer_1 (
    .in0(Syscall), .in1(1'b0), .out(multiplexer_1_out), .sel(clr));
  Multiplexer #(.select(1), .width(1), .disabled("Z"), .enable("false")) multiplexer_2 (
    .in0(MemToReg), .in1(1'b0), .out(multiplexer_2_out), .sel(clr));
  Multiplexer #(.select(1), .width(1), .disabled("Z"), .enable("false")) multiplexer_3 (
    .in0(RegWrite), .in1(1'b0), .out(multiplexer_3_out), .sel(clr));
  Multiplexer #(.select(1), .width(1), .disabled("Z"), .enable("false")) multiplexer_4 (
    .in0(RegDst), .in1(1'b0), .out(multiplexer_4_out), .sel(clr));
  Multiplexer #(.select(1), .width(5), .disabled("Z"), .enable("false")) multiplexer_5 (
    .in0(rt_num), .in1({5{1'b0}}), .out(multiplexer_5_out), .sel(clr));
  Multiplexer #(.select(1), .width(5), .disabled("Z"), .enable("false")) multiplexer_6 (
    .in0(rd_num), .in1({5{1'b0}}), .out(multiplexer_6_out), .sel(clr));
  Multiplexer #(.select(1), .width(1), .disabled("Z"), .enable("false")) multiplexer_7 (
    .in0(JAL), .in1(1'b0), .out(multiplexer_7_out), .sel(clr));
  Multiplexer #(.select(1), .width(1), .disabled("Z"), .enable("false")) multiplexer_8 (
    .in0(LH), .in1(1'b0), .out(multiplexer_8_out), .sel(clr));
  Multiplexer #(.select(1), .width(32), .disabled("Z"), .enable("false")) multiplexer_9 (
    .in0(PC), .in1({32{1'b0}}), .out(multiplexer_9_out), .sel(clr));
  Multiplexer #(.select(1), .width(32), .disabled("Z"), .enable("false")) multiplexer_10 (
    .in0(IR), .in1({32{1'b0}}), .out(multiplexer_10_out), .sel(clr));
  Multiplexer #(.select(1), .width(32), .disabled("Z"), .enable("false")) multiplexer_11 (
    .in0(ALU), .in1({32{1'b0}}), .out(multiplexer_11_out), .sel(clr));
  Multiplexer #(.select(1), .width(32), .disabled("Z"), .enable("false")) multiplexer_12 (
    .in0(MD), .in1({32{1'b0}}), .out(multiplexer_12_out), .sel(clr));
  Multiplexer #(.select(1), .width(32), .disabled("Z"), .enable("false")) multiplexer_13 (
    .in0(HW), .in1({32{1'b0}}), .out(multiplexer_13_out), .sel(clr));
  Register #(.width(1), .trigger("rising"), .Select("low")) register_1 (
    .D(multiplexer_1_out), .en(EN), .Q(Syscall_2), .clk(CLK));  // open: clr
  Register #(.width(1), .trigger("rising"), .Select("low")) register_2 (
    .D(multiplexer_2_out), .en(EN), .Q(MemToReg_2), .clk(CLK));  // open: clr
  Register #(.width(1), .trigger("rising"), .Select("low")) register_3 (
    .D(multiplexer_3_out), .en(EN), .Q(RegWrite_2), .clk(CLK));  // open: clr
  Register #(.width(1), .trigger("rising"), .Select("low")) register_4 (
    .D(multiplexer_4_out), .en(EN), .Q(RegDst_2), .clk(CLK));  // open: clr
  Register #(.width(5), .trigger("rising"), .Select("low")) register_5 (
    .D(multiplexer_5_out), .en(EN), .Q(rt_num_2), .clk(CLK));  // open: clr
  Register #(.width(5), .trigger("rising"), .Select("low")) register_6 (
    .D(multiplexer_6_out), .en(EN), .Q(rd_num_2), .clk(CLK));  // open: clr
  Register #(.width(1), .trigger("rising"), .Select("low")) register_7 (
    .D(multiplexer_7_out), .en(EN), .Q(JAL_2), .clk(CLK));  // open: clr
  Register #(.width(1), .trigger("rising"), .Select("low")) register_8 (
    .D(multiplexer_8_out), .en(EN), .Q(LH_2), .clk(CLK));  // open: clr
  Register #(.width(32), .trigger("rising"), .Select("low")) register_9 (
    .D(multiplexer_9_out), .en(EN), .Q(PC_2), .clk(CLK));  // open: clr
  Register #(.width(32), .trigger("rising"), .Select("low")) register_10 (
    .D(multiplexer_10_out), .en(EN), .Q(IR_2), .clk(CLK));  // open: clr
  Register #(.width(32), .trigger("rising"), .Select("low")) register_11 (
    .D(multiplexer_11_out), .en(EN), .Q(ALU_2), .clk(CLK));  // open: clr
  Register #(.width(32), .trigger("rising"), .Select("low")) register_12 (
    .D(multiplexer_12_out), .en(EN), .Q(MD_2), .clk(CLK));  // open: clr
  Register #(.width(32), .trigger("rising"), .Select("low")) register_13 (
    .D(multiplexer_13_out), .en(EN), .Q(HW_2), .clk(CLK));  // open: clr
endmodule
